// Logisim project cpu21-riscv.circ as structural Verilog: 26 circuits, main circuit ◇单周期RISC-V
module \单周期RISC_V  (
  input  IR1,
  input  IR2,
  input  IR3,
  output RegWrite,
  output MemWrite,
  output [31:0] PC,
  output [31:0] IR,
  output [31:0] RDin,
  output [31:0] MDin,
  output [31:0] LedData
);

  wire ALU_equal, ALU_less, ALU_more_equal, AluSrcB, AUIPC, Beq, BLTU, Bne, CLK, clock_2_out,
       comparator_1_eq, comparator_1_lt, d_ff_1_q, ecall, Go, halt, IR1_t, IR2_t, IR3_t, IRA, IRB, IRC, JAL,
       JALR, LH, LUI, MemToReg, nand_1_out, not_1_out, not_2_out, or_4_out, RST, S_type, W1, W2, W3;
  wire [3:0] AluOP;
  wire [4:0] multiplexer_1_out, multiplexer_2_out;
  wire [12:0] CNT_num;
  wire [15:0] \总周期数 ;
  wire [31:0] ALU_reslut, bit_extender_2_out, bit_extender_5_out, bit_extender_6_out, I_offset,
       Mem_LH_reslut, Mem_reslut, multiplexer_3_out, multiplexer_4_out, pc_next_1_next_pc, rs1_data;
  wire [31:1] B_offset, J_offset;
  wire [31:31] bit_extender_3_out, bit_extender_4_out;

  Clock #(.highDuration(1), .lowDuration(1)) clock_1 ();  // open: out
  Button _1 (.out(IRA));
  Button _2 (.out(IRB));
  Button _3 (.out(IRC));
  LED #(.active("true")) led_1 (.in(W1));
  LED #(.active("true")) led_2 (.in(W2));
  LED #(.active("true")) led_3 (.in(W3));
  Button \u_复位  (.out(RST));
  Button \u_继续运行  (.out(Go));
  Hex_Digit_Display hex_digit_display_1 (.value(LedData[31:28]));  // open: dp
  ecall_deal ecall_deal_1 (
    .ecall(ecall), .a0(MDin), .clk(CLK), .go(Go), .LedData(LedData), .halt(halt), .rs1_data(rs1_data));
  pc_next pc_next_1 (
    .pc(PC), .B_offset({B_offset, 1'b0}), .J_offset({J_offset, 1'b0}), .I_offset(I_offset),
    .next_pc(pc_next_1_next_pc), .rs1(rs1_data), .ALU_equal(ALU_equal), .Bne(Bne), .Beq(Beq), .JALR(JALR),
    .ALU_less(ALU_less), .JAL(JAL), .BLTU(BLTU));
  Hex_Digit_Display hex_digit_display_2 (.value(LedData[27:24]));  // open: dp
  Hex_Digit_Display hex_digit_display_3 (.value(LedData[23:20]));  // open: dp
  // Probe on pc_next_1_next_pc
  Hex_Digit_Display hex_digit_display_4 (.value(LedData[19:16]));  // open: dp
  Hex_Digit_Display hex_digit_display_5 (.value(LedData[15:12]));  // open: dp
  Register #(.width(32), .trigger("rising"), .Select("low")) u_PC (
    .D(pc_next_1_next_pc), .en(not_1_out), .Q(PC), .clk(CLK), .clr(RST));
  not not_1 (not_1_out, halt);
  Hex_Digit_Display hex_digit_display_6 (.value(LedData[11:8]));  // open: dp
  Hex_Digit_Display hex_digit_display_7 (.value(LedData[7:4]));  // open: dp
  // Probe on \总周期数 
  not not_2 (not_2_out, halt);
  Counter #(.width(16), .max('hffff), .ongoal("wrap"), .trigger("rising"), .behavior("new")) counter_1 (
    .D(16'h1), .count(not_2_out), .Q(\总周期数 ), .clk(CLK), .clr(RST));  // open: load, carry, preset, down
  // Probe on PC
  Hex_Digit_Display hex_digit_display_8 (.value(LedData[3:0]));  // open: dp
  // Probe on PC[11:2]
  or or_1 (IR1_t, IR1, IRA);
  or or_2 (IR2_t, IR2, IRB);
  // RiscV_Probe riscv_probe_1: pin names not known; wires that end beside it: IR
  ROM #(.addrWidth(10), .dataWidth(32), .Select("high")) rom_1 (.addr(PC[11:2]), .data(IR));
  or or_3 (IR3_t, IR3, IRC);
  \单周期硬布线控制器  \u_单周期硬布线控制器_1  (
    .Funct({IR[30], IR[25], IR[14:12]}), .OP(IR[6:2]), .ALU_OP(AluOP), .MemToReg(MemToReg),
    .MemWrite(MemWrite), .ALU_SRC(AluSrcB), .RegWrite(RegWrite), .ecall(ecall), .S_type(S_type), .Jalr(JALR),
    .Beq(Beq), .JAL(JAL), .Bne(Bne), .AUIPC(AUIPC), .BLTU(BLTU), .LH(LH), .LUI(LUI));  // open: CSRRSI, CSRRCI
  Multiplexer #(.select(1), .width(5), .disabled("Z"), .enable("false")) multiplexer_1 (
    .in0(IR[19:15]), .in1(5'b10001), .out(multiplexer_1_out), .sel(ecall));
  Multiplexer #(.select(1), .width(5), .disabled("Z"), .enable("false")) multiplexer_2 (
    .in0(IR[24:20]), .in1(5'b01010), .out(multiplexer_2_out), .sel(ecall));
  rd_in rd_in_1 (
    .ALU_result(ALU_reslut), .Mem_result(Mem_reslut), .MemToReg(MemToReg), .PC(PC), .JAL(JAL), .JALR(JALR),
    .RDin(RDin), .U_imm({IR[31:12], {12{1'b0}}}), .LUI(LUI), .AUIPC(AUIPC), .LH(LH),
    .Mem_LH_result(Mem_LH_reslut));
  assign I_offset = {{20{IR[31]}}, IR[31:20]};  // Bit_Extender bit_extender_1
  assign bit_extender_2_out = {{20{IR[31]}}, {IR[31:25], IR[11:7]}};  // Bit_Extender bit_extender_2
  assign {bit_extender_3_out[31], B_offset} = {{20{IR[31]}}, {IR[31], IR[7], IR[30:25], IR[11:8]}};  // Bit_Extender bit_extender_3
  assign {bit_extender_4_out[31], J_offset} = {{12{IR[31]}}, {IR[31], IR[19:12], IR[20], IR[30:21]}};  // Bit_Extender bit_extender_4
  // Probe on multiplexer_1_out
  // Probe on multiplexer_2_out
  // Probe on IR[11:7]
  // Probe on RDin
  // Probe on I_offset
  // Probe on bit_extender_2_out
  // Probe on {B_offset, 1'b0}
  // Probe on {J_offset, 1'b0}
  // Probe on {IR[31:12], {12{1'b0}}}
  Regifile regifile_1 (
    .Din(RDin), .Clk(CLK), .R1(rs1_data), .R2(MDin), .WE(RegWrite), .W_num(IR[11:7]),
    .R1_num(multiplexer_1_out), .R2_num(multiplexer_2_out));
  Multiplexer #(.select(1), .width(32), .disabled("Z"), .enable("false")) multiplexer_3 (
    .in0(MDin), .in1(I_offset), .out(multiplexer_3_out), .sel(AluSrcB));
  D_Flip_Flop #(.trigger("high"), .Pre_Clr_Positions("LEGACY"), .NegatePresetClear("false"), .enable("true"), .NewFFLayout("false")) d_ff_1 (.Q(d_ff_1_q));  // open: clk, D, Qn, preset, en, reset
  // Probe on 13'hc
  // Probe on rs1_data
  Multiplexer #(.select(1), .width(32), .disabled("Z"), .enable("false")) multiplexer_4 (
    .in0(multiplexer_3_out), .in1(bit_extender_2_out), .out(multiplexer_4_out), .sel(S_type));
  // Probe on multiplexer_4_out
  Comparator #(.width(13), .mode("twosComplement")) comparator_1 (
    .a(CNT_num), .b(13'hc), .eq(comparator_1_eq), .lt(comparator_1_lt));  // open: gt
  Clock #(.highDuration(1), .lowDuration(1)) clock_2 (.out(clock_2_out));
  Counter #(.width(13), .max('h1fff), .ongoal("stay"), .trigger("rising"), .behavior("old")) counter_2 (
    .count(comparator_1_lt), .Q(CNT_num), .clk(clock_2_out));  // open: load, D, carry, clr, preset
  ALU alu_1 (
    .X(rs1_data), .Y(multiplexer_4_out), .AluOP(AluOP), .Equal(ALU_equal), .Result(ALU_reslut),
    .out_4(ALU_more_equal), .out_6(ALU_less));  // open: Result_2
  nand nand_1 (nand_1_out, d_ff_1_q, comparator_1_eq);
  assign CLK = nand_1_out ? clock_2_out : 1'bz;  // Controlled_Buffer controlled_buffer_1
  Pull_Resistor #(.pull(1)) pull_resistor_1 (.node(CLK));
  // Probe on ALU_reslut
  or or_4 (or_4_out, MemWrite, MemToReg);
  RAM #(.addrWidth(10), .dataWidth(32), .bus("separate"), .Select("high")) ram_1 (
    .addr(ALU_reslut[11:2]), .din(MDin), .data(Mem_reslut), .str(MemWrite), .sel(or_4_out), .clk(CLK),
    .ld(MemToReg), .clr(RST));
  assign bit_extender_5_out = {{16{Mem_reslut[15]}}, Mem_reslut[15:0]};  // Bit_Extender bit_extender_5
  assign bit_extender_6_out = {{16{Mem_reslut[31]}}, Mem_reslut[31:16]};  // Bit_Extender bit_extender_6
  Multiplexer #(.select(2), .width(32), .disabled("Z"), .enable("false")) multiplexer_5 (
    .in0(bit_extender_5_out), .in1({32{1'b0}}), .in2(bit_extender_6_out), .in3({32{1'b0}}),
    .out(Mem_LH_reslut), .sel(ALU_reslut[1:0]));

  // Other names for the same wires on the sheet: rs2_data[31:0] = MDin; U_RDin[31:12] = IR[31:12]

  // Notes on the sheet:
  //   中断源
  //   ecall 信号处理
  //   中断等待指示
  //   总复位信号应将除ROM以外所有存储组件全部清零
  //   数码管输出
  //   周期计数
  //   数码管输出应该用寄存器锁存，否则显示数据只能一闪而过
  //   指令存储器
  //   contents of rom_1 (hex, n*v repeats v):
  //   100493 100006f 100493 200913 300993 100006f 100493 200913 300993 100006f 100493 200913 300993
  //   100006f 100493 200913 300993 29c000ef 100413 100493 1f49493 900533 2200893 73 24d493 48463 fedff06f
  //   900533 2200893 73 100493 249493 900533 2200893 73 48463 fedff06f 100493 1f49493 900533 2200893 73
  //   4034d493 900533 2200893 73 4044d493 900533 2200893 73 4044d493 900533 2200893 73 4044d493 900533
  //   2200893 73 4044d493 900533 2200893 73 4044d493 900533 2200893 73 4044d493 900533 2200893 73 4044d493
  //   900533 2200893 73 100413 1f41993 41f9d993 433 c00913 300b13 140413 f47413 800293 100313 499993
  //   89e9b3 1300533 2200893 73 406282b3 fe0294e3 140413 f00f93 1f47433 1c41413 800293 100313 49d993
  //   89e9b3 1300533 2200893 73 406282b3 fe0294e3 1c45413 406b0b33 b0463 f95ff06f 2b3 fff2c293 829293
  //   ff2e293 500533 2200893 73 fff00413 493 84a023 140413 448493 84a023 140413 448493 84a023 140413
  //   448493 84a023 140413 448493 84a023 140413 448493 84a023 140413 448493 84a023 140413 448493 84a023
  //   140413 448493 84a023 140413 448493 84a023 140413 448493 84a023 140413 448493 84a023 140413 448493
  //   84a023 140413 448493 84a023 140413 448493 84a023 140413 448493 84a023 140413 448493 140413 433
  //   3c00493 42983 4aa03 149a2b3 28663 134a023 1442023 ffc48493 fe9412e3 800533 2200893 73 440413 3c00493
  //   fc9416e3 a00893 73 413 140413 800533 2200893 73 240413 800533 2200893 73 340413 800533 2200893 73
  //   440413 800533 2200893 73 540413 800533 2200893 73 640413 800533 2200893 73 740413 800533 2200893 73
  //   840413 800533 2200893 2200893 73 8067
  //   opcode
  //   funct
  //   rs1
  //   rs2
  //   指令字
  //   rd
  //   I:imm
  //   S:imm
  //   B:imm
  //   J:imm
  //   U:imm
  //   Beq
  //   JAL
  //   JALR
  //   Bne
  //   ecall
  //   MemToReg
  //   MemWrite
  //   AluOP
  //   AluSrcB
  //   RegWrite
  //   S_type
  //   为方便自动评测，需要输出PC，IR，寄存器堆写如数据RDin
  //   RAM写使能MemWrite、RAM写入数据MDin等信号
  //   控制位
  //   暂停节拍，不能为0
  //   戳工具置1进入计数暂停模式，ctrl+k时钟自动运行到对应节拍暂停
  //   ctrl+k关闭时钟连续运行，将控制位置零，进入单步调试模式调试
  //   用这个时钟源需要去掉电路中的其他时钟源
  //   可计数暂停的时钟源
  //   数据存储器
endmodule

// 单周期硬布线控制器
module \单周期硬布线控制器  (
  input  [4:0] OP,
  input  [4:0] Funct,
  output [3:0] ALU_OP,
  output MemToReg,
  output MemWrite,
  output ALU_SRC,
  output RegWrite,
  output ecall,
  output S_type,
  output Beq,
  output Bne,
  output Jalr,
  output JAL,
  output LUI,
  output AUIPC,
  output LH,
  output BLTU,
  output CSRRSI,
  output CSRRCI
);

  // Probe on OP
  \运算控制器自动生成  \u_运算控制器自动生成_1  (
    .OP2(OP[0]), .OP3(OP[1]), .OP4(OP[2]), .OP5(OP[3]), .OP6(OP[4]), .F12(Funct[0]), .F13(Funct[1]),
    .F14(Funct[2]), .F25(Funct[3]), .F30(Funct[4]), .S0(ALU_OP[0]), .S1(ALU_OP[1]), .S2(ALU_OP[2]),
    .S3(ALU_OP[3]));
  \控制信号自动生成  \u_控制信号自动生成_1  (
    .OP2(OP[0]), .OP3(OP[1]), .OP4(OP[2]), .OP5(OP[3]), .MemToReg(MemToReg), .OP6(OP[4]), .F12(Funct[0]),
    .F13(Funct[1]), .F14(Funct[2]), .F25(Funct[3]), .F30(Funct[4]), .MemWrite(MemWrite), .ALU_SRC(ALU_SRC),
    .RegWrite(RegWrite), .ecall(ecall), .S_Type(S_type), .BEQ(Beq), .BNE(Bne), .JALR(Jalr), .JAL(JAL),
    .LUI(LUI), .AUIPC(AUIPC), .LH(LH), .BLTU(BLTU), .CSRRSI(CSRRSI), .CSRRCI(CSRRCI));
  // Probe on Funct
  // Probe on ALU_OP

  // Other names for the same wires on the sheet: OP_CODE[4:0] = OP

  // Notes on the sheet:
  //   运算器控制器，根据指令生成运算器功能选择信号
  //   控制信号生成，产生数据通路需要的其他控制信号
endmodule

// 运算器控制器
module \运算控制器自动生成  (
  input  OP2,
  input  OP3,
  input  OP4,
  input  OP5,
  input  OP6,
  input  F12,
  input  F13,
  input  F14,
  input  F25,
  input  F30,
  output S0,
  output S1,
  output S2,
  output S3
);

  wire and_1_out, and_2_out, and_3_out, and_4_out, and_5_out, and_6_out, and_7_out, and_8_out, and_9_out,
       and_10_out, and_11_out, and_12_out, and_13_out, and_14_out, and_15_out, and_16_out, and_17_out,
       and_18_out, and_19_out, and_20_out, and_21_out, and_22_out, and_23_out, and_24_out, and_25_out,
       and_26_out, and_27_out, and_28_out, and_29_out, and_30_out, and_31_out, and_32_out, and_33_out,
       and_34_out, and_35_out, and_36_out, and_37_out, and_38_out, and_39_out, and_40_out, and_41_out,
       and_42_out, not_1_out, not_2_out, not_3_out, not_4_out, not_5_out, not_6_out, not_7_out, not_8_out,
       not_9_out, not_10_out, not_11_out, not_12_out, not_13_out, not_14_out, not_15_out, not_16_out,
       not_17_out, not_18_out, not_19_out, not_20_out, not_21_out, not_22_out, not_23_out, not_24_out,
       not_25_out, not_26_out, not_27_out, not_28_out, not_29_out, not_30_out, not_31_out, not_32_out,
       not_33_out, not_34_out, not_35_out, not_36_out, not_37_out, not_38_out, not_39_out, not_40_out,
       not_41_out, not_42_out, not_43_out, not_44_out, not_45_out, not_46_out, not_47_out, not_48_out,
       not_49_out, not_50_out, not_51_out, not_52_out, not_53_out, not_54_out, not_55_out, not_56_out,
       not_57_out, not_58_out, not_59_out, not_60_out, not_61_out, not_62_out, not_63_out, not_64_out,
       not_65_out, not_66_out, not_67_out, not_68_out, not_69_out, not_70_out, not_71_out, not_72_out,
       not_73_out, not_74_out, not_75_out, not_76_out, not_77_out, not_78_out, not_79_out, not_80_out,
       not_81_out, not_82_out, not_83_out, not_84_out, not_85_out, not_86_out, not_87_out, not_88_out,
       not_89_out, not_90_out, not_91_out, not_92_out, not_93_out, not_94_out, not_95_out, not_96_out,
       not_97_out, not_98_out, not_99_out, not_100_out, not_101_out, not_102_out, not_103_out, not_104_out,
       not_105_out, not_106_out, not_107_out, not_108_out, not_109_out, not_110_out, not_111_out,
       not_112_out, not_113_out, not_114_out, not_115_out, not_116_out, not_117_out, not_118_out,
       not_119_out, not_120_out, not_121_out, not_122_out, not_123_out, not_124_out, not_125_out,
       not_126_out, not_127_out, not_128_out, not_129_out, not_130_out, not_131_out, not_132_out,
       not_133_out, not_134_out, not_135_out, not_136_out, not_137_out, not_138_out, not_139_out,
       not_140_out, not_141_out, not_142_out, not_143_out, not_144_out, not_145_out, not_146_out,
       not_147_out, not_148_out, not_149_out, not_150_out, not_151_out, not_152_out, not_153_out,
       not_154_out, not_155_out, not_156_out, not_157_out, not_158_out, not_159_out, not_160_out,
       not_161_out, not_162_out, not_163_out, not_164_out, not_165_out, not_166_out, not_167_out,
       not_168_out, not_169_out, not_170_out, not_171_out, not_172_out, not_173_out, not_174_out,
       not_175_out, not_176_out, not_177_out, not_178_out, not_179_out, not_180_out, not_181_out,
       not_182_out, not_183_out, not_184_out, not_185_out, not_186_out, not_187_out, not_188_out,
       not_189_out, not_190_out, not_191_out, not_192_out, not_193_out, not_194_out, not_195_out,
       not_196_out, not_197_out, not_198_out, not_199_out, not_200_out, not_201_out, not_202_out,
       not_203_out, not_204_out, not_205_out, not_206_out, not_207_out, not_208_out, not_209_out,
       not_210_out, not_211_out, not_212_out, not_213_out, not_214_out, not_215_out, not_216_out,
       not_217_out, not_218_out, not_219_out, not_220_out, not_221_out, not_222_out, not_223_out,
       not_224_out, not_225_out, not_226_out, not_227_out, not_228_out, not_229_out, not_230_out,
       not_231_out, not_232_out, not_233_out, not_234_out, not_235_out, not_236_out, not_237_out,
       not_238_out, not_239_out, not_240_out;

  not not_1 (not_1_out, F30);
  not not_2 (not_2_out, F25);
  not not_3 (not_3_out, F14);
  not not_4 (not_4_out, F13);
  not not_5 (not_5_out, F12);
  not not_6 (not_6_out, OP6);
  not not_7 (not_7_out, OP3);
  not not_8 (not_8_out, OP2);
  not not_9 (not_9_out, F30);
  not not_10 (not_10_out, F25);
  not not_11 (not_11_out, OP6);
  not not_12 (not_12_out, OP3);
  not not_13 (not_13_out, OP2);
  not not_14 (not_14_out, F30);
  not not_15 (not_15_out, F25);
  not not_16 (not_16_out, F14);
  not not_17 (not_17_out, F12);
  not not_18 (not_18_out, OP6);
  not not_19 (not_19_out, OP3);
  not not_20 (not_20_out, OP2);
  not not_21 (not_21_out, F14);
  not not_22 (not_22_out, F13);
  not not_23 (not_23_out, F12);
  not not_24 (not_24_out, OP6);
  not not_25 (not_25_out, OP5);
  not not_26 (not_26_out, OP3);
  not not_27 (not_27_out, OP2);
  not not_28 (not_28_out, OP6);
  not not_29 (not_29_out, OP5);
  not not_30 (not_30_out, OP3);
  not not_31 (not_31_out, OP2);
  not not_32 (not_32_out, F13);
  not not_33 (not_33_out, F12);
  not not_34 (not_34_out, OP6);
  not not_35 (not_35_out, OP5);
  not not_36 (not_36_out, OP3);
  not not_37 (not_37_out, OP2);
  not not_38 (not_38_out, F14);
  not not_39 (not_39_out, F12);
  not not_40 (not_40_out, OP6);
  not not_41 (not_41_out, OP5);
  not not_42 (not_42_out, OP3);
  not not_43 (not_43_out, OP2);
  not not_44 (not_44_out, F25);
  not not_45 (not_45_out, F13);
  not not_46 (not_46_out, OP6);
  not not_47 (not_47_out, OP5);
  not not_48 (not_48_out, OP3);
  not not_49 (not_49_out, OP2);
  not not_50 (not_50_out, F14);
  not not_51 (not_51_out, F12);
  not not_52 (not_52_out, OP6);
  not not_53 (not_53_out, OP5);
  not not_54 (not_54_out, OP4);
  not not_55 (not_55_out, OP3);
  not not_56 (not_56_out, OP2);
  not not_57 (not_57_out, F14);
  not not_58 (not_58_out, F12);
  not not_59 (not_59_out, OP6);
  not not_60 (not_60_out, OP4);
  not not_61 (not_61_out, OP3);
  not not_62 (not_62_out, OP2);
  not not_63 (not_63_out, OP4);
  not not_64 (not_64_out, F14);
  not not_65 (not_65_out, F13);
  not not_66 (not_66_out, F12);
  not not_67 (not_67_out, OP4);
  not not_68 (not_68_out, OP3);
  not not_69 (not_69_out, F14);
  not not_70 (not_70_out, F13);
  not not_71 (not_71_out, OP6);
  not not_72 (not_72_out, OP5);
  not not_73 (not_73_out, OP4);
  not not_74 (not_74_out, OP3);
  not not_75 (not_75_out, OP2);
  not not_76 (not_76_out, F25);
  not not_77 (not_77_out, F14);
  not not_78 (not_78_out, F13);
  not not_79 (not_79_out, F12);
  not not_80 (not_80_out, OP6);
  not not_81 (not_81_out, OP3);
  not not_82 (not_82_out, OP2);
  not not_83 (not_83_out, F30);
  not not_84 (not_84_out, F25);
  not not_85 (not_85_out, OP6);
  not not_86 (not_86_out, OP3);
  not not_87 (not_87_out, OP2);
  not not_88 (not_88_out, F30);
  not not_89 (not_89_out, F25);
  not not_90 (not_90_out, F14);
  not not_91 (not_91_out, F12);
  not not_92 (not_92_out, OP6);
  not not_93 (not_93_out, OP3);
  not not_94 (not_94_out, OP2);
  not not_95 (not_95_out, OP6);
  not not_96 (not_96_out, OP5);
  not not_97 (not_97_out, OP3);
  not not_98 (not_98_out, OP2);
  not not_99 (not_99_out, F14);
  not not_100 (not_100_out, F12);
  not not_101 (not_101_out, OP6);
  not not_102 (not_102_out, OP5);
  not not_103 (not_103_out, OP3);
  not not_104 (not_104_out, OP2);
  not not_105 (not_105_out, F30);
  not not_106 (not_106_out, F25);
  not not_107 (not_107_out, F13);
  not not_108 (not_108_out, OP6);
  not not_109 (not_109_out, OP5);
  not not_110 (not_110_out, OP3);
  not not_111 (not_111_out, OP2);
  not not_112 (not_112_out, F14);
  not not_113 (not_113_out, F13);
  not not_114 (not_114_out, F12);
  not not_115 (not_115_out, OP4);
  not not_116 (not_116_out, OP3);
  not not_117 (not_117_out, OP2);
  not not_118 (not_118_out, F14);
  not not_119 (not_119_out, F13);
  not not_120 (not_120_out, OP4);
  not not_121 (not_121_out, OP3);
  not not_122 (not_122_out, OP2);
  not not_123 (not_123_out, F30);
  not not_124 (not_124_out, F25);
  not not_125 (not_125_out, F14);
  not not_126 (not_126_out, F13);
  not not_127 (not_127_out, F12);
  not not_128 (not_128_out, OP6);
  not not_129 (not_129_out, OP3);
  not not_130 (not_130_out, OP2);
  not not_131 (not_131_out, F25);
  not not_132 (not_132_out, F14);
  not not_133 (not_133_out, F13);
  not not_134 (not_134_out, F12);
  not not_135 (not_135_out, OP6);
  not not_136 (not_136_out, OP3);
  not not_137 (not_137_out, OP2);
  not not_138 (not_138_out, F30);
  not not_139 (not_139_out, F25);
  not not_140 (not_140_out, OP6);
  not not_141 (not_141_out, OP3);
  not not_142 (not_142_out, OP2);
  not not_143 (not_143_out, F30);
  not not_144 (not_144_out, F25);
  not not_145 (not_145_out, F14);
  not not_146 (not_146_out, OP6);
  not not_147 (not_147_out, OP3);
  not not_148 (not_148_out, OP2);
  not not_149 (not_149_out, F14);
  not not_150 (not_150_out, F13);
  not not_151 (not_151_out, F12);
  not not_152 (not_152_out, OP6);
  not not_153 (not_153_out, OP5);
  not not_154 (not_154_out, OP3);
  not not_155 (not_155_out, OP2);
  not not_156 (not_156_out, OP6);
  not not_157 (not_157_out, OP5);
  not not_158 (not_158_out, OP3);
  not not_159 (not_159_out, OP2);
  not not_160 (not_160_out, F14);
  not not_161 (not_161_out, F12);
  not not_162 (not_162_out, OP6);
  not not_163 (not_163_out, OP5);
  not not_164 (not_164_out, OP4);
  not not_165 (not_165_out, OP3);
  not not_166 (not_166_out, OP2);
  not not_167 (not_167_out, F14);
  not not_168 (not_168_out, F12);
  not not_169 (not_169_out, OP6);
  not not_170 (not_170_out, OP4);
  not not_171 (not_171_out, OP3);
  not not_172 (not_172_out, OP2);
  not not_173 (not_173_out, F14);
  not not_174 (not_174_out, F13);
  not not_175 (not_175_out, F12);
  not not_176 (not_176_out, OP4);
  not not_177 (not_177_out, OP3);
  not not_178 (not_178_out, OP2);
  not not_179 (not_179_out, F14);
  not not_180 (not_180_out, F13);
  not not_181 (not_181_out, OP4);
  not not_182 (not_182_out, OP3);
  not not_183 (not_183_out, OP2);
  not not_184 (not_184_out, OP4);
  not not_185 (not_185_out, F14);
  not not_186 (not_186_out, F13);
  not not_187 (not_187_out, F12);
  not not_188 (not_188_out, OP4);
  not not_189 (not_189_out, OP3);
  not not_190 (not_190_out, F14);
  not not_191 (not_191_out, F13);
  not not_192 (not_192_out, OP6);
  not not_193 (not_193_out, OP5);
  not not_194 (not_194_out, OP4);
  not not_195 (not_195_out, OP3);
  not not_196 (not_196_out, OP2);
  not not_197 (not_197_out, F12);
  not not_198 (not_198_out, OP4);
  not not_199 (not_199_out, OP3);
  not not_200 (not_200_out, OP2);
  not not_201 (not_201_out, F30);
  not not_202 (not_202_out, F25);
  not not_203 (not_203_out, F12);
  not not_204 (not_204_out, OP6);
  not not_205 (not_205_out, OP3);
  not not_206 (not_206_out, OP2);
  not not_207 (not_207_out, F30);
  not not_208 (not_208_out, F25);
  not not_209 (not_209_out, F14);
  not not_210 (not_210_out, F12);
  not not_211 (not_211_out, OP6);
  not not_212 (not_212_out, OP3);
  not not_213 (not_213_out, OP2);
  not not_214 (not_214_out, F30);
  not not_215 (not_215_out, F25);
  not not_216 (not_216_out, F14);
  not not_217 (not_217_out, OP6);
  not not_218 (not_218_out, OP3);
  not not_219 (not_219_out, OP2);
  not not_220 (not_220_out, F12);
  not not_221 (not_221_out, OP6);
  not not_222 (not_222_out, OP5);
  not not_223 (not_223_out, OP3);
  not not_224 (not_224_out, OP2);
  not not_225 (not_225_out, F13);
  not not_226 (not_226_out, F12);
  not not_227 (not_227_out, OP6);
  not not_228 (not_228_out, OP5);
  not not_229 (not_229_out, OP3);
  not not_230 (not_230_out, OP2);
  not not_231 (not_231_out, F14);
  not not_232 (not_232_out, F12);
  not not_233 (not_233_out, OP6);
  not not_234 (not_234_out, OP5);
  not not_235 (not_235_out, OP3);
  not not_236 (not_236_out, OP2);
  not not_237 (not_237_out, F12);
  not not_238 (not_238_out, OP4);
  not not_239 (not_239_out, OP3);
  not not_240 (not_240_out, OP2);
  and and_1 (and_1_out, not_1_out, not_2_out, not_3_out, not_4_out, not_5_out, not_6_out, OP5, OP4, not_7_out, not_8_out);
  and and_2 (and_2_out, not_9_out, not_10_out, F14, F13, F12, not_11_out, OP5, OP4, not_12_out, not_13_out);
  and and_3 (and_3_out, not_14_out, not_15_out, not_16_out, F13, not_17_out, not_18_out, OP5, OP4, not_19_out, not_20_out);
  and and_4 (and_4_out, not_21_out, not_22_out, not_23_out, not_24_out, not_25_out, OP4, not_26_out, not_27_out);
  and and_5 (and_5_out, F14, F13, F12, not_28_out, not_29_out, OP4, not_30_out, not_31_out);
  and and_6 (and_6_out, F14, not_32_out, not_33_out, not_34_out, not_35_out, OP4, not_36_out, not_37_out);
  and and_7 (and_7_out, not_38_out, F13, not_39_out, not_40_out, not_41_out, OP4, not_42_out, not_43_out);
  and and_8 (and_8_out, F30, not_44_out, F14, not_45_out, F12, not_46_out, not_47_out, OP4, not_48_out, not_49_out);
  and and_9 (and_9_out, not_50_out, F13, not_51_out, not_52_out, not_53_out, not_54_out, not_55_out, not_56_out);
  and and_10 (and_10_out, not_57_out, F13, not_58_out, not_59_out, OP5, not_60_out, not_61_out, not_62_out);
  and and_11 (and_11_out, OP6, OP5, not_63_out, OP3, OP2);
  and and_12 (and_12_out, not_64_out, not_65_out, not_66_out, OP6, OP5, not_67_out, not_68_out, OP2);
  and and_13 (and_13_out, not_69_out, not_70_out, F12, not_71_out, not_72_out, not_73_out, not_74_out, not_75_out);
  and and_14 (and_14_out, F30, not_76_out, not_77_out, not_78_out, not_79_out, not_80_out, OP5, OP4, not_81_out, not_82_out);
  and and_15 (and_15_out, not_83_out, not_84_out, F14, F13, F12, not_85_out, OP5, OP4, not_86_out, not_87_out);
  and and_16 (and_16_out, not_88_out, not_89_out, not_90_out, F13, not_91_out, not_92_out, OP5, OP4, not_93_out, not_94_out);
  and and_17 (and_17_out, F14, F13, F12, not_95_out, not_96_out, OP4, not_97_out, not_98_out);
  and and_18 (and_18_out, not_99_out, F13, not_100_out, not_101_out, not_102_out, OP4, not_103_out, not_104_out);
  and and_19 (and_19_out, not_105_out, not_106_out, F14, not_107_out, F12, not_108_out, not_109_out, OP4, not_110_out, not_111_out);
  and and_20 (and_20_out, not_112_out, not_113_out, not_114_out, OP6, OP5, not_115_out, not_116_out, not_117_out);
  and and_21 (and_21_out, not_118_out, not_119_out, F12, OP6, OP5, not_120_out, not_121_out, not_122_out);
  and and_22 (and_22_out, not_123_out, not_124_out, not_125_out, not_126_out, not_127_out, not_128_out, OP5, OP4, not_129_out, not_130_out);
  and and_23 (and_23_out, F30, not_131_out, not_132_out, not_133_out, not_134_out, not_135_out, OP5, OP4, not_136_out, not_137_out);
  and and_24 (and_24_out, not_138_out, not_139_out, F14, F13, F12, not_140_out, OP5, OP4, not_141_out, not_142_out);
  and and_25 (and_25_out, not_143_out, not_144_out, not_145_out, F13, F12, not_146_out, OP5, OP4, not_147_out, not_148_out);
  and and_26 (and_26_out, not_149_out, not_150_out, not_151_out, not_152_out, not_153_out, OP4, not_154_out, not_155_out);
  and and_27 (and_27_out, F14, F13, F12, not_156_out, not_157_out, OP4, not_158_out, not_159_out);
  and and_28 (and_28_out, not_160_out, F13, not_161_out, not_162_out, not_163_out, not_164_out, not_165_out, not_166_out);
  and and_29 (and_29_out, not_167_out, F13, not_168_out, not_169_out, OP5, not_170_out, not_171_out, not_172_out);
  and and_30 (and_30_out, not_173_out, not_174_out, not_175_out, OP6, OP5, not_176_out, not_177_out, not_178_out);
  and and_31 (and_31_out, not_179_out, not_180_out, F12, OP6, OP5, not_181_out, not_182_out, not_183_out);
  and and_32 (and_32_out, OP6, OP5, not_184_out, OP3, OP2);
  and and_33 (and_33_out, not_185_out, not_186_out, not_187_out, OP6, OP5, not_188_out, not_189_out, OP2);
  and and_34 (and_34_out, not_190_out, not_191_out, F12, not_192_out, not_193_out, not_194_out, not_195_out, not_196_out);
  and and_35 (and_35_out, F14, F13, not_197_out, OP6, OP5, not_198_out, not_199_out, not_200_out);
  and and_36 (and_36_out, not_201_out, not_202_out, F14, F13, not_203_out, not_204_out, OP5, OP4, not_205_out, not_206_out);
  and and_37 (and_37_out, not_207_out, not_208_out, not_209_out, F13, not_210_out, not_211_out, OP5, OP4, not_212_out, not_213_out);
  and and_38 (and_38_out, not_214_out, not_215_out, not_216_out, F13, F12, not_217_out, OP5, OP4, not_218_out, not_219_out);
  and and_39 (and_39_out, F14, F13, not_220_out, not_221_out, not_222_out, OP4, not_223_out, not_224_out);
  and and_40 (and_40_out, F14, not_225_out, not_226_out, not_227_out, not_228_out, OP4, not_229_out, not_230_out);
  and and_41 (and_41_out, not_231_out, F13, not_232_out, not_233_out, not_234_out, OP4, not_235_out, not_236_out);
  and and_42 (and_42_out, F14, F13, not_237_out, OP6, OP5, not_238_out, not_239_out, not_240_out);
  or or_1 (S0, and_1_out, and_2_out, and_3_out, and_4_out, and_5_out, and_6_out, and_7_out, and_8_out, and_9_out, and_10_out, and_11_out, and_12_out, and_13_out);
  or or_2 (S1, and_14_out, and_15_out, and_16_out, and_17_out, and_18_out, and_19_out, and_20_out, and_21_out);
  or or_3 (S2, and_22_out, and_23_out, and_24_out, and_25_out, and_26_out, and_27_out, and_28_out, and_29_out, and_30_out, and_31_out, and_32_out, and_33_out, and_34_out, and_35_out);
  or or_4 (S3, and_36_out, and_37_out, and_38_out, and_39_out, and_40_out, and_41_out, and_42_out);
endmodule

// 控制信号生成
module \控制信号自动生成  (
  input  OP2,
  input  OP3,
  input  OP4,
  input  OP5,
  input  OP6,
  input  F12,
  input  F13,
  input  F14,
  input  F25,
  input  F30,
  output MemToReg,
  output MemWrite,
  output ALU_SRC,
  output RegWrite,
  output ecall,
  output S_Type,
  output BEQ,
  output BNE,
  output JALR,
  output JAL,
  output LUI,
  output AUIPC,
  output LH,
  output BLTU,
  output CSRRSI,
  output CSRRCI
);

  wire and_1_out, and_2_out, and_4_out, and_5_out, and_6_out, and_7_out, and_8_out, and_9_out, and_10_out,
       and_11_out, and_12_out, and_13_out, and_14_out, and_15_out, and_16_out, and_17_out, and_18_out,
       and_19_out, and_20_out, and_21_out, and_22_out, and_23_out, and_24_out, and_25_out, and_26_out,
       and_27_out, and_28_out, and_29_out, and_30_out, and_31_out, and_32_out, and_33_out, and_34_out,
       and_35_out, and_36_out, not_1_out, not_2_out, not_3_out, not_4_out, not_5_out, not_6_out, not_7_out,
       not_8_out, not_9_out, not_10_out, not_11_out, not_12_out, not_13_out, not_14_out, not_15_out,
       not_16_out, not_17_out, not_18_out, not_19_out, not_20_out, not_21_out, not_22_out, not_23_out,
       not_24_out, not_25_out, not_26_out, not_27_out, not_28_out, not_29_out, not_30_out, not_31_out,
       not_32_out, not_33_out, not_34_out, not_35_out, not_36_out, not_37_out, not_38_out, not_39_out,
       not_40_out, not_41_out, not_42_out, not_43_out, not_44_out, not_45_out, not_46_out, not_47_out,
       not_48_out, not_49_out, not_50_out, not_51_out, not_52_out, not_53_out, not_54_out, not_55_out,
       not_56_out, not_57_out, not_58_out, not_59_out, not_60_out, not_61_out, not_62_out, not_63_out,
       not_64_out, not_65_out, not_66_out, not_67_out, not_68_out, not_69_out, not_70_out, not_71_out,
       not_72_out, not_73_out, not_74_out, not_75_out, not_76_out, not_77_out, not_78_out, not_79_out,
       not_80_out, not_81_out, not_82_out, not_83_out, not_84_out, not_85_out, not_86_out, not_87_out,
       not_88_out, not_89_out, not_90_out, not_91_out, not_92_out, not_93_out, not_94_out, not_95_out,
       not_96_out, not_97_out, not_98_out, not_99_out, not_100_out, not_101_out, not_102_out, not_103_out,
       not_104_out, not_105_out, not_106_out, not_107_out, not_108_out, not_109_out, not_110_out,
       not_111_out, not_112_out, not_113_out, not_114_out, not_115_out, not_116_out, not_117_out,
       not_118_out, not_119_out, not_120_out, not_121_out, not_122_out, not_123_out, not_124_out,
       not_125_out, not_126_out, not_127_out, not_128_out, not_129_out, not_130_out, not_131_out,
       not_132_out, not_133_out, not_134_out, not_135_out, not_136_out, not_137_out, not_138_out,
       not_139_out, not_140_out, not_141_out, not_142_out, not_143_out, not_144_out, not_145_out,
       not_146_out, not_147_out, not_148_out, not_149_out, not_150_out, not_151_out, not_152_out,
       not_153_out, not_154_out, not_155_out, not_156_out, not_157_out, not_158_out, not_159_out,
       not_160_out, not_161_out, not_162_out, not_163_out, not_164_out, not_165_out, not_166_out,
       not_167_out, not_168_out, not_169_out, not_170_out, not_171_out, not_172_out, not_173_out,
       not_174_out, not_175_out, not_176_out, not_177_out, not_178_out, not_179_out, not_180_out,
       not_181_out, not_182_out, not_183_out, not_184_out, not_185_out, not_186_out, not_187_out,
       not_188_out, not_189_out, not_190_out, not_191_out, not_192_out, not_193_out, not_194_out,
       not_195_out, not_196_out, not_197_out, not_198_out, not_199_out, not_200_out, not_201_out,
       not_202_out, not_203_out, not_204_out, not_205_out, not_206_out, not_207_out, not_208_out,
       not_209_out, not_210_out, not_211_out, not_212_out, not_213_out, not_214_out, not_215_out,
       not_216_out, not_217_out, not_218_out, not_219_out, not_220_out, not_221_out, not_222_out,
       not_223_out, not_224_out, not_225_out, not_226_out, not_227_out, not_228_out, not_229_out,
       not_230_out, not_231_out, not_232_out, not_233_out, not_234_out, not_235_out, not_236_out,
       not_237_out, not_238_out, not_239_out, not_240_out, not_241_out, not_242_out, not_243_out,
       not_244_out, not_245_out, not_246_out, not_247_out, not_248_out, not_249_out, not_250_out,
       not_251_out, not_252_out, not_253_out, not_254_out, not_255_out, not_256_out;

  not not_1 (not_1_out, F14);
  not not_2 (not_2_out, F12);
  not not_3 (not_3_out, OP6);
  not not_4 (not_4_out, OP5);
  not not_5 (not_5_out, OP4);
  not not_6 (not_6_out, OP3);
  not not_7 (not_7_out, OP2);
  not not_8 (not_8_out, F14);
  not not_9 (not_9_out, F13);
  not not_10 (not_10_out, OP6);
  not not_11 (not_11_out, OP5);
  not not_12 (not_12_out, OP4);
  not not_13 (not_13_out, OP3);
  not not_14 (not_14_out, OP2);
  not not_15 (not_15_out, F14);
  not not_16 (not_16_out, F12);
  not not_17 (not_17_out, OP6);
  not not_18 (not_18_out, OP4);
  not not_19 (not_19_out, OP3);
  not not_20 (not_20_out, OP2);
  not not_21 (not_21_out, F14);
  not not_22 (not_22_out, F13);
  not not_23 (not_23_out, F12);
  not not_24 (not_24_out, OP6);
  not not_25 (not_25_out, OP5);
  not not_26 (not_26_out, OP3);
  not not_27 (not_27_out, OP2);
  not not_28 (not_28_out, OP6);
  not not_29 (not_29_out, OP5);
  not not_30 (not_30_out, OP3);
  not not_31 (not_31_out, OP2);
  not not_32 (not_32_out, F12);
  not not_33 (not_33_out, OP6);
  not not_34 (not_34_out, OP5);
  not not_35 (not_35_out, OP3);
  not not_36 (not_36_out, OP2);
  not not_37 (not_37_out, F13);
  not not_38 (not_38_out, F12);
  not not_39 (not_39_out, OP6);
  not not_40 (not_40_out, OP5);
  not not_41 (not_41_out, OP3);
  not not_42 (not_42_out, OP2);
  not not_43 (not_43_out, F14);
  not not_44 (not_44_out, F12);
  not not_45 (not_45_out, OP6);
  not not_46 (not_46_out, OP5);
  not not_47 (not_47_out, OP3);
  not not_48 (not_48_out, OP2);
  not not_49 (not_49_out, F30);
  not not_50 (not_50_out, F25);
  not not_51 (not_51_out, F14);
  not not_52 (not_52_out, F13);
  not not_53 (not_53_out, OP6);
  not not_54 (not_54_out, OP5);
  not not_55 (not_55_out, OP3);
  not not_56 (not_56_out, OP2);
  not not_57 (not_57_out, F30);
  not not_58 (not_58_out, F25);
  not not_59 (not_59_out, F13);
  not not_60 (not_60_out, OP6);
  not not_61 (not_61_out, OP5);
  not not_62 (not_62_out, OP3);
  not not_63 (not_63_out, OP2);
  not not_64 (not_64_out, F25);
  not not_65 (not_65_out, F13);
  not not_66 (not_66_out, OP6);
  not not_67 (not_67_out, OP5);
  not not_68 (not_68_out, OP3);
  not not_69 (not_69_out, OP2);
  not not_70 (not_70_out, F14);
  not not_71 (not_71_out, F12);
  not not_72 (not_72_out, OP6);
  not not_73 (not_73_out, OP5);
  not not_74 (not_74_out, OP4);
  not not_75 (not_75_out, OP3);
  not not_76 (not_76_out, OP2);
  not not_77 (not_77_out, F14);
  not not_78 (not_78_out, F12);
  not not_79 (not_79_out, OP6);
  not not_80 (not_80_out, OP4);
  not not_81 (not_81_out, OP3);
  not not_82 (not_82_out, OP2);
  not not_83 (not_83_out, F14);
  not not_84 (not_84_out, F13);
  not not_85 (not_85_out, OP6);
  not not_86 (not_86_out, OP5);
  not not_87 (not_87_out, OP4);
  not not_88 (not_88_out, OP3);
  not not_89 (not_89_out, OP2);
  not not_90 (not_90_out, F30);
  not not_91 (not_91_out, F25);
  not not_92 (not_92_out, F14);
  not not_93 (not_93_out, F13);
  not not_94 (not_94_out, F12);
  not not_95 (not_95_out, OP6);
  not not_96 (not_96_out, OP3);
  not not_97 (not_97_out, OP2);
  not not_98 (not_98_out, F25);
  not not_99 (not_99_out, F14);
  not not_100 (not_100_out, F13);
  not not_101 (not_101_out, F12);
  not not_102 (not_102_out, OP6);
  not not_103 (not_103_out, OP3);
  not not_104 (not_104_out, OP2);
  not not_105 (not_105_out, F30);
  not not_106 (not_106_out, F25);
  not not_107 (not_107_out, OP6);
  not not_108 (not_108_out, OP3);
  not not_109 (not_109_out, OP2);
  not not_110 (not_110_out, F30);
  not not_111 (not_111_out, F25);
  not not_112 (not_112_out, F12);
  not not_113 (not_113_out, OP6);
  not not_114 (not_114_out, OP3);
  not not_115 (not_115_out, OP2);
  not not_116 (not_116_out, F30);
  not not_117 (not_117_out, F25);
  not not_118 (not_118_out, F14);
  not not_119 (not_119_out, F12);
  not not_120 (not_120_out, OP6);
  not not_121 (not_121_out, OP3);
  not not_122 (not_122_out, OP2);
  not not_123 (not_123_out, F30);
  not not_124 (not_124_out, F25);
  not not_125 (not_125_out, F14);
  not not_126 (not_126_out, OP6);
  not not_127 (not_127_out, OP3);
  not not_128 (not_128_out, OP2);
  not not_129 (not_129_out, F14);
  not not_130 (not_130_out, F13);
  not not_131 (not_131_out, F12);
  not not_132 (not_132_out, OP6);
  not not_133 (not_133_out, OP5);
  not not_134 (not_134_out, OP3);
  not not_135 (not_135_out, OP2);
  not not_136 (not_136_out, OP6);
  not not_137 (not_137_out, OP5);
  not not_138 (not_138_out, OP3);
  not not_139 (not_139_out, OP2);
  not not_140 (not_140_out, F12);
  not not_141 (not_141_out, OP6);
  not not_142 (not_142_out, OP5);
  not not_143 (not_143_out, OP3);
  not not_144 (not_144_out, OP2);
  not not_145 (not_145_out, F13);
  not not_146 (not_146_out, F12);
  not not_147 (not_147_out, OP6);
  not not_148 (not_148_out, OP5);
  not not_149 (not_149_out, OP3);
  not not_150 (not_150_out, OP2);
  not not_151 (not_151_out, F14);
  not not_152 (not_152_out, F12);
  not not_153 (not_153_out, OP6);
  not not_154 (not_154_out, OP5);
  not not_155 (not_155_out, OP3);
  not not_156 (not_156_out, OP2);
  not not_157 (not_157_out, F30);
  not not_158 (not_158_out, F25);
  not not_159 (not_159_out, F14);
  not not_160 (not_160_out, F13);
  not not_161 (not_161_out, OP6);
  not not_162 (not_162_out, OP5);
  not not_163 (not_163_out, OP3);
  not not_164 (not_164_out, OP2);
  not not_165 (not_165_out, F30);
  not not_166 (not_166_out, F25);
  not not_167 (not_167_out, F13);
  not not_168 (not_168_out, OP6);
  not not_169 (not_169_out, OP5);
  not not_170 (not_170_out, OP3);
  not not_171 (not_171_out, OP2);
  not not_172 (not_172_out, F25);
  not not_173 (not_173_out, F13);
  not not_174 (not_174_out, OP6);
  not not_175 (not_175_out, OP5);
  not not_176 (not_176_out, OP3);
  not not_177 (not_177_out, OP2);
  not not_178 (not_178_out, F14);
  not not_179 (not_179_out, F12);
  not not_180 (not_180_out, OP6);
  not not_181 (not_181_out, OP5);
  not not_182 (not_182_out, OP4);
  not not_183 (not_183_out, OP3);
  not not_184 (not_184_out, OP2);
  not not_185 (not_185_out, OP4);
  not not_186 (not_186_out, F14);
  not not_187 (not_187_out, F13);
  not not_188 (not_188_out, F12);
  not not_189 (not_189_out, OP4);
  not not_190 (not_190_out, OP3);
  not not_191 (not_191_out, OP6);
  not not_192 (not_192_out, OP5);
  not not_193 (not_193_out, OP3);
  not not_194 (not_194_out, OP6);
  not not_195 (not_195_out, OP3);
  not not_196 (not_196_out, F14);
  not not_197 (not_197_out, F13);
  not not_198 (not_198_out, OP6);
  not not_199 (not_199_out, OP5);
  not not_200 (not_200_out, OP4);
  not not_201 (not_201_out, OP3);
  not not_202 (not_202_out, OP2);
  not not_203 (not_203_out, F14);
  not not_204 (not_204_out, F13);
  not not_205 (not_205_out, F12);
  not not_206 (not_206_out, OP3);
  not not_207 (not_207_out, OP2);
  not not_208 (not_208_out, F14);
  not not_209 (not_209_out, F13);
  not not_210 (not_210_out, F12);
  not not_211 (not_211_out, OP3);
  not not_212 (not_212_out, OP2);
  not not_213 (not_213_out, F14);
  not not_214 (not_214_out, F12);
  not not_215 (not_215_out, OP6);
  not not_216 (not_216_out, OP4);
  not not_217 (not_217_out, OP3);
  not not_218 (not_218_out, OP2);
  not not_219 (not_219_out, F14);
  not not_220 (not_220_out, F13);
  not not_221 (not_221_out, F12);
  not not_222 (not_222_out, OP4);
  not not_223 (not_223_out, OP3);
  not not_224 (not_224_out, OP2);
  not not_225 (not_225_out, F14);
  not not_226 (not_226_out, F13);
  not not_227 (not_227_out, OP4);
  not not_228 (not_228_out, OP3);
  not not_229 (not_229_out, OP2);
  not not_230 (not_230_out, F14);
  not not_231 (not_231_out, F13);
  not not_232 (not_232_out, F12);
  not not_233 (not_233_out, OP4);
  not not_234 (not_234_out, OP3);
  not not_235 (not_235_out, OP4);
  not not_236 (not_236_out, OP6);
  not not_237 (not_237_out, OP3);
  not not_238 (not_238_out, OP6);
  not not_239 (not_239_out, OP5);
  not not_240 (not_240_out, OP3);
  not not_241 (not_241_out, F14);
  not not_242 (not_242_out, F13);
  not not_243 (not_243_out, OP6);
  not not_244 (not_244_out, OP5);
  not not_245 (not_245_out, OP4);
  not not_246 (not_246_out, OP3);
  not not_247 (not_247_out, OP2);
  not not_248 (not_248_out, F12);
  not not_249 (not_249_out, OP4);
  not not_250 (not_250_out, OP3);
  not not_251 (not_251_out, OP2);
  not not_252 (not_252_out, F12);
  not not_253 (not_253_out, OP3);
  not not_254 (not_254_out, OP2);
  not not_255 (not_255_out, OP3);
  not not_256 (not_256_out, OP2);
  and and_1 (and_1_out, not_1_out, F13, not_2_out, not_3_out, not_4_out, not_5_out, not_6_out, not_7_out);
  and and_2 (and_2_out, not_8_out, not_9_out, F12, not_10_out, not_11_out, not_12_out, not_13_out, not_14_out);
  and and_3 (MemWrite, not_15_out, F13, not_16_out, not_17_out, OP5, not_18_out, not_19_out, not_20_out);
  and and_4 (and_4_out, not_21_out, not_22_out, not_23_out, not_24_out, not_25_out, OP4, not_26_out, not_27_out);
  and and_5 (and_5_out, F14, F13, F12, not_28_out, not_29_out, OP4, not_30_out, not_31_out);
  and and_6 (and_6_out, F14, F13, not_32_out, not_33_out, not_34_out, OP4, not_35_out, not_36_out);
  and and_7 (and_7_out, F14, not_37_out, not_38_out, not_39_out, not_40_out, OP4, not_41_out, not_42_out);
  and and_8 (and_8_out, not_43_out, F13, not_44_out, not_45_out, not_46_out, OP4, not_47_out, not_48_out);
  and and_9 (and_9_out, not_49_out, not_50_out, not_51_out, not_52_out, F12, not_53_out, not_54_out, OP4, not_55_out, not_56_out);
  and and_10 (and_10_out, not_57_out, not_58_out, F14, not_59_out, F12, not_60_out, not_61_out, OP4, not_62_out, not_63_out);
  and and_11 (and_11_out, F30, not_64_out, F14, not_65_out, F12, not_66_out, not_67_out, OP4, not_68_out, not_69_out);
  and and_12 (and_12_out, not_70_out, F13, not_71_out, not_72_out, not_73_out, not_74_out, not_75_out, not_76_out);
  and and_13 (and_13_out, not_77_out, F13, not_78_out, not_79_out, OP5, not_80_out, not_81_out, not_82_out);
  and and_14 (and_14_out, not_83_out, not_84_out, F12, not_85_out, not_86_out, not_87_out, not_88_out, not_89_out);
  and and_15 (and_15_out, not_90_out, not_91_out, not_92_out, not_93_out, not_94_out, not_95_out, OP5, OP4, not_96_out, not_97_out);
  and and_16 (and_16_out, F30, not_98_out, not_99_out, not_100_out, not_101_out, not_102_out, OP5, OP4, not_103_out, not_104_out);
  and and_17 (and_17_out, not_105_out, not_106_out, F14, F13, F12, not_107_out, OP5, OP4, not_108_out, not_109_out);
  and and_18 (and_18_out, not_110_out, not_111_out, F14, F13, not_112_out, not_113_out, OP5, OP4, not_114_out, not_115_out);
  and and_19 (and_19_out, not_116_out, not_117_out, not_118_out, F13, not_119_out, not_120_out, OP5, OP4, not_121_out, not_122_out);
  and and_20 (and_20_out, not_123_out, not_124_out, not_125_out, F13, F12, not_126_out, OP5, OP4, not_127_out, not_128_out);
  and and_21 (and_21_out, not_129_out, not_130_out, not_131_out, not_132_out, not_133_out, OP4, not_134_out, not_135_out);
  and and_22 (and_22_out, F14, F13, F12, not_136_out, not_137_out, OP4, not_138_out, not_139_out);
  and and_23 (and_23_out, F14, F13, not_140_out, not_141_out, not_142_out, OP4, not_143_out, not_144_out);
  and and_24 (and_24_out, F14, not_145_out, not_146_out, not_147_out, not_148_out, OP4, not_149_out, not_150_out);
  and and_25 (and_25_out, not_151_out, F13, not_152_out, not_153_out, not_154_out, OP4, not_155_out, not_156_out);
  and and_26 (and_26_out, not_157_out, not_158_out, not_159_out, not_160_out, F12, not_161_out, not_162_out, OP4, not_163_out, not_164_out);
  and and_27 (and_27_out, not_165_out, not_166_out, F14, not_167_out, F12, not_168_out, not_169_out, OP4, not_170_out, not_171_out);
  and and_28 (and_28_out, F30, not_172_out, F14, not_173_out, F12, not_174_out, not_175_out, OP4, not_176_out, not_177_out);
  and and_29 (and_29_out, not_178_out, F13, not_179_out, not_180_out, not_181_out, not_182_out, not_183_out, not_184_out);
  and and_30 (and_30_out, OP6, OP5, not_185_out, OP3, OP2);
  and and_31 (and_31_out, not_186_out, not_187_out, not_188_out, OP6, OP5, not_189_out, not_190_out, OP2);
  and and_32 (and_32_out, not_191_out, not_192_out, OP4, not_193_out, OP2);
  and and_33 (and_33_out, not_194_out, OP5, OP4, not_195_out, OP2);
  and and_34 (and_34_out, not_196_out, not_197_out, F12, not_198_out, not_199_out, not_200_out, not_201_out, not_202_out);
  and and_35 (and_35_out, not_203_out, not_204_out, not_205_out, OP6, OP5, OP4, not_206_out, not_207_out);
  and and_36 (and_36_out, not_208_out, not_209_out, not_210_out, OP6, OP5, OP4, not_211_out, not_212_out);
  and and_37 (S_Type, not_213_out, F13, not_214_out, not_215_out, OP5, not_216_out, not_217_out, not_218_out);
  and and_38 (BEQ, not_219_out, not_220_out, not_221_out, OP6, OP5, not_222_out, not_223_out, not_224_out);
  and and_39 (BNE, not_225_out, not_226_out, F12, OP6, OP5, not_227_out, not_228_out, not_229_out);
  and and_40 (JALR, not_230_out, not_231_out, not_232_out, OP6, OP5, not_233_out, not_234_out, OP2);
  and and_41 (JAL, OP6, OP5, not_235_out, OP3, OP2);
  and and_42 (LUI, not_236_out, OP5, OP4, not_237_out, OP2);
  and and_43 (AUIPC, not_238_out, not_239_out, OP4, not_240_out, OP2);
  and and_44 (LH, not_241_out, not_242_out, F12, not_243_out, not_244_out, not_245_out, not_246_out, not_247_out);
  and and_45 (BLTU, F14, F13, not_248_out, OP6, OP5, not_249_out, not_250_out, not_251_out);
  and and_46 (CSRRSI, F14, F13, not_252_out, OP6, OP5, OP4, not_253_out, not_254_out);
  and and_47 (CSRRCI, F14, F13, F12, OP6, OP5, OP4, not_255_out, not_256_out);
  or or_1 (MemToReg, and_1_out, and_2_out);
  or or_2 (ecall, and_35_out, and_36_out);
  or or_3 (ALU_SRC, and_4_out, and_5_out, and_6_out, and_7_out, and_8_out, and_9_out, and_10_out, and_11_out, and_12_out, and_13_out, and_14_out);
  or or_4 (RegWrite, and_15_out, and_16_out, and_17_out, and_18_out, and_19_out, and_20_out, and_21_out, and_22_out, and_23_out, and_24_out, and_25_out, and_26_out, and_27_out, and_28_out, and_29_out, and_30_out, and_31_out, and_32_out, and_33_out, and_34_out);
endmodule

// ALU
module ALU (
  input  [31:0] X,
  input  [31:0] Y,
  input  [3:0] AluOP,
  output out_4,
  output Equal,
  output out_6,
  output [31:0] Result,
  output [31:0] Result_2
);

  wire [0:0] comparator_1_lt, comparator_2_lt;
  wire [31:0] adder_1_out, AND_out, divider_1_out, divider_1_rem, multiplier_1_cout, multiplier_1_out,
       NOR_out, OR_out, shifter_1_out, shifter_2_out, shifter_3_out, subtractor_1_out, XOR_out;

  assign AND_out = X & Y;  // AND_Gate AND, 32 bits wide
  assign OR_out = X | Y;  // OR_Gate OR, 32 bits wide
  Shifter #(.width(32), .shift("ll")) shifter_1 (.in(X), .\dist (Y[4:0]), .out(shifter_1_out));
  Shifter #(.width(32), .shift("ar")) shifter_2 (.in(X), .\dist (Y[4:0]), .out(shifter_2_out));
  Shifter #(.width(32), .shift("lr")) shifter_3 (.in(X), .\dist (Y[4:0]), .out(shifter_3_out));
  Multiplier #(.width(32)) multiplier_1 (.a(X), .b(Y), .out(multiplier_1_out), .cout(multiplier_1_cout));  // open: cin
  Divider #(.width(32)) divider_1 (.a(X), .b(Y), .out(divider_1_out), .rem(divider_1_rem));  // open: upper
  Adder #(.width(32)) adder_1 (.a(X), .b(Y), .out(adder_1_out));  // open: cin, cout
  Subtractor #(.width(32)) subtractor_1 (.a(X), .b(Y), .out(subtractor_1_out));  // open: bin, bout
  assign XOR_out = X ^ Y;  // XOR_Gate XOR, 32 bits wide
  assign NOR_out = ~(X | Y);  // NOR_Gate NOR, 32 bits wide
  Comparator #(.width(32), .mode("twosComplement")) comparator_1 (
    .a(X), .b(Y), .eq(Equal), .lt(comparator_1_lt[0]));  // open: gt
  Comparator #(.width(32), .mode("unsigned")) comparator_2 (.a(X), .b(Y), .lt(comparator_2_lt[0]));  // open: gt, eq
  Multiplexer #(.select(4), .width(32), .disabled("Z"), .enable("false")) multiplexer_1 (
    .in0(shifter_1_out), .in1(shifter_2_out), .in2(shifter_3_out), .in3(multiplier_1_out),
    .in4(divider_1_out), .in5(adder_1_out), .in6(subtractor_1_out), .in7(AND_out), .in8(OR_out),
    .in9(XOR_out), .in10(NOR_out), .in11({{31{1'b0}}, comparator_1_lt[0]}),
    .in12({{31{1'b0}}, comparator_2_lt[0]}), .in13({32{1'b0}}), .in14({32{1'b0}}), .in15({32{1'b0}}),
    .out(Result), .sel(AluOP));
  Multiplexer #(.select(4), .width(32), .disabled("Z"), .enable("false")) multiplexer_2 (
    .in0({32{1'b0}}), .in1({32{1'b0}}), .in2({32{1'b0}}), .in3(multiplier_1_cout), .in4(divider_1_rem),
    .in5({32{1'b0}}), .in6({32{1'b0}}), .in7({32{1'b0}}), .in8({32{1'b0}}), .in9({32{1'b0}}),
    .in10({32{1'b0}}), .in11({32{1'b0}}), .in12({32{1'b0}}), .in13({32{1'b0}}), .in14({32{1'b0}}),
    .in15({32{1'b0}}), .out(Result_2), .sel(AluOP));
  Multiplexer #(.select(4), .width(1), .disabled("Z"), .enable("false")) multiplexer_3 (
    .in0(1'b0), .in1(1'b0), .in2(1'b0), .in3(1'b0), .in4(1'b0), .in5(1'b0), .in6(1'b0), .in7(1'b0),
    .in8(1'b0), .in9(1'b0), .in10(1'b0), .in11(comparator_1_lt[0]), .in12(comparator_2_lt[0]), .in13(1'b0),
    .in14(1'b0), .in15(1'b0), .out(out_6), .sel(AluOP));
  not not_1 (out_4, out_6);

  // Other names for the same wires on the sheet: Result2[31:0] = Result_2; S[3:0] = AluOP; tunnel = out_6;
  //   tunnel_t = out_4

  // Notes on the sheet:
  //   不要改变此引脚区域内容，也不要改变ALU封装形式
  //   输入引脚
  //   输出引脚
endmodule

module Regifile (
  input  [31:0] Din,
  input  Clk,
  input  WE,
  input  [4:0] R1_num,
  input  [4:0] W_num,
  input  [4:0] R2_num,
  output [31:0] R1,
  output [31:0] R2
);

  // RegisterFile registerfile_1: pin names not known; wires that end beside it: Din, Clk, WE, W_num, R1_num, R2_num, R1, R2

  // Notes on the sheet:
  //   寄存器堆使用下降沿触发
  //   其他寄存器使用上升沿触发
  //   可以解决ID与WB的数据冲突
endmodule

module \理想流水线  (
  output RegWrite,
  output MemWrite,
  output [31:0] IF_PC,
  output [31:0] ID_PC,
  output [31:0] EX_PC,
  output [31:0] M_PC,
  output [31:0] WB_PC,
  output [31:0] RDin,
  output [31:0] MDin,
  output [31:0] LedData
);

  wire alu_1_equal, alu_1_out_4, alu_1_out_6, and_1_out, and_2_out, and_3_out, CLK, clock_1_out, clock_2_out,
       comparator_1_eq, comparator_1_lt, d_ff_1_q, ecall_deal_1_halt, ex_mem_1_haltout, ex_mem_1_lhout,
       ex_mem_1_memtoregout, ex_mem_1_regwriteout, Go, halt, id_ex_1_alusrcbout, id_ex_1_beqout,
       id_ex_1_bltuout, id_ex_1_bneout, id_ex_1_ecallout, id_ex_1_jalout, id_ex_1_jalrout, id_ex_1_lhout,
       id_ex_1_memtoregout, id_ex_1_memwriteout, id_ex_1_regwriteout, IR1, IR2, IR3, mem_we_1_memtoregout,
       nand_1_out, not_1_out, not_2_out, not_3_out, or_1_out, or_2_out, or_3_out, or_4_out, RST, W1, W2, W3,
       \单周期硬布线控制器_1_alu_src , \单周期硬布线控制器_1_auipc , \单周期硬布线控制器_1_beq , \单周期硬布线控制器_1_bltu , \单周期硬布线控制器_1_bne ,
       \单周期硬布线控制器_1_ecall , \单周期硬布线控制器_1_jal , \单周期硬布线控制器_1_jalr , \单周期硬布线控制器_1_lh , \单周期硬布线控制器_1_lui ,
       \单周期硬布线控制器_1_memtoreg , \单周期硬布线控制器_1_memwrite , \单周期硬布线控制器_1_regwrite , \单周期硬布线控制器_1_s_type ;
  wire [3:0] id_ex_1_aluopout, \单周期硬布线控制器_1_alu_op ;
  wire [4:0] ex_mem_1_rdout, id_ex_1_rdout, mem_we_1_rdout, multiplexer_2_out, multiplexer_3_out;
  wire [12:0] CNT_num;
  wire [15:0] \LoadUse次数 , \总周期数 , \插入气泡数 , \无条件分支数 , \条件分支成功数 ;
  wire [31:0] adder_1_out, adder_2_out, alu_1_result, bit_extender_1_out, bit_extender_2_out,
       bit_extender_3_out, bit_extender_4_out, bit_extender_5_out, bit_extender_6_out, EX_IR,
       ex_mem_1_alu_resultout, id_ex_1_immout, id_ex_1_rs1out, id_ex_1_rs2out, ID_IR, if_id_1_irout, IF_IR,
       MEM_IR, mem_we_1_alu_resultout, mem_we_1_mem_resultout, multiplexer_1_out, multiplexer_4_out,
       multiplexer_5_out, multiplexer_6_out, multiplexer_7_out, multiplexer_8_out, multiplexer_9_out,
       multiplexer_10_out, ram_1_data, regifile_1_r1, regifile_1_r2, riscv_probe_4_p1, WB_IR;

  Button \u_总复位  (.out(RST));
  Button _1 (.out(IR1));
  Button _2 (.out(IR2));
  Button _3 (.out(IR3));
  // Probe on \总周期数 
  // Probe on \总周期数 
  Button \u_继续运行  (.out(Go));
  LED #(.active("true")) led_1 (.in(W1));
  LED #(.active("true")) led_2 (.in(W2));
  LED #(.active("true")) led_3 (.in(W3));
  Multiplexer #(.select(1), .width(32), .disabled("Z"), .enable("false")) multiplexer_1 (
    .in0(adder_1_out), .in1(adder_2_out), .out(multiplexer_1_out), .sel(or_3_out));
  Hex_Digit_Display hex_digit_display_1 (.value(LedData[31:28]));  // open: dp
  // Probe on IF_PC[19:0]
  // RiscV_Probe riscv_probe_1: pin names not known; wires that end beside it: IF_IR
  // Probe on multiplexer_1_out
  Register #(.width(32), .trigger("rising"), .Select("low")) PC (
    .D(multiplexer_1_out), .en(not_1_out), .Q(IF_PC), .clk(CLK), .clr(RST));
  not not_1 (not_1_out, halt);
  Hex_Digit_Display hex_digit_display_2 (.value(LedData[27:24]));  // open: dp
  Hex_Digit_Display hex_digit_display_3 (.value(LedData[23:20]));  // open: dp
  // Probe on ID_PC[19:0]
  // RiscV_Probe riscv_probe_2: pin names not known; wires that end beside it: ID_IR
  // Probe on IF_PC
  Hex_Digit_Display hex_digit_display_4 (.value(LedData[19:16]));  // open: dp
  Hex_Digit_Display hex_digit_display_5 (.value(LedData[15:12]));  // open: dp
  Adder #(.width(32)) adder_1 (.a(IF_PC), .b(32'h4), .out(adder_1_out));  // open: cin, cout
  Hex_Digit_Display hex_digit_display_6 (.value(LedData[11:8]));  // open: dp
  Hex_Digit_Display hex_digit_display_7 (.value(LedData[7:4]));  // open: dp
  Clock #(.highDuration(1), .lowDuration(1)) clock_1 (.out(clock_1_out));
  // Probe on EX_PC[19:0]
  // RiscV_Probe riscv_probe_3: pin names not known; wires that end beside it: clock_1_out, EX_IR, CLK
  // RiscV_Probe riscv_probe_4: pin names not known; wires that end beside it: riscv_probe_4_p1
  ROM #(.addrWidth(10), .dataWidth(32), .Select("high")) \u_指令存储器  (.addr(IF_PC[11:2]), .data(riscv_probe_4_p1));
  Hex_Digit_Display hex_digit_display_8 (.value(LedData[3:0]));  // open: dp
  // Probe on \总周期数 
  // Probe on M_PC[19:0]
  // RiscV_Probe riscv_probe_5: pin names not known; wires that end beside it: MEM_IR
  IF_ID if_id_1 (
    .IRin(riscv_probe_4_p1), .PCin(IF_PC), .CLK(CLK), .RST(RST), .halt(halt), .IRout(if_id_1_irout),
    .PCout(ID_PC));  // open: en
  // Probe on \总周期数 
  // Probe on \无条件分支数 
  // Probe on \条件分支成功数 
  // Probe on \插入气泡数 
  // Probe on \LoadUse次数 
  // Probe on IF_PC[11:0]
  // Probe on WB_PC[19:0]
  // RiscV_Probe riscv_probe_6: pin names not known; wires that end beside it: WB_IR
  \单周期硬布线控制器  \u_单周期硬布线控制器_1  (
    .Funct({if_id_1_irout[30], if_id_1_irout[25], if_id_1_irout[14:12]}), .OP(if_id_1_irout[6:2]),
    .ALU_OP(\单周期硬布线控制器_1_alu_op ), .MemToReg(\单周期硬布线控制器_1_memtoreg ), .MemWrite(\单周期硬布线控制器_1_memwrite ),
    .ALU_SRC(\单周期硬布线控制器_1_alu_src ), .RegWrite(\单周期硬布线控制器_1_regwrite ), .ecall(\单周期硬布线控制器_1_ecall ),
    .S_type(\单周期硬布线控制器_1_s_type ), .Jalr(\单周期硬布线控制器_1_jalr ), .Beq(\单周期硬布线控制器_1_beq ),
    .JAL(\单周期硬布线控制器_1_jal ), .Bne(\单周期硬布线控制器_1_bne ), .AUIPC(\单周期硬布线控制器_1_auipc ), .BLTU(\单周期硬布线控制器_1_bltu ),
    .LH(\单周期硬布线控制器_1_lh ), .LUI(\单周期硬布线控制器_1_lui ));  // open: CSRRSI, CSRRCI
  Multiplexer #(.select(1), .width(5), .disabled("Z"), .enable("false")) multiplexer_2 (
    .in0(if_id_1_irout[19:15]), .in1(5'b10001), .out(multiplexer_2_out), .sel(\单周期硬布线控制器_1_ecall ));
  Multiplexer #(.select(1), .width(5), .disabled("Z"), .enable("false")) multiplexer_3 (
    .in0(if_id_1_irout[24:20]), .in1(5'b01010), .out(multiplexer_3_out), .sel(\单周期硬布线控制器_1_ecall ));
  assign bit_extender_1_out = {{20{if_id_1_irout[31]}}, if_id_1_irout[31:20]};  // Bit_Extender bit_extender_1
  assign bit_extender_2_out = {{20{if_id_1_irout[31]}}, {if_id_1_irout[31:25], if_id_1_irout[11:7]}};  // Bit_Extender bit_extender_2
  assign bit_extender_3_out = {{20{if_id_1_irout[31]}}, {if_id_1_irout[31], if_id_1_irout[7], if_id_1_irout[30:25], if_id_1_irout[11:8]}};  // Bit_Extender bit_extender_3
  assign bit_extender_4_out = {{12{if_id_1_irout[31]}}, {if_id_1_irout[31], if_id_1_irout[19:12], if_id_1_irout[20], if_id_1_irout[30:21]}};  // Bit_Extender bit_extender_4
  // Probe on ID_PC[11:0]
  // Probe on EX_PC[11:0]
  Multiplexer #(.select(1), .width(32), .disabled("Z"), .enable("false")) multiplexer_4 (
    .in0(bit_extender_1_out), .in1(bit_extender_2_out), .out(multiplexer_4_out), .sel(\单周期硬布线控制器_1_s_type ));
  // Probe on M_PC[11:0]
  D_Flip_Flop #(.trigger("high"), .Pre_Clr_Positions("LEGACY"), .NegatePresetClear("false"), .enable("true"), .NewFFLayout("false")) d_ff_1 (.Q(d_ff_1_q));  // open: clk, D, Qn, preset, en, reset
  // Probe on 13'hc
  // Probe on RDin
  // Probe on WB_PC[11:0]
  Comparator #(.width(13), .mode("twosComplement")) comparator_1 (
    .a(CNT_num), .b(13'hc), .eq(comparator_1_eq), .lt(comparator_1_lt));  // open: gt
  Clock #(.highDuration(1), .lowDuration(1)) clock_2 (.out(clock_2_out));
  // Probe on multiplexer_2_out
  // Probe on multiplexer_3_out
  // Probe on mem_we_1_rdout
  or or_1 (or_1_out, \单周期硬布线控制器_1_beq , \单周期硬布线控制器_1_bne , \单周期硬布线控制器_1_bltu );
  Multiplexer #(.select(1), .width(32), .disabled("Z"), .enable("false")) multiplexer_5 (
    .in0(multiplexer_4_out), .in1({bit_extender_3_out[30:0], 1'b0}), .out(multiplexer_5_out), .sel(or_1_out));
  nand nand_1 (nand_1_out, d_ff_1_q, comparator_1_eq);
  Counter #(.width(13), .max('h1fff), .ongoal("stay"), .trigger("rising"), .behavior("old")) counter_1 (
    .count(comparator_1_lt), .Q(CNT_num), .clk(clock_2_out));  // open: load, D, carry, clr, preset
  Multiplexer #(.select(1), .width(32), .disabled("Z"), .enable("false")) multiplexer_6 (
    .in0(multiplexer_5_out), .in1({bit_extender_4_out[30:0], 1'b0}), .out(multiplexer_6_out),
    .sel(\单周期硬布线控制器_1_jal ));
  assign CLK = nand_1_out ? clock_2_out : 1'bz;  // Controlled_Buffer controlled_buffer_1
  Regifile regifile_1 (
    .Din(RDin), .Clk(CLK), .R1(regifile_1_r1), .R2(regifile_1_r2), .WE(RegWrite), .W_num(mem_we_1_rdout),
    .R1_num(multiplexer_2_out), .R2_num(multiplexer_3_out));
  or or_2 (or_2_out, \单周期硬布线控制器_1_lui , \单周期硬布线控制器_1_auipc );
  Pull_Resistor #(.pull(1)) pull_resistor_1 (.node(CLK));
  Multiplexer #(.select(1), .width(32), .disabled("Z"), .enable("false")) multiplexer_7 (
    .in0(multiplexer_6_out), .in1({if_id_1_irout[31:12], {12{1'b0}}}), .out(multiplexer_7_out), .sel(or_2_out));
  // Probe on regifile_1_r1
  // Probe on regifile_1_r2
  // Probe on multiplexer_7_out
  // Probe on if_id_1_irout[11:7]
  // Probe on ID_PC
  not not_2 (not_2_out, halt);
  Counter #(.width(16), .max('hffff), .ongoal("wrap"), .trigger("rising"), .behavior("new")) counter_2 (
    .D(16'h1), .count(not_2_out), .Q(\总周期数 ), .clk(CLK), .clr(RST));  // open: load, carry, preset, down
  ID_EX id_ex_1 (
    .JALin(\单周期硬布线控制器_1_jal ), .JALRin(\单周期硬布线控制器_1_jalr ), .Beqin(\单周期硬布线控制器_1_beq ),
    .Bnein(\单周期硬布线控制器_1_bne ), .MemToRegin(\单周期硬布线控制器_1_memtoreg ), .LHin(\单周期硬布线控制器_1_lh ),
    .MemWritein(\单周期硬布线控制器_1_memwrite ), .RS1(regifile_1_r1), .BLTUin(\单周期硬布线控制器_1_bltu ),
    .AluOPin(\单周期硬布线控制器_1_alu_op ), .RS2(regifile_1_r2), .AluSrcBin(\单周期硬布线控制器_1_alu_src ),
    .RD(if_id_1_irout[11:7]), .RegWrite(\单周期硬布线控制器_1_regwrite ), .imm(multiplexer_7_out), .CLK(CLK),
    .RST(RST), .halt(halt), .JALout(id_ex_1_jalout), .JALRout(id_ex_1_jalrout), .Beqout(id_ex_1_beqout),
    .Bneout(id_ex_1_bneout), .MemToRegout(id_ex_1_memtoregout), .LHout(id_ex_1_lhout),
    .MemWriteout(id_ex_1_memwriteout), .RS1out(id_ex_1_rs1out), .BLTUout(id_ex_1_bltuout),
    .AluOPout(id_ex_1_aluopout), .RS2out(id_ex_1_rs2out), .AluSrcBout(id_ex_1_alusrcbout),
    .RDout(id_ex_1_rdout), .RegWriteout(id_ex_1_regwriteout), .Immout(id_ex_1_immout), .PC(ID_PC),
    .PCout(EX_PC), .Ecallin(\单周期硬布线控制器_1_ecall ), .Ecallout(id_ex_1_ecallout));  // open: AUIPCin, LUIin, URETin, CSRRSIin, CSRRCIin, S_typein, ALUIPCout, LUIout, URETout, CSRRSIout, CSRRCIout, S_typeout, IRin, IRout, RS1_f_in, RS1_f_out, RS2_f_in, RS2_f_out
  Multiplexer #(.select(1), .width(32), .disabled("Z"), .enable("false")) multiplexer_8 (
    .in0(id_ex_1_rs2out), .in1(id_ex_1_immout), .out(multiplexer_8_out), .sel(id_ex_1_alusrcbout));
  Adder #(.width(32)) adder_2 (.a(id_ex_1_immout), .b(EX_PC), .out(adder_2_out));  // open: cin, cout
  or or_3 (or_3_out, and_3_out, id_ex_1_jalrout, id_ex_1_jalout, and_1_out, and_2_out);
  ALU alu_1 (
    .X(id_ex_1_rs1out), .Y(multiplexer_8_out), .AluOP(id_ex_1_aluopout), .Equal(alu_1_equal),
    .Result(alu_1_result), .out_4(alu_1_out_4), .out_6(alu_1_out_6));  // open: Result_2
  and and_1 (and_1_out, not_3_out, id_ex_1_bneout);
  and and_2 (and_2_out, alu_1_equal, id_ex_1_beqout);
  not not_3 (not_3_out, alu_1_equal);
  // Probe on id_ex_1_rs2out
  // Probe on id_ex_1_rs1out
  and and_3 (and_3_out, id_ex_1_bltuout, alu_1_out_6);
  // Probe on id_ex_1_rs2out
  // Probe on id_ex_1_rdout
  // Probe on alu_1_result
  ecall_deal ecall_deal_1 (
    .ecall(id_ex_1_ecallout), .a0(id_ex_1_rs2out), .clk(CLK), .go(Go), .LedData(LedData),
    .halt(ecall_deal_1_halt), .rs1_data(id_ex_1_rs1out));
  // Probe on \总周期数 
  EX_MEM ex_mem_1 (
    .JALin(id_ex_1_jalout), .JALRin(id_ex_1_jalrout), .Beqin(id_ex_1_beqout), .Bnein(id_ex_1_bneout),
    .MemToRegin(id_ex_1_memtoregout), .LHin(id_ex_1_lhout), .ALU_Result(alu_1_result),
    .MemWritein(id_ex_1_memwriteout), .BLTUin(id_ex_1_bltuout), .AluOPin(id_ex_1_aluopout),
    .WriteData(id_ex_1_rs2out), .AluSrcBin(id_ex_1_alusrcbout), .RD(id_ex_1_rdout),
    .RegWrite(id_ex_1_regwriteout), .CLK(CLK), .RST(RST), .halt(halt), .MemToRegout(ex_mem_1_memtoregout),
    .LHout(ex_mem_1_lhout), .ALU_Resultout(ex_mem_1_alu_resultout), .MemWriteout(MemWrite),
    .WirteDataout(MDin), .RDout(ex_mem_1_rdout), .RegWriteout(ex_mem_1_regwriteout),
    .Ecallin(id_ex_1_ecallout), .PC(EX_PC), .PCout(M_PC), .Haltin(ecall_deal_1_halt),
    .Haltout(ex_mem_1_haltout));  // open: AUIPCin, LUIin, URETin, CSRRSIin, CSRRCIin, S_typein, JALout, JALRout, Beqout, ALUIPCout, Bneout, LUIout, BLTUout, AluOPout, URETout, AluSrcBout, CSRRSIout, CSRRCIout, S_typeout, Ecallout, IRin, IRout
  or or_4 (or_4_out, MemWrite, ex_mem_1_memtoregout);
  RAM #(.addrWidth(10), .dataWidth(32), .bus("separate"), .Select("high")) ram_1 (
    .addr(ex_mem_1_alu_resultout[11:2]), .din(MDin), .data(ram_1_data), .str(MemWrite), .sel(or_4_out),
    .clk(CLK), .ld(ex_mem_1_memtoregout), .clr(RST));
  // Probe on ex_mem_1_rdout
  assign bit_extender_5_out = {{16{ram_1_data[15]}}, ram_1_data[15:0]};  // Bit_Extender bit_extender_5
  assign bit_extender_6_out = {{16{ram_1_data[31]}}, ram_1_data[31:16]};  // Bit_Extender bit_extender_6
  // Probe on ex_mem_1_alu_resultout
  Multiplexer #(.select(2), .width(32), .disabled("Z"), .enable("false")) multiplexer_9 (
    .in0(bit_extender_5_out), .in1({32{1'b0}}), .in2(bit_extender_6_out), .in3({32{1'b0}}),
    .out(multiplexer_9_out), .sel(ex_mem_1_alu_resultout[1:0]));
  Multiplexer #(.select(1), .width(32), .disabled("Z"), .enable("false")) multiplexer_10 (
    .in0(ram_1_data), .in1(multiplexer_9_out), .out(multiplexer_10_out), .sel(ex_mem_1_lhout));
  // Probe on multiplexer_10_out
  MEM_WE mem_we_1 (
    .MemToRegin(ex_mem_1_memtoregout), .LHin(ex_mem_1_lhout), .MemWritein(MemWrite),
    .ALU_Result(ex_mem_1_alu_resultout), .Mem_Result(multiplexer_10_out), .RegWrite(ex_mem_1_regwriteout),
    .RD(ex_mem_1_rdout), .CLK(CLK), .RST(RST), .halt(halt), .MemToRegout(mem_we_1_memtoregout),
    .ALU_Resultout(mem_we_1_alu_resultout), .Mem_Resultout(mem_we_1_mem_resultout), .RegWriteout(RegWrite),
    .RDout(mem_we_1_rdout), .PC(M_PC), .PCout(WB_PC), .Haltin(ex_mem_1_haltout), .Haltout(halt));  // open: JALin, JALRin, Beqin, AUIPCin, Bnein, LUIin, BLTUin, AluOPin, URETin, AluSrcBin, CSRRSIin, CSRRCIin, S_typein, JALout, JALRout, Beqout, ALUIPCout, Bneout, LUIout, LHout, MemWriteout, BLTUout, AluOPout, URETout, AluSrcBout, CSRRSIout, CSRRCIout, S_typeout, Ecallin, Ecallout, IRin, IRout
  Multiplexer #(.select(1), .width(32), .disabled("Z"), .enable("false")) multiplexer_11 (
    .in0(mem_we_1_alu_resultout), .in1(mem_we_1_mem_resultout), .out(RDin), .sel(mem_we_1_memtoregout));

  // Other names for the same wires on the sheet: MEM_PC[31:0] = M_PC

  // Notes on the sheet:
  //   中断源
  //   时空图监测，可删除
  //   中断等待指示
  //   数码管输出
  //   contents of 指令存储器 (hex, n*v repeats v):
  //   413 493 913 993 46413 14e493 296913 39e993 842023 942223 1242423 1342623 a00893 493 913 993 73
  //   opcode
  //   funct
  //   rs1
  //   rs2
  //   JAL
  //   JALR
  //   ecall
  //   I:imm
  //   S:imm
  //   B:imm
  //   J:imm
  //   U:imm
  //   rd
  //   Beq
  //   Bne
  //   MemToReg
  //   MemWrite
  //   AluOP
  //   AluSrcB
  //   RegWrite
  //   S_type
  //   控制位
  //   流水调试日志用
  //   暂停节拍，不能为0
  //   戳工具置1进入计数暂停模式，ctrl+k时钟自动运行到对应节拍暂停
  //   ctrl+k关闭时钟连续运行，将控制位置零，进入单步调试模式调试
  //   用这个时钟源需要去掉电路中的其他时钟源
  //   可计数暂停的时钟源
  //   为方便自动评测，需要输出流水线各段保存的PC值，注意是PC不是PC+4，另外ID段寄存器写入信息，Mem段内存写入信息也要输出
  //   数据存储器
endmodule

module \气泡流水线  (
  output RegWrite,
  output MemWrite,
  output [31:0] IF_PC,
  output [31:0] ID_PC,
  output [31:0] EX_PC,
  output [31:0] M_PC,
  output [31:0] WB_PC,
  output [31:0] RDin,
  output [31:0] MDin,
  output [31:0] LedData
);

  wire alu_1_equal, alu_1_out_4, alu_1_out_6, and_1_out, and_2_out, and_3_out, and_5_out, and_6_out, CLK,
       clock_1_out, clock_2_out, comparator_1_eq, comparator_1_lt, d_ff_1_q, ecall_deal_1_halt, ex_mem_1_p17,
       ex_mem_1_p19, ex_mem_1_p20, ex_mem_1_p26, Go, halt, id_ex_1_aluipcout, id_ex_1_alusrcbout,
       id_ex_1_beqout, id_ex_1_bltuout, id_ex_1_bneout, id_ex_1_ecallout, id_ex_1_jalout, id_ex_1_jalrout,
       id_ex_1_lhout, id_ex_1_luiout, id_ex_1_memtoregout, id_ex_1_memwriteout, id_ex_1_regwriteout, IR1,
       IR2, IR3, mem_we_1_haltout, mem_we_1_memtoregout, nand_1_out, not_1_out, not_2_out, not_3_out,
       not_4_out, not_5_out, or_1_out, or_2_out, or_3_out, or_4_out, or_5_out, or_6_out, RST, W1, W2, W3,
       \单周期硬布线控制器_1_alu_src , \单周期硬布线控制器_1_auipc , \单周期硬布线控制器_1_beq , \单周期硬布线控制器_1_bltu , \单周期硬布线控制器_1_bne ,
       \单周期硬布线控制器_1_ecall , \单周期硬布线控制器_1_jal , \单周期硬布线控制器_1_jalr , \单周期硬布线控制器_1_lh , \单周期硬布线控制器_1_lui ,
       \单周期硬布线控制器_1_memtoreg , \单周期硬布线控制器_1_memwrite , \单周期硬布线控制器_1_regwrite , \单周期硬布线控制器_1_s_type ,
       \相关逻辑处理_气泡_1_id_ex_clr , \相关逻辑处理_气泡_1_if_id_clr , \相关逻辑处理_气泡_1_if_id_en , \相关逻辑处理_气泡_1_stall ;
  wire [3:0] id_ex_1_aluopout, \单周期硬布线控制器_1_alu_op ;
  wire [4:0] ex_mem_1_p23, id_ex_1_rdout, mem_we_1_rdout, multiplexer_2_out, multiplexer_3_out,
       multiplexer_5_out;
  wire [12:0] CNT_num;
  wire [15:0] \LoadUse次数 , \总周期数 , \插入气泡数 , \无条件分支数 , \条件分支成功数 ;
  wire [31:0] adder_1_out, adder_2_out, adder_3_out, adder_4_out, adder_5_out, alu_1_result, and_4_out,
       bit_extender_1_out, bit_extender_2_out, bit_extender_3_out, bit_extender_4_out, bit_extender_5_out,
       bit_extender_6_out, EX_IR, ex_mem_1_p21, id_ex_1_immout, id_ex_1_rs1out, id_ex_1_rs2out, ID_IR, IF_IR,
       MEM_IR, mem_we_1_alu_resultout, mem_we_1_mem_resultout, multiplexer_1_out, multiplexer_4_out,
       multiplexer_6_out, multiplexer_7_out, multiplexer_8_out, multiplexer_9_out, multiplexer_10_out,
       multiplexer_11_out, multiplexer_12_out, multiplexer_13_out, multiplexer_14_out, multiplexer_15_out,
       ram_1_data, regifile_1_r1, regifile_1_r2, WB_IR;

  Button \u_总复位  (.out(RST));
  Button _1 (.out(IR1));
  Button _2 (.out(IR2));
  Button _3 (.out(IR3));
  // Probe on \总周期数 
  // Probe on \总周期数 
  Button \u_继续运行  (.out(Go));
  LED #(.active("true")) led_1 (.in(W1));
  LED #(.active("true")) led_2 (.in(W2));
  LED #(.active("true")) led_3 (.in(W3));
  Multiplexer #(.select(1), .width(32), .disabled("Z"), .enable("false")) multiplexer_1 (
    .in0(adder_1_out), .in1(multiplexer_11_out), .out(multiplexer_1_out), .sel(or_4_out));
  not not_1 (not_1_out, halt);
  Hex_Digit_Display hex_digit_display_1 (.value(LedData[31:28]));  // open: dp
  // Probe on IF_PC[19:0]
  // RiscV_Probe riscv_probe_1: pin names not known; wires that end beside it: IF_IR
  // Probe on multiplexer_1_out
  Register #(.width(32), .trigger("rising"), .Select("low")) PC (
    .D(multiplexer_1_out), .en(and_1_out), .Q(IF_PC), .clk(CLK), .clr(RST));
  and and_1 (and_1_out, not_2_out, not_1_out);
  Hex_Digit_Display hex_digit_display_2 (.value(LedData[23:20]));  // open: dp
  Hex_Digit_Display hex_digit_display_3 (.value(LedData[27:24]));  // open: dp
  // Probe on ID_PC[19:0]
  // RiscV_Probe riscv_probe_2: pin names not known; wires that end beside it: ID_IR
  // Probe on IF_PC
  Hex_Digit_Display hex_digit_display_4 (.value(LedData[19:16]));  // open: dp
  Hex_Digit_Display hex_digit_display_5 (.value(LedData[15:12]));  // open: dp
  Adder #(.width(32)) adder_1 (.a(IF_PC), .b(32'h4), .out(adder_1_out));  // open: cin, cout
  Hex_Digit_Display hex_digit_display_6 (.value(LedData[7:4]));  // open: dp
  Hex_Digit_Display hex_digit_display_7 (.value(LedData[11:8]));  // open: dp
  Clock #(.highDuration(1), .lowDuration(1)) clock_1 (.out(clock_1_out));
  // Probe on EX_PC[19:0]
  // RiscV_Probe riscv_probe_3: pin names not known; wires that end beside it: clock_1_out, EX_IR, CLK
  not not_2 (not_2_out, \相关逻辑处理_气泡_1_stall );
  // RiscV_Probe riscv_probe_4: pin names not known; wires that end beside it: IF_IR
  ROM #(.addrWidth(10), .dataWidth(32), .Select("high")) \u_指令存储器  (.addr(IF_PC[11:2]), .data(IF_IR));
  Hex_Digit_Display hex_digit_display_8 (.value(LedData[3:0]));  // open: dp
  // Probe on \总周期数 
  // Probe on M_PC[19:0]
  // RiscV_Probe riscv_probe_5: pin names not known; wires that end beside it: MEM_IR
  IF_ID if_id_1 (
    .IRin(IF_IR), .PCin(IF_PC), .CLK(CLK), .RST(\相关逻辑处理_气泡_1_if_id_clr ), .halt(halt), .IRout(ID_IR),
    .PCout(ID_PC), .en(\相关逻辑处理_气泡_1_if_id_en ));
  // Probe on \总周期数 
  // Probe on \无条件分支数 
  // Probe on \条件分支成功数 
  // Probe on \插入气泡数 
  // Probe on \LoadUse次数 
  // Probe on IF_PC[11:0]
  // Probe on WB_PC[19:0]
  // RiscV_Probe riscv_probe_6: pin names not known; wires that end beside it: WB_IR
  \单周期硬布线控制器  \u_单周期硬布线控制器_1  (
    .Funct({ID_IR[30], ID_IR[25], ID_IR[14:12]}), .OP(ID_IR[6:2]), .ALU_OP(\单周期硬布线控制器_1_alu_op ),
    .MemToReg(\单周期硬布线控制器_1_memtoreg ), .MemWrite(\单周期硬布线控制器_1_memwrite ), .ALU_SRC(\单周期硬布线控制器_1_alu_src ),
    .RegWrite(\单周期硬布线控制器_1_regwrite ), .ecall(\单周期硬布线控制器_1_ecall ), .S_type(\单周期硬布线控制器_1_s_type ),
    .Jalr(\单周期硬布线控制器_1_jalr ), .Beq(\单周期硬布线控制器_1_beq ), .JAL(\单周期硬布线控制器_1_jal ), .Bne(\单周期硬布线控制器_1_bne ),
    .AUIPC(\单周期硬布线控制器_1_auipc ), .BLTU(\单周期硬布线控制器_1_bltu ), .LH(\单周期硬布线控制器_1_lh ), .LUI(\单周期硬布线控制器_1_lui ));  // open: CSRRSI, CSRRCI
  Multiplexer #(.select(1), .width(5), .disabled("Z"), .enable("false")) multiplexer_2 (
    .in0(ID_IR[19:15]), .in1(5'b10001), .out(multiplexer_2_out), .sel(\单周期硬布线控制器_1_ecall ));
  Multiplexer #(.select(1), .width(5), .disabled("Z"), .enable("false")) multiplexer_3 (
    .in0(ID_IR[24:20]), .in1(5'b01010), .out(multiplexer_3_out), .sel(\单周期硬布线控制器_1_ecall ));
  assign bit_extender_1_out = {{20{ID_IR[31]}}, ID_IR[31:20]};  // Bit_Extender bit_extender_1
  assign bit_extender_2_out = {{20{ID_IR[31]}}, {ID_IR[31:25], ID_IR[11:7]}};  // Bit_Extender bit_extender_2
  assign bit_extender_3_out = {{20{ID_IR[31]}}, {ID_IR[31], ID_IR[7], ID_IR[30:25], ID_IR[11:8]}};  // Bit_Extender bit_extender_3
  assign bit_extender_4_out = {{12{ID_IR[31]}}, {ID_IR[31], ID_IR[19:12], ID_IR[20], ID_IR[30:21]}};  // Bit_Extender bit_extender_4
  // Probe on ID_PC[11:0]
  // Probe on EX_PC[11:0]
  Multiplexer #(.select(1), .width(32), .disabled("Z"), .enable("false")) multiplexer_4 (
    .in0(bit_extender_1_out), .in1(bit_extender_2_out), .out(multiplexer_4_out), .sel(\单周期硬布线控制器_1_s_type ));
  // Probe on M_PC[11:0]
  D_Flip_Flop #(.trigger("high"), .Pre_Clr_Positions("LEGACY"), .NegatePresetClear("false"), .enable("true"), .NewFFLayout("false")) d_ff_1 (.Q(d_ff_1_q));  // open: clk, D, Qn, preset, en, reset
  // Probe on 13'hc
  // Probe on multiplexer_2_out
  // Probe on multiplexer_5_out
  Multiplexer #(.select(1), .width(5), .disabled("Z"), .enable("false")) multiplexer_5 (
    .in0(multiplexer_3_out), .in1({5{1'b0}}), .out(multiplexer_5_out), .sel(or_1_out));
  // Probe on RDin
  // Probe on WB_PC[11:0]
  Comparator #(.width(13), .mode("twosComplement")) comparator_1 (
    .a(CNT_num), .b(13'hc), .eq(comparator_1_eq), .lt(comparator_1_lt));  // open: gt
  Clock #(.highDuration(1), .lowDuration(1)) clock_2 (.out(clock_2_out));
  or or_1 (or_1_out, \单周期硬布线控制器_1_lui , \单周期硬布线控制器_1_auipc , \单周期硬布线控制器_1_jalr , \单周期硬布线控制器_1_jal , \单周期硬布线控制器_1_alu_src );
  // Probe on multiplexer_2_out
  // Probe on multiplexer_3_out
  // Probe on mem_we_1_rdout
  or or_2 (or_2_out, \单周期硬布线控制器_1_beq , \单周期硬布线控制器_1_bne , \单周期硬布线控制器_1_bltu );
  Multiplexer #(.select(1), .width(32), .disabled("Z"), .enable("false")) multiplexer_6 (
    .in0(multiplexer_4_out), .in1({bit_extender_3_out[30:0], 1'b0}), .out(multiplexer_6_out), .sel(or_2_out));
  nand nand_1 (nand_1_out, d_ff_1_q, comparator_1_eq);
  Counter #(.width(13), .max('h1fff), .ongoal("stay"), .trigger("rising"), .behavior("old")) counter_1 (
    .count(comparator_1_lt), .Q(CNT_num), .clk(clock_2_out));  // open: load, D, carry, clr, preset
  Multiplexer #(.select(1), .width(32), .disabled("Z"), .enable("false")) multiplexer_7 (
    .in0(multiplexer_6_out), .in1({bit_extender_4_out[30:0], 1'b0}), .out(multiplexer_7_out),
    .sel(\单周期硬布线控制器_1_jal ));
  assign CLK = nand_1_out ? clock_2_out : 1'bz;  // Controlled_Buffer controlled_buffer_1
  Regifile regifile_1 (
    .Din(RDin), .Clk(CLK), .R1(regifile_1_r1), .R2(regifile_1_r2), .WE(RegWrite), .W_num(mem_we_1_rdout),
    .R1_num(multiplexer_2_out), .R2_num(multiplexer_3_out));
  or or_3 (or_3_out, \单周期硬布线控制器_1_lui , \单周期硬布线控制器_1_auipc );
  Pull_Resistor #(.pull(1)) pull_resistor_1 (.node(CLK));
  Multiplexer #(.select(1), .width(32), .disabled("Z"), .enable("false")) multiplexer_8 (
    .in0(multiplexer_7_out), .in1({ID_IR[31:12], {12{1'b0}}}), .out(multiplexer_8_out), .sel(or_3_out));
  // Probe on regifile_1_r1
  // Probe on regifile_1_r2
  // Probe on multiplexer_8_out
  // Probe on ID_IR[11:7]
  // Probe on ID_PC
  // RiscV_Probe riscv_probe_7: pin names not known
  // Probe on \总周期数 
  not not_3 (not_3_out, halt);
  Counter #(.width(16), .max('hffff), .ongoal("wrap"), .trigger("rising"), .behavior("new")) counter_2 (
    .D(16'h1), .count(not_3_out), .Q(\总周期数 ), .clk(CLK), .clr(RST));  // open: load, carry, preset, down
  ID_EX id_ex_1 (
    .JALin(\单周期硬布线控制器_1_jal ), .JALRin(\单周期硬布线控制器_1_jalr ), .Beqin(\单周期硬布线控制器_1_beq ),
    .AUIPCin(\单周期硬布线控制器_1_auipc ), .Bnein(\单周期硬布线控制器_1_bne ), .LUIin(\单周期硬布线控制器_1_lui ),
    .MemToRegin(\单周期硬布线控制器_1_memtoreg ), .LHin(\单周期硬布线控制器_1_lh ), .MemWritein(\单周期硬布线控制器_1_memwrite ),
    .RS1(regifile_1_r1), .BLTUin(\单周期硬布线控制器_1_bltu ), .AluOPin(\单周期硬布线控制器_1_alu_op ), .RS2(regifile_1_r2),
    .AluSrcBin(\单周期硬布线控制器_1_alu_src ), .RD(ID_IR[11:7]), .RegWrite(\单周期硬布线控制器_1_regwrite ),
    .imm(multiplexer_8_out), .CLK(CLK), .RST(\相关逻辑处理_气泡_1_id_ex_clr ), .halt(halt), .JALout(id_ex_1_jalout),
    .JALRout(id_ex_1_jalrout), .Beqout(id_ex_1_beqout), .ALUIPCout(id_ex_1_aluipcout),
    .Bneout(id_ex_1_bneout), .LUIout(id_ex_1_luiout), .MemToRegout(id_ex_1_memtoregout),
    .LHout(id_ex_1_lhout), .MemWriteout(id_ex_1_memwriteout), .RS1out(id_ex_1_rs1out),
    .BLTUout(id_ex_1_bltuout), .AluOPout(id_ex_1_aluopout), .RS2out(id_ex_1_rs2out),
    .AluSrcBout(id_ex_1_alusrcbout), .RDout(id_ex_1_rdout), .RegWriteout(id_ex_1_regwriteout),
    .Immout(id_ex_1_immout), .PC(ID_PC), .PCout(EX_PC), .Ecallin(\单周期硬布线控制器_1_ecall ),
    .Ecallout(id_ex_1_ecallout), .IRin(ID_IR), .IRout(EX_IR));  // open: URETin, CSRRSIin, CSRRCIin, S_typein, URETout, CSRRSIout, CSRRCIout, S_typeout, RS1_f_in, RS1_f_out, RS2_f_in, RS2_f_out
  Multiplexer #(.select(1), .width(32), .disabled("Z"), .enable("false")) multiplexer_9 (
    .in0(id_ex_1_rs2out), .in1(id_ex_1_immout), .out(multiplexer_9_out), .sel(id_ex_1_alusrcbout));
  or or_4 (or_4_out, and_5_out, id_ex_1_jalrout, id_ex_1_jalout, and_3_out, and_2_out);
  ALU alu_1 (
    .X(id_ex_1_rs1out), .Y(multiplexer_9_out), .AluOP(id_ex_1_aluopout), .Equal(alu_1_equal),
    .Result(alu_1_result), .out_4(alu_1_out_4), .out_6(alu_1_out_6));  // open: Result_2
  // Probe on id_ex_1_rs2out
  // Probe on id_ex_1_rs1out
  Adder #(.width(32)) adder_2 (.a(EX_PC), .b(id_ex_1_immout), .out(adder_2_out));  // open: cin, cout
  Adder #(.width(32)) adder_3 (.a(32'h4), .b(EX_PC), .out(adder_3_out));  // open: cin, cout
  Adder #(.width(32)) adder_4 (.a(id_ex_1_immout), .b(EX_PC), .out(adder_4_out));  // open: cin, cout
  Adder #(.width(32)) adder_5 (.a(id_ex_1_rs1out), .b(id_ex_1_immout), .out(adder_5_out));  // open: cin, cout
  and and_2 (and_2_out, alu_1_equal, id_ex_1_beqout);
  and and_3 (and_3_out, not_4_out, id_ex_1_bneout);
  not not_4 (not_4_out, alu_1_equal);
  or or_5 (or_5_out, id_ex_1_jalout, id_ex_1_jalrout);
  Multiplexer #(.select(1), .width(32), .disabled("Z"), .enable("false")) multiplexer_10 (
    .in0(alu_1_result), .in1(adder_3_out), .out(multiplexer_10_out), .sel(or_5_out));
  Multiplexer #(.select(1), .width(32), .disabled("Z"), .enable("false")) multiplexer_11 (
    .in0(adder_4_out), .in1(and_4_out), .out(multiplexer_11_out), .sel(id_ex_1_jalrout));
  assign and_4_out = adder_5_out & 32'hfffffffe;  // AND_Gate and_4, 32 bits wide
  Multiplexer #(.select(1), .width(32), .disabled("Z"), .enable("false")) multiplexer_12 (
    .in0(multiplexer_10_out), .in1(adder_2_out), .out(multiplexer_12_out), .sel(id_ex_1_aluipcout));
  and and_5 (and_5_out, id_ex_1_bltuout, alu_1_out_6);
  Multiplexer #(.select(1), .width(32), .disabled("Z"), .enable("false")) multiplexer_13 (
    .in0(multiplexer_12_out), .in1(id_ex_1_immout), .out(multiplexer_13_out), .sel(id_ex_1_luiout));
  // Probe on id_ex_1_rdout
  ecall_deal ecall_deal_1 (
    .ecall(id_ex_1_ecallout), .a0(id_ex_1_rs2out), .clk(CLK), .go(1'b0), .LedData(LedData),
    .halt(ecall_deal_1_halt), .rs1_data(id_ex_1_rs1out));
  // Probe on multiplexer_13_out
  // Probe on id_ex_1_rdout
  // RiscV_Probe riscv_probe_8: pin names not known; wires that end beside it: multiplexer_13_out
  // EX_MEM ex_mem_1: pin names not known; wires that end beside it: alu_1_equal, alu_1_out_4, alu_1_out_6, id_ex_1_memtoregout, id_ex_1_memwriteout, id_ex_1_regwriteout, id_ex_1_lhout, multiplexer_13_out, id_ex_1_rs2out, id_ex_1_rdout, EX_PC, EX_IR, ecall_deal_1_halt, RST, CLK, halt, ex_mem_1_p17, MemWrite, ex_mem_1_p19, ex_mem_1_p20, ex_mem_1_p21, MDin, ex_mem_1_p23, M_PC, MEM_IR, ex_mem_1_p26
  \相关逻辑处理_气泡  \u_相关逻辑处理_气泡_1  (
    .ID_rs1(multiplexer_2_out), .ID_rs2(multiplexer_5_out), .EX_rd(id_ex_1_rdout), .MEM_rd(ex_mem_1_p23),
    .EX_rw(id_ex_1_regwriteout), .MEM_rw(ex_mem_1_p19), .branch(or_4_out), .stall(\相关逻辑处理_气泡_1_stall ),
    .IF_ID_en(\相关逻辑处理_气泡_1_if_id_en ), .IF_ID_clr(\相关逻辑处理_气泡_1_if_id_clr ),
    .ID_EX_clr(\相关逻辑处理_气泡_1_id_ex_clr ));
  // Probe on ex_mem_1_p23
  or or_6 (or_6_out, MemWrite, ex_mem_1_p17);
  RAM #(.addrWidth(10), .dataWidth(32), .bus("separate"), .Select("high")) ram_1 (
    .addr(ex_mem_1_p21[11:2]), .din(MDin), .data(ram_1_data), .str(MemWrite), .sel(or_6_out), .clk(CLK),
    .ld(ex_mem_1_p17), .clr(RST));
  // Probe on ex_mem_1_p23
  assign bit_extender_5_out = {{16{ram_1_data[15]}}, ram_1_data[15:0]};  // Bit_Extender bit_extender_5
  assign bit_extender_6_out = {{16{ram_1_data[31]}}, ram_1_data[31:16]};  // Bit_Extender bit_extender_6
  // Probe on ex_mem_1_p21
  Multiplexer #(.select(2), .width(32), .disabled("Z"), .enable("false")) multiplexer_14 (
    .in0(bit_extender_5_out), .in1({32{1'b0}}), .in2(bit_extender_6_out), .in3({32{1'b0}}),
    .out(multiplexer_14_out), .sel(ex_mem_1_p21[1:0]));
  // RiscV_Probe riscv_probe_9: pin names not known; wires that end beside it: ex_mem_1_p26
  // Probe on multiplexer_15_out
  Multiplexer #(.select(1), .width(32), .disabled("Z"), .enable("false")) multiplexer_15 (
    .in0(ram_1_data), .in1(multiplexer_14_out), .out(multiplexer_15_out), .sel(ex_mem_1_p20));
  MEM_WE mem_we_1 (
    .MemToRegin(ex_mem_1_p17), .ALU_Result(ex_mem_1_p21), .Mem_Result(multiplexer_15_out),
    .RegWrite(ex_mem_1_p19), .RD(ex_mem_1_p23), .CLK(CLK), .RST(RST), .halt(halt),
    .MemToRegout(mem_we_1_memtoregout), .ALU_Resultout(mem_we_1_alu_resultout),
    .Mem_Resultout(mem_we_1_mem_resultout), .RegWriteout(RegWrite), .RDout(mem_we_1_rdout), .PC(M_PC),
    .PCout(WB_PC), .Haltin(ex_mem_1_p26), .Haltout(mem_we_1_haltout), .IRin(MEM_IR), .IRout(WB_IR));  // open: JALin, JALRin, Beqin, AUIPCin, Bnein, LUIin, LHin, MemWritein, BLTUin, AluOPin, URETin, AluSrcBin, CSRRSIin, CSRRCIin, S_typein, JALout, JALRout, Beqout, ALUIPCout, Bneout, LUIout, LHout, MemWriteout, BLTUout, AluOPout, URETout, AluSrcBout, CSRRSIout, CSRRCIout, S_typeout, Ecallin, Ecallout
  Multiplexer #(.select(1), .width(32), .disabled("Z"), .enable("false")) multiplexer_16 (
    .in0(mem_we_1_alu_resultout), .in1(mem_we_1_mem_resultout), .out(RDin), .sel(mem_we_1_memtoregout));
  not not_5 (not_5_out, Go);
  and and_6 (and_6_out, mem_we_1_haltout, not_5_out);
  D_Flip_Flop #(.trigger("falling"), .Pre_Clr_Positions("ABOVE_BELOW"), .NegatePresetClear("false"), .enable("false"), .NewFFLayout("true")) d_ff_2 (
    .clk(CLK), .D(and_6_out), .Q(halt));  // open: Qn, preset, reset

  // Other names for the same wires on the sheet: MEM_PC[31:0] = M_PC

  // Notes on the sheet:
  //   中断源
  //   时空图监测，可删除
  //   中断等待指示
  //   数码管输出
  //   contents of 指令存储器 (hex, n*v repeats v):
  //   13 430497 900533 2200893 73 430497 900533 2200893 73 430497 900533 2200893 73 430497 900533 2200893
  //   73 430497 900533 2200893 73 430497 900533 2200893 73 430497 900533 2200893 73 430497 900533 2200893
  //   73 a00893 73
  //   opcode
  //   funct
  //   rs1
  //   rs2
  //   JAL
  //   JALR
  //   AUIPC
  //   LUI
  //   ecall
  //   I:imm
  //   S:imm
  //   B:imm
  //   J:imm
  //   U:imm
  //   rd
  //   Beq
  //   Bne
  //   MemToReg
  //   MemWrite
  //   AluOP
  //   AluSrcB
  //   RegWrite
  //   S_type
  //   控制位
  //   流水调试日志用
  //   暂停节拍，不能为0
  //   戳工具置1进入计数暂停模式，ctrl+k时钟自动运行到对应节拍暂停
  //   ctrl+k关闭时钟连续运行，将控制位置零，进入单步调试模式调试
  //   可计数暂停的时钟源
  //   为方便自动评测，需要输出流水线各段保存的PC值，注意是PC不是PC+4，另外ID段寄存器写入信息，Mem段内存写入信息也要输出
  //   数据存储器
endmodule
module \重定向流水线  (
  output RegWrite,
  output MemWrite,
  output [31:0] IF_PC,
  output [31:0] ID_PC,
  output [31:0] EX_PC,
  output [31:0] M_PC,
  output [31:0] WB_PC,
  output [31:0] RDin,
  output [31:0] MDin,
  output [31:0] LedData
);

  wire and_1_out, and_2_out, and_3_out, and_4_out, and_6_out, and_7_out, and_8_out, BranchTaken, CLK,
       clock_1_out, clock_2_out, comparator_1_eq, comparator_1_lt, d_ff_1_q, ecall_deal_1_halt, EX_AUIPC,
       EX_Beq, EX_Bltu, EX_Bne, EX_ecall, EX_eq, EX_JAL, EX_JALR, EX_less, EX_LUI, ex_mem_1_p16,
       ex_mem_1_p18, ex_mem_1_p19, ex_mem_1_p25, EX_SrcB, Go, halt, id_ex_1_lhout, id_ex_1_memtoregout,
       id_ex_1_memwriteout, id_ex_1_regwriteout, IR1, IR2, IR3, mem_we_1_haltout, mem_we_1_memtoregout,
       nand_1_out, not_1_out, not_2_out, not_3_out, not_4_out, not_5_out, not_6_out, or_1_out, or_2_out,
       or_3_out, or_5_out, or_6_out, or_7_out, or_8_out, RST, W1, W2, W3, \单周期硬布线控制器_1_alu_src ,
       \单周期硬布线控制器_1_auipc , \单周期硬布线控制器_1_beq , \单周期硬布线控制器_1_bltu , \单周期硬布线控制器_1_bne , \单周期硬布线控制器_1_ecall ,
       \单周期硬布线控制器_1_jal , \单周期硬布线控制器_1_jalr , \单周期硬布线控制器_1_lh , \单周期硬布线控制器_1_lui , \单周期硬布线控制器_1_memtoreg ,
       \单周期硬布线控制器_1_memwrite , \单周期硬布线控制器_1_regwrite , \单周期硬布线控制器_1_s_type , \相关逻辑处理_重定向_1_id_ex_clr ,
       \相关逻辑处理_重定向_1_if_id_clr , \相关逻辑处理_重定向_1_loaduse , \相关逻辑处理_重定向_1_stall ;
  wire [1:0] id_ex_1_rs1_f_out, id_ex_1_rs2_f_out, \相关逻辑处理_重定向_1_rs1_forward , \相关逻辑处理_重定向_1_rs2_forward ;
  wire [3:0] EX_AluOP, \单周期硬布线控制器_1_alu_op ;
  wire [4:0] ex_mem_1_p22, id_ex_1_rdout, mem_we_1_rdout, multiplexer_2_out, multiplexer_3_out,
       multiplexer_5_out;
  wire [12:0] CNT_num;
  wire [15:0] \LoadUse次数 , \总周期数 , \无条件分支数 , \条件分支成功数 ;
  wire [31:0] adder_1_out, adder_2_out, adder_3_out, adder_4_out, adder_5_out, and_5_out, bit_extender_1_out,
       bit_extender_2_out, bit_extender_3_out, bit_extender_4_out, bit_extender_5_out, bit_extender_6_out,
       EX_ALUData, EX_IR, id_ex_1_immout, id_ex_1_rs1out, id_ex_1_rs2out, ID_IR, IF_IR, MEM_ALUData, MEM_IR,
       mem_we_1_alu_resultout, mem_we_1_mem_resultout, multiplexer_1_out, multiplexer_4_out,
       multiplexer_6_out, multiplexer_7_out, multiplexer_8_out, multiplexer_9_out, multiplexer_10_out,
       multiplexer_11_out, multiplexer_12_out, multiplexer_13_out, multiplexer_14_out, multiplexer_15_out,
       multiplexer_16_out, multiplexer_17_out, ram_1_data, regifile_1_r1, regifile_1_r2, WB_IR;

  Button \u_总复位  (.out(RST));
  Button _1 (.out(IR1));
  Button _2 (.out(IR2));
  Button _3 (.out(IR3));
  // Probe on \总周期数 
  // Probe on \总周期数 
  Button \u_继续运行  (.out(Go));
  LED #(.active("true")) led_1 (.in(W1));
  LED #(.active("true")) led_2 (.in(W2));
  LED #(.active("true")) led_3 (.in(W3));
  Multiplexer #(.select(1), .width(32), .disabled("Z"), .enable("false")) multiplexer_1 (
    .in0(adder_1_out), .in1(multiplexer_12_out), .out(multiplexer_1_out), .sel(BranchTaken));
  not not_1 (not_1_out, halt);
  Hex_Digit_Display hex_digit_display_1 (.value(LedData[31:28]));  // open: dp
  // Probe on IF_PC[19:0]
  // RiscV_Probe riscv_probe_1: pin names not known; wires that end beside it: IF_IR
  // Probe on multiplexer_1_out
  Register #(.width(32), .trigger("rising"), .Select("low")) PC (
    .D(multiplexer_1_out), .en(and_1_out), .Q(IF_PC), .clk(CLK), .clr(RST));
  and and_1 (and_1_out, not_2_out, not_1_out);
  Hex_Digit_Display hex_digit_display_2 (.value(LedData[23:20]));  // open: dp
  Hex_Digit_Display hex_digit_display_3 (.value(LedData[27:24]));  // open: dp
  // Probe on ID_PC[19:0]
  // RiscV_Probe riscv_probe_2: pin names not known; wires that end beside it: ID_IR
  // Probe on IF_PC
  Hex_Digit_Display hex_digit_display_4 (.value(LedData[15:12]));  // open: dp
  Hex_Digit_Display hex_digit_display_5 (.value(LedData[19:16]));  // open: dp
  Adder #(.width(32)) adder_1 (.a(IF_PC), .b(32'h4), .out(adder_1_out));  // open: cin, cout
  Hex_Digit_Display hex_digit_display_6 (.value(LedData[7:4]));  // open: dp
  Hex_Digit_Display hex_digit_display_7 (.value(LedData[11:8]));  // open: dp
  Clock #(.highDuration(1), .lowDuration(1)) clock_1 (.out(clock_1_out));
  // Probe on EX_PC[19:0]
  // RiscV_Probe riscv_probe_3: pin names not known; wires that end beside it: clock_1_out, EX_IR, CLK
  not not_2 (not_2_out, \相关逻辑处理_重定向_1_stall );
  // RiscV_Probe riscv_probe_4: pin names not known; wires that end beside it: IF_IR
  ROM #(.addrWidth(10), .dataWidth(32), .Select("high")) \u_指令存储器  (.addr(IF_PC[11:2]), .data(IF_IR));
  Hex_Digit_Display hex_digit_display_8 (.value(LedData[3:0]));  // open: dp
  // Probe on \总周期数 
  // Probe on M_PC[19:0]
  // RiscV_Probe riscv_probe_5: pin names not known; wires that end beside it: MEM_IR
  IF_ID if_id_1 (
    .IRin(IF_IR), .PCin(IF_PC), .CLK(CLK), .RST(\相关逻辑处理_重定向_1_if_id_clr ), .halt(halt), .IRout(ID_IR),
    .PCout(ID_PC), .en(not_2_out));
  // Probe on \总周期数 
  // Probe on \无条件分支数 
  // Probe on \条件分支成功数 
  // Probe on \LoadUse次数 
  // Probe on \LoadUse次数 
  // Probe on IF_PC[11:0]
  // Probe on WB_PC[19:0]
  // RiscV_Probe riscv_probe_6: pin names not known; wires that end beside it: WB_IR
  \单周期硬布线控制器  \u_单周期硬布线控制器_1  (
    .Funct({ID_IR[30], ID_IR[25], ID_IR[14:12]}), .OP(ID_IR[6:2]), .ALU_OP(\单周期硬布线控制器_1_alu_op ),
    .MemToReg(\单周期硬布线控制器_1_memtoreg ), .MemWrite(\单周期硬布线控制器_1_memwrite ), .ALU_SRC(\单周期硬布线控制器_1_alu_src ),
    .RegWrite(\单周期硬布线控制器_1_regwrite ), .ecall(\单周期硬布线控制器_1_ecall ), .S_type(\单周期硬布线控制器_1_s_type ),
    .Jalr(\单周期硬布线控制器_1_jalr ), .Beq(\单周期硬布线控制器_1_beq ), .JAL(\单周期硬布线控制器_1_jal ), .Bne(\单周期硬布线控制器_1_bne ),
    .AUIPC(\单周期硬布线控制器_1_auipc ), .BLTU(\单周期硬布线控制器_1_bltu ), .LH(\单周期硬布线控制器_1_lh ), .LUI(\单周期硬布线控制器_1_lui ));  // open: CSRRSI, CSRRCI
  Multiplexer #(.select(1), .width(5), .disabled("Z"), .enable("false")) multiplexer_2 (
    .in0(ID_IR[19:15]), .in1(5'b10001), .out(multiplexer_2_out), .sel(\单周期硬布线控制器_1_ecall ));
  Multiplexer #(.select(1), .width(5), .disabled("Z"), .enable("false")) multiplexer_3 (
    .in0(ID_IR[24:20]), .in1(5'b01010), .out(multiplexer_3_out), .sel(\单周期硬布线控制器_1_ecall ));
  assign bit_extender_1_out = {{20{ID_IR[31]}}, ID_IR[31:20]};  // Bit_Extender bit_extender_1
  assign bit_extender_2_out = {{20{ID_IR[31]}}, {ID_IR[31:25], ID_IR[11:7]}};  // Bit_Extender bit_extender_2
  assign bit_extender_3_out = {{20{ID_IR[31]}}, {ID_IR[31], ID_IR[7], ID_IR[30:25], ID_IR[11:8]}};  // Bit_Extender bit_extender_3
  assign bit_extender_4_out = {{12{ID_IR[31]}}, {ID_IR[31], ID_IR[19:12], ID_IR[20], ID_IR[30:21]}};  // Bit_Extender bit_extender_4
  // Probe on ID_PC[11:0]
  // Probe on EX_PC[11:0]
  Multiplexer #(.select(1), .width(32), .disabled("Z"), .enable("false")) multiplexer_4 (
    .in0(bit_extender_1_out), .in1(bit_extender_2_out), .out(multiplexer_4_out), .sel(\单周期硬布线控制器_1_s_type ));
  // Probe on M_PC[11:0]
  D_Flip_Flop #(.trigger("high"), .Pre_Clr_Positions("LEGACY"), .NegatePresetClear("false"), .enable("true"), .NewFFLayout("false")) d_ff_1 (.Q(d_ff_1_q));  // open: clk, D, Qn, preset, en, reset
  // Probe on 13'h340
  // Probe on multiplexer_5_out
  // Probe on multiplexer_2_out
  Multiplexer #(.select(1), .width(5), .disabled("Z"), .enable("false")) multiplexer_5 (
    .in0(multiplexer_3_out), .in1({5{1'b0}}), .out(multiplexer_5_out), .sel(and_2_out));
  // Probe on RDin
  // Probe on WB_PC[11:0]
  Comparator #(.width(13), .mode("twosComplement")) comparator_1 (
    .a(CNT_num), .b(13'h340), .eq(comparator_1_eq), .lt(comparator_1_lt));  // open: gt
  Clock #(.highDuration(1), .lowDuration(1)) clock_2 (.out(clock_2_out));
  and and_2 (and_2_out, not_3_out, or_1_out);
  or or_1 (or_1_out, \单周期硬布线控制器_1_lui , \单周期硬布线控制器_1_auipc , \单周期硬布线控制器_1_jalr , \单周期硬布线控制器_1_jal , \单周期硬布线控制器_1_alu_src );
  // Probe on multiplexer_2_out
  // Probe on multiplexer_3_out
  // Probe on mem_we_1_rdout
  or or_2 (or_2_out, \单周期硬布线控制器_1_beq , \单周期硬布线控制器_1_bne , \单周期硬布线控制器_1_bltu );
  Multiplexer #(.select(1), .width(32), .disabled("Z"), .enable("false")) multiplexer_6 (
    .in0(multiplexer_4_out), .in1({bit_extender_3_out[30:0], 1'b0}), .out(multiplexer_6_out), .sel(or_2_out));
  nand nand_1 (nand_1_out, d_ff_1_q, comparator_1_eq);
  Counter #(.width(13), .max('h1fff), .ongoal("stay"), .trigger("rising"), .behavior("old")) counter_1 (
    .count(comparator_1_lt), .Q(CNT_num), .clk(clock_2_out));  // open: load, D, carry, clr, preset
  not not_3 (not_3_out, \单周期硬布线控制器_1_s_type );
  Multiplexer #(.select(1), .width(32), .disabled("Z"), .enable("false")) multiplexer_7 (
    .in0(multiplexer_6_out), .in1({bit_extender_4_out[30:0], 1'b0}), .out(multiplexer_7_out),
    .sel(\单周期硬布线控制器_1_jal ));
  assign CLK = nand_1_out ? clock_2_out : 1'bz;  // Controlled_Buffer controlled_buffer_1
  Regifile regifile_1 (
    .Din(RDin), .Clk(CLK), .R1(regifile_1_r1), .R2(regifile_1_r2), .WE(RegWrite), .W_num(mem_we_1_rdout),
    .R1_num(multiplexer_2_out), .R2_num(multiplexer_3_out));
  or or_3 (or_3_out, \单周期硬布线控制器_1_lui , \单周期硬布线控制器_1_auipc );
  Pull_Resistor #(.pull(1)) pull_resistor_1 (.node(CLK));
  // Probe on \相关逻辑处理_重定向_1_rs2_forward 
  // Probe on \相关逻辑处理_重定向_1_rs1_forward 
  Multiplexer #(.select(1), .width(32), .disabled("Z"), .enable("false")) multiplexer_8 (
    .in0(multiplexer_7_out), .in1({ID_IR[31:12], {12{1'b0}}}), .out(multiplexer_8_out), .sel(or_3_out));
  // Probe on regifile_1_r1
  // Probe on regifile_1_r2
  // Probe on multiplexer_8_out
  // Probe on ID_IR[11:7]
  // Probe on ID_PC
  // RiscV_Probe riscv_probe_7: pin names not known
  not not_4 (not_4_out, halt);
  Counter #(.width(16), .max('hffff), .ongoal("wrap"), .trigger("rising"), .behavior("new")) counter_2 (
    .D(16'h1), .count(not_4_out), .Q(\总周期数 ), .clk(CLK), .clr(RST));  // open: load, carry, preset, down
  ID_EX id_ex_1 (
    .JALin(\单周期硬布线控制器_1_jal ), .JALRin(\单周期硬布线控制器_1_jalr ), .Beqin(\单周期硬布线控制器_1_beq ),
    .AUIPCin(\单周期硬布线控制器_1_auipc ), .Bnein(\单周期硬布线控制器_1_bne ), .LUIin(\单周期硬布线控制器_1_lui ),
    .MemToRegin(\单周期硬布线控制器_1_memtoreg ), .LHin(\单周期硬布线控制器_1_lh ), .MemWritein(\单周期硬布线控制器_1_memwrite ),
    .RS1(regifile_1_r1), .BLTUin(\单周期硬布线控制器_1_bltu ), .AluOPin(\单周期硬布线控制器_1_alu_op ), .RS2(regifile_1_r2),
    .AluSrcBin(\单周期硬布线控制器_1_alu_src ), .RD(ID_IR[11:7]), .RegWrite(\单周期硬布线控制器_1_regwrite ),
    .imm(multiplexer_8_out), .CLK(CLK), .RST(\相关逻辑处理_重定向_1_id_ex_clr ), .halt(halt), .JALout(EX_JAL),
    .JALRout(EX_JALR), .Beqout(EX_Beq), .ALUIPCout(EX_AUIPC), .Bneout(EX_Bne), .LUIout(EX_LUI),
    .MemToRegout(id_ex_1_memtoregout), .LHout(id_ex_1_lhout), .MemWriteout(id_ex_1_memwriteout),
    .RS1out(id_ex_1_rs1out), .BLTUout(EX_Bltu), .AluOPout(EX_AluOP), .RS2out(id_ex_1_rs2out),
    .AluSrcBout(EX_SrcB), .RDout(id_ex_1_rdout), .RegWriteout(id_ex_1_regwriteout), .Immout(id_ex_1_immout),
    .PC(ID_PC), .PCout(EX_PC), .Ecallin(\单周期硬布线控制器_1_ecall ), .Ecallout(EX_ecall), .IRin(ID_IR),
    .IRout(EX_IR), .RS1_f_in(\相关逻辑处理_重定向_1_rs1_forward ), .RS1_f_out(id_ex_1_rs1_f_out),
    .RS2_f_in(\相关逻辑处理_重定向_1_rs2_forward ), .RS2_f_out(id_ex_1_rs2_f_out));  // open: URETin, CSRRSIin, CSRRCIin, S_typein, URETout, CSRRSIout, CSRRCIout, S_typeout
  // Probe on MEM_ALUData
  or or_4 (BranchTaken, and_6_out, EX_JALR, EX_JAL, and_4_out, and_3_out);
  // Probe on id_ex_1_rs1_f_out
  Multiplexer #(.select(2), .width(32), .disabled("Z"), .enable("false")) multiplexer_9 (
    .in0(id_ex_1_rs1out), .in1(RDin), .in2(MEM_ALUData), .in3(id_ex_1_rs1out), .out(multiplexer_9_out),
    .sel(id_ex_1_rs1_f_out));
  // Probe on id_ex_1_rs2_f_out
  Multiplexer #(.select(2), .width(32), .disabled("Z"), .enable("false")) multiplexer_10 (
    .in0(id_ex_1_rs2out), .in1(RDin), .in2(MEM_ALUData), .in3(id_ex_1_rs2out), .out(multiplexer_10_out),
    .sel(id_ex_1_rs2_f_out));
  Adder #(.width(32)) adder_2 (.a(EX_PC), .b(id_ex_1_immout), .out(adder_2_out));  // open: cin, cout
  Adder #(.width(32)) adder_3 (.a(32'h4), .b(EX_PC), .out(adder_3_out));  // open: cin, cout
  Adder #(.width(32)) adder_4 (.a(id_ex_1_immout), .b(EX_PC), .out(adder_4_out));  // open: cin, cout
  Adder #(.width(32)) adder_5 (.a(multiplexer_9_out), .b(id_ex_1_immout), .out(adder_5_out));  // open: cin, cout
  and and_3 (and_3_out, EX_eq, EX_Beq);
  and and_4 (and_4_out, not_5_out, EX_Bne);
  not not_5 (not_5_out, EX_eq);
  // Probe on RDin
  // Probe on multiplexer_10_out
  or or_5 (or_5_out, EX_JAL, EX_JALR);
  Multiplexer #(.select(1), .width(32), .disabled("Z"), .enable("false")) multiplexer_11 (
    .in0(EX_ALUData), .in1(adder_3_out), .out(multiplexer_11_out), .sel(or_5_out));
  Multiplexer #(.select(1), .width(32), .disabled("Z"), .enable("false")) multiplexer_12 (
    .in0(adder_4_out), .in1(and_5_out), .out(multiplexer_12_out), .sel(EX_JALR));
  assign and_5_out = adder_5_out & 32'hfffffffe;  // AND_Gate and_5, 32 bits wide
  Multiplexer #(.select(1), .width(32), .disabled("Z"), .enable("false")) multiplexer_13 (
    .in0(multiplexer_10_out), .in1(id_ex_1_immout), .out(multiplexer_13_out), .sel(EX_SrcB));
  Multiplexer #(.select(1), .width(32), .disabled("Z"), .enable("false")) multiplexer_14 (
    .in0(multiplexer_11_out), .in1(adder_2_out), .out(multiplexer_14_out), .sel(EX_AUIPC));
  // Probe on multiplexer_12_out
  and and_6 (and_6_out, EX_Bltu, EX_less);
  // Probe on multiplexer_9_out
  // Probe on multiplexer_13_out
  Multiplexer #(.select(1), .width(32), .disabled("Z"), .enable("false")) multiplexer_15 (
    .in0(multiplexer_14_out), .in1(id_ex_1_immout), .out(multiplexer_15_out), .sel(EX_LUI));
  ALU alu_1 (
    .X(multiplexer_9_out), .Y(multiplexer_13_out), .AluOP(EX_AluOP), .Equal(EX_eq), .Result(EX_ALUData),
    .out_6(EX_less));  // open: Result_2, out_4
  // Probe on multiplexer_15_out
  // Probe on id_ex_1_rdout
  ecall_deal ecall_deal_1 (
    .ecall(EX_ecall), .a0(multiplexer_10_out), .clk(CLK), .go(1'b0), .LedData(LedData),
    .halt(ecall_deal_1_halt), .rs1_data(multiplexer_9_out));
  // RiscV_Probe riscv_probe_8: pin names not known
  // EX_MEM ex_mem_1: pin names not known; wires that end beside it: EX_eq, EX_less, id_ex_1_memtoregout, id_ex_1_memwriteout, id_ex_1_regwriteout, id_ex_1_lhout, multiplexer_15_out, multiplexer_10_out, id_ex_1_rdout, EX_PC, EX_IR, ecall_deal_1_halt, RST, CLK, halt, ex_mem_1_p16, MemWrite, ex_mem_1_p18, ex_mem_1_p19, MEM_ALUData, MDin, ex_mem_1_p22, M_PC, MEM_IR, ex_mem_1_p25
  // RiscV_Probe riscv_probe_9: pin names not known; wires that end beside it: multiplexer_15_out
  // Probe on ex_mem_1_p22
  // Probe on MDin
  or or_6 (or_6_out, EX_JAL, EX_JALR);
  Counter #(.width(16), .max('hffff), .ongoal("wrap"), .trigger("rising"), .behavior("new")) counter_3 (
    .D(16'h1), .count(or_6_out), .Q(\无条件分支数 ), .clk(CLK));  // open: load, carry, clr, preset, down
  // Probe on MEM_ALUData
  // Probe on ex_mem_1_p22
  or or_7 (or_7_out, MemWrite, ex_mem_1_p16);
  or or_8 (or_8_out, EX_Beq, EX_Bne, EX_Bltu);
  RAM #(.addrWidth(10), .dataWidth(32), .bus("separate"), .Select("high")) ram_1 (
    .addr(MEM_ALUData[11:2]), .din(MDin), .data(ram_1_data), .str(MemWrite), .sel(or_7_out), .clk(CLK),
    .ld(ex_mem_1_p16), .clr(RST));
  and and_7 (and_7_out, or_8_out, BranchTaken);
  Counter #(.width(16), .max('hffff), .ongoal("wrap"), .trigger("rising"), .behavior("new")) counter_4 (
    .D(16'h1), .count(and_7_out), .Q(\条件分支成功数 ), .clk(CLK));  // open: load, carry, clr, preset, down
  \相关逻辑处理_重定向  \u_相关逻辑处理_重定向_1  (
    .rs1(multiplexer_2_out), .rs2(multiplexer_5_out), .EX_WriteReg(id_ex_1_rdout),
    .EX_MemToReg(id_ex_1_memtoregout), .EX_RegWrite(id_ex_1_regwriteout), .MEM_WriteReg(ex_mem_1_p22),
    .MEM_RegWrite(ex_mem_1_p18), .BranchTaken(BranchTaken), .stall(\相关逻辑处理_重定向_1_stall ),
    .IF_ID_CLR(\相关逻辑处理_重定向_1_if_id_clr ), .ID_EX_CLR(\相关逻辑处理_重定向_1_id_ex_clr ),
    .RS1_Forward(\相关逻辑处理_重定向_1_rs1_forward ), .RS2_Forward(\相关逻辑处理_重定向_1_rs2_forward ),
    .LoadUse(\相关逻辑处理_重定向_1_loaduse ));  // open: PC_EN
  assign bit_extender_5_out = {{16{ram_1_data[15]}}, ram_1_data[15:0]};  // Bit_Extender bit_extender_5
  assign bit_extender_6_out = {{16{ram_1_data[31]}}, ram_1_data[31:16]};  // Bit_Extender bit_extender_6
  // Probe on MEM_ALUData
  Counter #(.width(16), .max('hffff), .ongoal("wrap"), .trigger("rising"), .behavior("new")) counter_5 (
    .D(16'h1), .count(\相关逻辑处理_重定向_1_loaduse ), .Q(\LoadUse次数 ), .clk(CLK));  // open: load, carry, clr, preset, down
  Multiplexer #(.select(2), .width(32), .disabled("Z"), .enable("false")) multiplexer_16 (
    .in0(bit_extender_5_out), .in1({32{1'b0}}), .in2(bit_extender_6_out), .in3({32{1'b0}}),
    .out(multiplexer_16_out), .sel(MEM_ALUData[1:0]));
  Multiplexer #(.select(1), .width(32), .disabled("Z"), .enable("false")) multiplexer_17 (
    .in0(ram_1_data), .in1(multiplexer_16_out), .out(multiplexer_17_out), .sel(ex_mem_1_p19));
  // Probe on multiplexer_17_out
  MEM_WE mem_we_1 (
    .MemToRegin(ex_mem_1_p16), .ALU_Result(MEM_ALUData), .Mem_Result(multiplexer_17_out),
    .RegWrite(ex_mem_1_p18), .RD(ex_mem_1_p22), .CLK(CLK), .RST(RST), .halt(halt),
    .MemToRegout(mem_we_1_memtoregout), .ALU_Resultout(mem_we_1_alu_resultout),
    .Mem_Resultout(mem_we_1_mem_resultout), .RegWriteout(RegWrite), .RDout(mem_we_1_rdout), .PC(M_PC),
    .PCout(WB_PC), .Haltin(ex_mem_1_p25), .Haltout(mem_we_1_haltout), .IRin(MEM_IR), .IRout(WB_IR));  // open: JALin, JALRin, Beqin, AUIPCin, Bnein, LUIin, LHin, MemWritein, BLTUin, AluOPin, URETin, AluSrcBin, CSRRSIin, CSRRCIin, S_typein, JALout, JALRout, Beqout, ALUIPCout, Bneout, LUIout, LHout, MemWriteout, BLTUout, AluOPout, URETout, AluSrcBout, CSRRSIout, CSRRCIout, S_typeout, Ecallin, Ecallout
  Multiplexer #(.select(1), .width(32), .disabled("Z"), .enable("false")) multiplexer_18 (
    .in0(mem_we_1_alu_resultout), .in1(mem_we_1_mem_resultout), .out(RDin), .sel(mem_we_1_memtoregout));
  // Probe on RDin
  not not_6 (not_6_out, Go);
  // RiscV_Probe riscv_probe_10: pin names not known; wires that end beside it: ex_mem_1_p25
  and and_8 (and_8_out, mem_we_1_haltout, not_6_out);
  D_Flip_Flop #(.trigger("falling"), .Pre_Clr_Positions("ABOVE_BELOW"), .NegatePresetClear("false"), .enable("false"), .NewFFLayout("true")) d_ff_2 (
    .clk(CLK), .D(and_8_out), .Q(halt));  // open: Qn, preset, reset

  // Other names for the same wires on the sheet: MEM_PC[31:0] = M_PC; WB_WriteData[31:0] = RDin;
  //   插入气泡数[15:0] = \LoadUse次数 

  // Notes on the sheet:
  //   中断源
  //   时空图监测，可删除
  //   中断等待指示
  //   数码管输出
  //   contents of 指令存储器 (hex, n*v repeats v):
  //   100493 100006f 100493 200913 300993 100006f 100493 200913 300993 100006f 100493 200913 300993
  //   100006f 100493 200913 300993 428000ef 100413 100493 1f49493 900533 2200893 73 24d493 48463 fedff06f
  //   900533 2200893 73 100493 249493 900533 2200893 73 48463 fedff06f 100493 1f49493 900533 2200893 73
  //   4034d493 900533 2200893 73 4044d493 900533 2200893 73 4044d493 900533 2200893 73 4044d493 900533
  //   2200893 73 4044d493 900533 2200893 73 4044d493 900533 2200893 73 4044d493 900533 2200893 73 4044d493
  //   900533 2200893 73 100413 1f41993 41f9d993 433 c00913 300b13 140413 f47413 800293 100313 499993
  //   89e9b3 1300533 2200893 73 406282b3 fe0294e3 140413 f00f93 1f47433 1c41413 800293 100313 49d993
  //   89e9b3 1300533 2200893 73 406282b3 fe0294e3 1c45413 406b0b33 b0463 f95ff06f 2b3 fff2c293 829293
  //   ff2e293 500533 2200893 73 fff00413 493 84a023 140413 448493 84a023 140413 448493 84a023 140413
  //   448493 84a023 140413 448493 84a023 140413 448493 84a023 140413 448493 84a023 140413 448493 84a023
  //   140413 448493 84a023 140413 448493 84a023 140413 448493 84a023 140413 448493 84a023 140413 448493
  //   84a023 140413 448493 84a023 140413 448493 84a023 140413 448493 84a023 140413 448493 140413 433
  //   3c00493 42983 4aa03 149a2b3 28663 134a023 1442023 ffc48493 fe9412e3 800533 2200893 73 440413 3c00493
  //   fc9416e3 13 430497 900533 2200893 73 430497 900533 2200893 73 430497 900533 2200893 73 430497 900533
  //   2200893 73 430497 900533 2200893 73 430497 900533 2200893 73 430497 900533 2200893 73 430497 900533
  //   2200893 73 a00893 73 800e13 fedc04b7 fff00413 1045413 84e4b3 900533 2200893 73 ba984b7 900533 73
  //   76544b7 900533 73 32104b7 900533 73 fffe0e13 fa0e1ee3 a00893 73 313 1000e13 8400493 849493 8348493
  //   400913 891913 490913 849493 8248493 849493 8148493 891913 490913 891913 490913 932023 12484b3 430313
  //   fffe0e13 fe0e18e3 2000e13 313 31483 900533 2200893 73 230313 fffe0e13 fe0e14e3 a00893 73 ff100493
  //   900533 2200893 73 148493 fe9068e3 900533 2200893 73 a00893 73 a00893 73 413 140413 800533 2200893 73
  //   240413 800533 2200893 73 340413 800533 2200893 73 440413 800533 2200893 73 540413 800533 2200893 73
  //   640413 800533 2200893 73 740413 800533 2200893 73 840413 800533 2200893 2200893 73 8067
  //   opcode
  //   funct
  //   rs1
  //   rs2
  //   JAL
  //   JALR
  //   AUIPC
  //   LUI
  //   ecall
  //   I:imm
  //   S:imm
  //   B:imm
  //   J:imm
  //   U:imm
  //   rd
  //   Beq
  //   Bne
  //   MemToReg
  //   MemWrite
  //   AluOP
  //   AluSrcB
  //   RegWrite
  //   S_type
  //   控制位
  //   流水调试日志用
  //   暂停节拍，不能为0
  //   戳工具置1进入计数暂停模式，ctrl+k时钟自动运行到对应节拍暂停
  //   ctrl+k关闭时钟连续运行，将控制位置零，进入单步调试模式调试
  //   可计数暂停的时钟源
  //   为方便自动评测，需要输出流水线各段保存的PC值，注意是PC不是PC+4，另外ID段寄存器写入信息，Mem段内存写入信息也要输出
  //   数据存储器
endmodule

module \中断按键参考电路  (
  input  \同步清零信号 ,
  output \与中断屏蔽位与 
);

  wire \_1号中断_out , and_1_out, clock_1_out, d_ff_1_q, or_1_out, or_2_out;

  Clock #(.highDuration(1), .lowDuration(1)) clock_1 (.out(clock_1_out));
  Button \_1号中断  (.out(\_1号中断_out ));
  or or_1 (or_1_out, \与中断屏蔽位与 , d_ff_1_q);
  LED #(.active("true")) \_1号中断等待指示灯  (.in(or_1_out));
  D_Flip_Flop #(.trigger("rising"), .Pre_Clr_Positions("LEGACY"), .NegatePresetClear("false"), .enable("true"), .NewFFLayout("false")) d_ff_1 (
    .clk(\_1号中断_out ), .D(1'b1), .Q(d_ff_1_q), .reset(\与中断屏蔽位与 ));  // open: Qn, preset, en
  or or_2 (or_2_out, d_ff_1_q, \与中断屏蔽位与 );
  and and_1 (and_1_out, or_2_out, ~\同步清零信号 );  // AND_Gate
  D_Flip_Flop #(.trigger("rising"), .Pre_Clr_Positions("LEGACY"), .NegatePresetClear("false"), .enable("true"), .NewFFLayout("false")) IR1 (
    .clk(clock_1_out), .D(and_1_out), .Q(\与中断屏蔽位与 ));  // open: Qn, preset, en, reset

  // Notes on the sheet:
  //   中断信号采样参考电路
  //   Reset 
endmodule

module \单周期_单级中断  (
  input  IR1,
  input  IR2,
  input  IR3,
  output RegWrite,
  output MemWrite,
  output [31:0] PC,
  output [31:0] IR,
  output [31:0] RDin,
  output [31:0] MDin,
  output [31:0] LedData
);

  wire ALU_equal, ALU_less, ALU_more_equal, AluSrcB, and_1_out, and_2_out, AUIPC, Beq, BLTU, Bne, CLK,
       clock_2_out, CLRA, CLRB, CLRC, comparator_1_eq, comparator_2_eq, comparator_3_eq, comparator_4_eq,
       comparator_5_eq, comparator_5_lt, controlled_inverter_1_out, controlled_inverter_2_out,
       controlled_inverter_3_out, d_ff_1_q, ecall, Go, halt, Int, IR1_t, IR2_t, IR3_t, IRA, IRB, IRC, JAL,
       JALR, LH, LUI, MemToReg, nand_1_out, not_1_out, not_2_out, not_3_out, or_1_out, or_2_out, or_6_out,
       priority_encoder_1_gs, RST, S_type, t_ff_1_q, t_ff_1_qn, uret, W1, W2, W3, \中断_1_与中断屏蔽位与 ,
       \中断_2_与中断屏蔽位与 , \中断_3_与中断屏蔽位与 , \单周期硬布线控制器_1_ecall ;
  wire [1:0] interrupt;
  wire [3:0] AluOP;
  wire [4:0] multiplexer_4_out, multiplexer_5_out;
  wire [12:0] CNT_num;
  wire [15:0] \总周期数 ;
  wire [31:0] ALU_reslut, bit_extender_2_out, bit_extender_5_out, bit_extender_6_out, I_offset,
       Mem_LH_reslut, Mem_reslut, multiplexer_1_out, multiplexer_2_out, multiplexer_3_out, multiplexer_6_out,
       multiplexer_7_out, pc_next_1_next_pc, register_1_q, rs1_data;
  wire [31:1] B_offset, J_offset;
  wire [31:31] bit_extender_3_out, bit_extender_4_out;

  Clock #(.highDuration(1), .lowDuration(1)) clock_1 ();  // open: out
  Button _1 (.out(IRA));
  Button _2 (.out(IRB));
  Button _3 (.out(IRC));
  Button \u_继续运行  (.out(Go));
  LED #(.active("true")) led_1 (.in(W1));
  LED #(.active("true")) led_2 (.in(W2));
  LED #(.active("true")) led_3 (.in(W3));
  Hex_Digit_Display hex_digit_display_1 (.value(LedData[31:28]));  // open: dp
  Comparator #(.width(16), .mode("twosComplement")) comparator_1 (
    .a(16'h23b), .b(\总周期数 ), .eq(comparator_1_eq));  // open: gt, lt
  Comparator #(.width(16), .mode("twosComplement")) comparator_2 (
    .a(\总周期数 ), .b(16'h1), .eq(comparator_2_eq));  // open: gt, lt
  Comparator #(.width(16), .mode("twosComplement")) comparator_3 (
    .a(\总周期数 ), .b(16'h4), .eq(comparator_3_eq));  // open: gt, lt
  Comparator #(.width(16), .mode("twosComplement")) comparator_4 (
    .a(\总周期数 ), .b(16'h7), .eq(comparator_4_eq));  // open: gt, lt
  pc_next pc_next_1 (
    .pc(PC), .B_offset({B_offset, 1'b0}), .J_offset({J_offset, 1'b0}), .I_offset(I_offset),
    .next_pc(pc_next_1_next_pc), .rs1(rs1_data), .ALU_equal(ALU_equal), .Bne(Bne), .Beq(Beq), .JALR(JALR),
    .ALU_less(ALU_less), .JAL(JAL), .BLTU(BLTU));
  Multiplexer #(.select(2), .width(32), .disabled("Z"), .enable("false")) multiplexer_1 (
    .in0({32{1'b0}}), .in1(32'h30ac), .in2(32'h3150), .in3(32'h31f4), .out(multiplexer_1_out), .sel(interrupt));
  \中断  \u_中断_1  (.wait_uret(W1), .\与中断屏蔽位与 (\中断_1_与中断屏蔽位与 ), .\同步清零信号 (CLRA), .clk(CLK), .button(IRA));
  \中断  \u_中断_2  (.wait_uret(W2), .\与中断屏蔽位与 (\中断_2_与中断屏蔽位与 ), .\同步清零信号 (CLRB), .clk(CLK), .button(IRB));
  \中断  \u_中断_3  (.wait_uret(W3), .\与中断屏蔽位与 (\中断_3_与中断屏蔽位与 ), .\同步清零信号 (CLRC), .clk(CLK), .button(IRC));
  Hex_Digit_Display hex_digit_display_2 (.value(LedData[23:20]));  // open: dp
  Hex_Digit_Display hex_digit_display_3 (.value(LedData[27:24]));  // open: dp
  or or_1 (or_1_out, comparator_1_eq, comparator_2_eq);
  assign controlled_inverter_1_out = or_1_out ? ~CLK : 1'bz;  // Controlled_Inverter controlled_inverter_1
  assign controlled_inverter_2_out = comparator_3_eq ? ~CLK : 1'bz;  // Controlled_Inverter controlled_inverter_2
  assign controlled_inverter_3_out = comparator_4_eq ? ~CLK : 1'bz;  // Controlled_Inverter controlled_inverter_3
  // Probe on pc_next_1_next_pc
  Hex_Digit_Display hex_digit_display_4 (.value(LedData[15:12]));  // open: dp
  Hex_Digit_Display hex_digit_display_5 (.value(LedData[19:16]));  // open: dp
  Pull_Resistor #(.pull(0)) pull_resistor_1 (.node(controlled_inverter_1_out));
  Pull_Resistor #(.pull(0)) pull_resistor_2 (.node(controlled_inverter_2_out));
  Pull_Resistor #(.pull(0)) pull_resistor_3 (.node(controlled_inverter_3_out));
  Multiplexer #(.select(1), .width(32), .disabled("Z"), .enable("false")) multiplexer_2 (
    .in0(pc_next_1_next_pc), .in1(multiplexer_1_out), .out(multiplexer_2_out), .sel(Int));
  Register #(.width(32), .trigger("rising"), .Select("low")) register_1 (
    .D(pc_next_1_next_pc), .en(Int), .Q(register_1_q), .clk(CLK));  // open: clr
  // Probe on register_1_q
  Priority_Encoder #(.select(2), .disabled("Z")) priority_encoder_1 (
    .in0(1'b0), .in1(\中断_1_与中断屏蔽位与 ), .in2(\中断_2_与中断屏蔽位与 ), .in3(\中断_3_与中断屏蔽位与 ), .out(interrupt),
    .gs(priority_encoder_1_gs), .en_in(1'b1));  // open: en_out
  Hex_Digit_Display hex_digit_display_6 (.value(LedData[7:4]));  // open: dp
  Hex_Digit_Display hex_digit_display_7 (.value(LedData[11:8]));  // open: dp
  // Probe on \总周期数 
  not not_1 (not_1_out, halt);
  Multiplexer #(.select(1), .width(32), .disabled("Z"), .enable("false")) multiplexer_3 (
    .in0(multiplexer_2_out), .in1(register_1_q), .out(multiplexer_3_out), .sel(uret));
  Demultiplexer #(.select(2), .width(1), .tristate("false"), .disabled(0), .enable("true")) demultiplexer_1 (
    .out1(CLRA), .out2(CLRB), .out3(CLRC), .in(Int), .sel(interrupt), .en(priority_encoder_1_gs));  // open: out0
  and and_1 (and_1_out, t_ff_1_qn, Int);
  and and_2 (and_2_out, uret, t_ff_1_q);
  Hex_Digit_Display hex_digit_display_8 (.value(LedData[3:0]));  // open: dp
  Counter #(.width(16), .max('hffff), .ongoal("wrap"), .trigger("rising"), .behavior("new")) counter_1 (
    .D(16'h1), .count(not_1_out), .Q(\总周期数 ), .clk(CLK), .clr(RST));  // open: load, carry, preset, down
  // Probe on multiplexer_3_out
  // Probe on multiplexer_3_out
  not not_2 (not_2_out, halt);
  or or_2 (or_2_out, and_1_out, and_2_out);
  ecall_deal ecall_deal_1 (
    .ecall(ecall), .a0(MDin), .clk(CLK), .go(Go), .LedData(LedData), .halt(halt), .rs1_data(rs1_data));
  Button \u_复位  (.out(RST));
  // Probe on PC
  // Probe on PC
  Register #(.width(32), .trigger("rising"), .Select("low")) u_PC (
    .D(multiplexer_3_out), .en(not_2_out), .Q(PC), .clk(CLK), .clr(RST));
  T_Flip_Flop #(.trigger("rising"), .Pre_Clr_Positions("ABOVE_BELOW"), .NegatePresetClear("false"), .enable("false"), .NewFFLayout("true")) t_ff_1 (
    .clk(CLK), .T(or_2_out), .Q(t_ff_1_q), .Qn(t_ff_1_qn));  // open: preset, reset
  or or_3 (IR1_t, IR1, IRA);
  // Probe on PC[11:2]
  and and_3 (Int, priority_encoder_1_gs, t_ff_1_qn);
  or or_4 (IR2_t, IR2, IRB);
  // RiscV_Probe riscv_probe_1: pin names not known; wires that end beside it: IR
  D_Flip_Flop #(.trigger("high"), .Pre_Clr_Positions("LEGACY"), .NegatePresetClear("false"), .enable("true"), .NewFFLayout("false")) d_ff_1 (.Q(d_ff_1_q));  // open: clk, D, Qn, preset, en, reset
  // Probe on 13'h2f5
  ROM #(.addrWidth(10), .dataWidth(32), .Select("high")) rom_1 (.addr(PC[11:2]), .data(IR));
  // Probe on IR
  or or_5 (IR3_t, IR3, IRC);
  Comparator #(.width(13), .mode("twosComplement")) comparator_5 (
    .a(CNT_num), .b(13'h2f5), .eq(comparator_5_eq), .lt(comparator_5_lt));  // open: gt
  Clock #(.highDuration(1), .lowDuration(1)) clock_2 (.out(clock_2_out));
  Counter #(.width(13), .max('h1fff), .ongoal("stay"), .trigger("rising"), .behavior("old")) counter_2 (
    .count(comparator_5_lt), .Q(CNT_num), .clk(clock_2_out));  // open: load, D, carry, clr, preset
  \单周期硬布线控制器  \u_单周期硬布线控制器_1  (
    .Funct({IR[30], IR[25], IR[14:12]}), .OP(IR[6:2]), .ALU_OP(AluOP), .MemToReg(MemToReg),
    .MemWrite(MemWrite), .ALU_SRC(AluSrcB), .RegWrite(RegWrite), .ecall(\单周期硬布线控制器_1_ecall ),
    .S_type(S_type), .Jalr(JALR), .Beq(Beq), .JAL(JAL), .Bne(Bne), .AUIPC(AUIPC), .BLTU(BLTU), .LH(LH),
    .LUI(LUI));  // open: CSRRSI, CSRRCI
  Multiplexer #(.select(1), .width(5), .disabled("Z"), .enable("false")) multiplexer_4 (
    .in0(IR[19:15]), .in1(5'b10001), .out(multiplexer_4_out), .sel(ecall));
  Multiplexer #(.select(1), .width(5), .disabled("Z"), .enable("false")) multiplexer_5 (
    .in0(IR[24:20]), .in1(5'b01010), .out(multiplexer_5_out), .sel(ecall));
  nand nand_1 (nand_1_out, d_ff_1_q, comparator_5_eq);
  not not_3 (not_3_out, uret);
  and and_4 (uret, IR[21], \单周期硬布线控制器_1_ecall );
  rd_in rd_in_1 (
    .ALU_result(ALU_reslut), .Mem_result(Mem_reslut), .MemToReg(MemToReg), .PC(PC), .JAL(JAL), .JALR(JALR),
    .RDin(RDin), .U_imm({IR[31:12], {12{1'b0}}}), .LUI(LUI), .AUIPC(AUIPC), .LH(LH),
    .Mem_LH_result(Mem_LH_reslut));
  assign I_offset = {{20{IR[31]}}, IR[31:20]};  // Bit_Extender bit_extender_1
  assign bit_extender_2_out = {{20{IR[31]}}, {IR[31:25], IR[11:7]}};  // Bit_Extender bit_extender_2
  assign {bit_extender_3_out[31], B_offset} = {{20{IR[31]}}, {IR[31], IR[7], IR[30:25], IR[11:8]}};  // Bit_Extender bit_extender_3
  assign {bit_extender_4_out[31], J_offset} = {{12{IR[31]}}, {IR[31], IR[19:12], IR[20], IR[30:21]}};  // Bit_Extender bit_extender_4
  assign CLK = nand_1_out ? clock_2_out : 1'bz;  // Controlled_Buffer controlled_buffer_1
  Pull_Resistor #(.pull(1)) pull_resistor_4 (.node(CLK));
  and and_5 (ecall, \单周期硬布线控制器_1_ecall , not_3_out);
  // Probe on multiplexer_4_out
  // Probe on multiplexer_5_out
  // Probe on IR[11:7]
  // Probe on RDin
  Regifile regifile_1 (
    .Din(RDin), .Clk(CLK), .R1(rs1_data), .R2(MDin), .WE(RegWrite), .W_num(IR[11:7]),
    .R1_num(multiplexer_4_out), .R2_num(multiplexer_5_out));
  // Probe on I_offset
  // Probe on bit_extender_2_out
  // Probe on {B_offset, 1'b0}
  // Probe on {J_offset, 1'b0}
  // Probe on {IR[31:12], {12{1'b0}}}
  Multiplexer #(.select(1), .width(32), .disabled("Z"), .enable("false")) multiplexer_6 (
    .in0(MDin), .in1(I_offset), .out(multiplexer_6_out), .sel(AluSrcB));
  Multiplexer #(.select(1), .width(32), .disabled("Z"), .enable("false")) multiplexer_7 (
    .in0(multiplexer_6_out), .in1(bit_extender_2_out), .out(multiplexer_7_out), .sel(S_type));
  // Probe on rs1_data
  // Probe on multiplexer_7_out
  ALU alu_1 (
    .X(rs1_data), .Y(multiplexer_7_out), .AluOP(AluOP), .Equal(ALU_equal), .Result(ALU_reslut),
    .out_4(ALU_more_equal), .out_6(ALU_less));  // open: Result_2
  // Probe on ALU_reslut
  or or_6 (or_6_out, MemWrite, MemToReg);
  RAM #(.addrWidth(10), .dataWidth(32), .bus("separate"), .Select("high")) ram_1 (
    .addr(ALU_reslut[11:2]), .din(MDin), .data(Mem_reslut), .str(MemWrite), .sel(or_6_out), .clk(CLK),
    .ld(MemToReg), .clr(RST));
  assign bit_extender_5_out = {{16{Mem_reslut[15]}}, Mem_reslut[15:0]};  // Bit_Extender bit_extender_5
  assign bit_extender_6_out = {{16{Mem_reslut[31]}}, Mem_reslut[31:16]};  // Bit_Extender bit_extender_6
  Multiplexer #(.select(2), .width(32), .disabled("Z"), .enable("false")) multiplexer_8 (
    .in0(bit_extender_5_out), .in1({32{1'b0}}), .in2(bit_extender_6_out), .in3({32{1'b0}}),
    .out(Mem_LH_reslut), .sel(ALU_reslut[1:0]));

  // Other names for the same wires on the sheet: rs2_data[31:0] = MDin; U_RDin[31:12] = IR[31:12]

  // Notes on the sheet:
  //   中断源
  //   中断等待指示
  //   总复位信号应将除ROM以外所有存储组件全部清零
  //   单级中断测试信号模拟器
  //   中断不能被其他中断请求中断
  //   数码管输出
  //   数码管输出应该用寄存器锁存，否则显示数据只能一闪而过
  //   ecall 信号处理
  //   周期计数
  //   指令存储器
  //   控制位
  //   暂停节拍，不能为0
  //   指令字
  //   contents of rom_1 (hex, n*v repeats v):
  //   7d000113 100413 1f41993 41f9d993 433 c00913 800b13 140413 f47413 800293 100313 499993 89e9b3 1300533
  //   2200893 73 406282b3 fe0294e3 140413 f00f93 1f47433 1c41413 800293 100313 49d993 89e9b3 1300533
  //   2200893 73 406282b3 fe0294e3 1c45413 406b0b33 b0463 f95ff06f 2b3 fff2c293 1029293 fff2e293 500533
  //   2200893 73 f5dff06f 1112023 410113 a12023 410113 812023 410113 1312023 410113 1412023 410113 1512023
  //   410113 1612023 410113 100b13 300a13 100a93 1600433 441413 14469b3 1300533 2200893 73 fe0416e3
  //   415a0a33 fe0a10e3 ffc10113 12b03 ffc10113 12a83 ffc10113 12a03 ffc10113 12983 ffc10113 12403
  //   ffc10113 12503 ffc10113 12883 200073 1112023 410113 a12023 410113 812023 410113 1312023 410113
  //   1412023 410113 1512023 410113 1612023 410113 200b13 300a13 100a93 1600433 441413 14469b3 1300533
  //   2200893 73 fe0416e3 415a0a33 fe0a10e3 ffc10113 12b03 ffc10113 12a83 ffc10113 12a03 ffc10113 12983
  //   ffc10113 12403 ffc10113 12503 ffc10113 12883 200073 1112023 410113 a12023 410113 812023 410113
  //   1312023 410113 1412023 410113 1512023 410113 1612023 410113 300b13 300a13 100a93 1600433 441413
  //   14469b3 1300533 2200893 73 fe0416e3 415a0a33 fe0a10e3 ffc10113 12b03 ffc10113 12a83 ffc10113 12a03
  //   ffc10113 12983 ffc10113 12403 ffc10113 12503 ffc10113 12883 200073
  //   JAL
  //   JALR
  //   opcode
  //   funct
  //   ecall
  //   rs1
  //   rs2
  //   rd
  //   I:imm
  //   S:imm
  //   B:imm
  //   J:imm
  //   U:imm
  //   Beq
  //   Bne
  //   MemToReg
  //   MemWrite
  //   AluOP
  //   AluSrcB
  //   RegWrite
  //   S_type
  //   为方便自动评测，需要输出PC，IR，寄存器堆写如数据RDin
  //   可计数暂停的时钟源
  //   RAM写使能MemWrite、RAM写入数据MDin等信号
  //   数据存储器
endmodule

module \单周期_多级中断  (
  input  IR1,
  input  IR2,
  input  IR3,
  output RegWrite,
  output MemWrite,
  output [31:0] PC,
  output [31:0] IR,
  output [31:0] RDin,
  output [31:0] MDin,
  output [31:0] LedData
);

  wire ALU_equal, ALU_less, ALU_more_equal, AluSrcB, and_1_out, and_2_out, and_3_out, AUIPC, Beq, BLTU, Bne,
       CLK, clock_2_out, CLRA, CLRB, CLRC, comparator_1_gt, comparator_2_eq, comparator_2_lt,
       comparator_3_eq, comparator_4_eq, comparator_5_eq, comparator_6_eq, comparator_7_eq, CSRRCI, CSRRSI,
       d_ff_1_q, ecall, Go, halt, Int, IR1_t, IR2_t, IR3_t, IRA, IRB, IRC, JAL, JALR, LH, LUI, MemToReg,
       multiplexer_5_out, nand_1_out, not_1_out, not_2_out, not_3_out, or_1_out, or_2_out, or_3_out,
       or_4_out, or_8_out, or_9_out, or_10_out, pop, priority_encoder_1_gs, RST, S_type, t_ff_1_q, t_ff_1_qn,
       W1, W2, W3, \中断_1_与中断屏蔽位与 , \中断_2_与中断屏蔽位与 , \中断_3_与中断屏蔽位与 , \单周期硬布线控制器_1_ecall ;
  wire [1:0] interrupt, Interrut_q, multiplexer_4_out;
  wire [3:0] AluOP;
  wire [4:0] multiplexer_6_out, multiplexer_7_out;
  wire [12:0] CNT_num;
  wire [15:0] \总周期数 ;
  wire [31:0] ALU_reslut, bit_extender_2_out, bit_extender_5_out, bit_extender_6_out,
       hardware_stack_1_data_out, I_offset, Mem_LH_reslut, Mem_reslut, multiplexer_1_out, multiplexer_2_out,
       multiplexer_3_out, multiplexer_8_out, multiplexer_9_out, pc_next_1_next_pc, rs1_data;
  wire [31:1] B_offset, J_offset;
  wire [31:31] bit_extender_3_out, bit_extender_4_out;

  Clock #(.highDuration(1), .lowDuration(1)) clock_1 ();  // open: out
  Button _1 ();  // open: out
  Button _2 ();  // open: out
  Button _3 ();  // open: out
  Button \u_继续运行  (.out(Go));
  LED #(.active("true")) led_1 (.in(W1));
  LED #(.active("true")) led_2 (.in(W2));
  LED #(.active("true")) led_3 (.in(W3));
  \中断  \u_中断_1  (.wait_uret(W1), .\与中断屏蔽位与 (\中断_1_与中断屏蔽位与 ), .\同步清零信号 (CLRA), .clk(CLK), .button(IRA));
  \中断  \u_中断_2  (.wait_uret(W2), .\与中断屏蔽位与 (\中断_2_与中断屏蔽位与 ), .\同步清零信号 (CLRB), .clk(CLK), .button(IRB));
  \中断  \u_中断_3  (.wait_uret(W3), .\与中断屏蔽位与 (\中断_3_与中断屏蔽位与 ), .\同步清零信号 (CLRC), .clk(CLK), .button(IRC));
  or or_1 (or_1_out, pop, CSRRSI);
  or or_2 (or_2_out, CSRRCI, and_3_out);
  Hex_Digit_Display hex_digit_display_1 (.value(LedData[31:28]));  // open: dp
  pc_next pc_next_1 (
    .pc(PC), .B_offset({B_offset, 1'b0}), .J_offset({J_offset, 1'b0}), .I_offset(I_offset),
    .next_pc(pc_next_1_next_pc), .rs1(rs1_data), .ALU_equal(ALU_equal), .Bne(Bne), .Beq(Beq), .JALR(JALR),
    .ALU_less(ALU_less), .JAL(JAL), .BLTU(BLTU));
  Multiplexer #(.select(2), .width(32), .disabled("Z"), .enable("false")) multiplexer_1 (
    .in0({32{1'b0}}), .in1(32'h30ac), .in2(32'h3158), .in3(32'h3204), .out(multiplexer_1_out), .sel(interrupt));
  Hex_Digit_Display hex_digit_display_2 (.value(LedData[27:24]));  // open: dp
  Hex_Digit_Display hex_digit_display_3 (.value(LedData[23:20]));  // open: dp
  // Probe on pc_next_1_next_pc
  Multiplexer #(.select(1), .width(32), .disabled("Z"), .enable("false")) multiplexer_2 (
    .in0(pc_next_1_next_pc), .in1(multiplexer_1_out), .out(multiplexer_2_out), .sel(Int));
  and and_1 (and_1_out, t_ff_1_q, or_1_out);
  or or_3 (or_3_out, and_1_out, and_2_out);
  and and_2 (and_2_out, or_2_out, t_ff_1_qn);
  Hex_Digit_Display hex_digit_display_4 (.value(LedData[15:12]));  // open: dp
  Hex_Digit_Display hex_digit_display_5 (.value(LedData[19:16]));  // open: dp
  hardware_stack hardware_stack_1 (
    .push(Int), .pop(pop), .data_in(pc_next_1_next_pc), .clk(CLK), .data_out(hardware_stack_1_data_out));
  Priority_Encoder #(.select(2), .disabled("Z")) priority_encoder_1 (
    .in0(1'b0), .in1(\中断_1_与中断屏蔽位与 ), .in2(\中断_2_与中断屏蔽位与 ), .in3(\中断_3_与中断屏蔽位与 ), .out(interrupt),
    .gs(priority_encoder_1_gs), .en_in(1'b1));  // open: en_out
  T_Flip_Flop #(.trigger("rising"), .Pre_Clr_Positions("ABOVE_BELOW"), .NegatePresetClear("false"), .enable("false"), .NewFFLayout("true")) t_ff_1 (
    .clk(CLK), .T(or_3_out), .Q(t_ff_1_q), .Qn(t_ff_1_qn));  // open: preset, reset
  Hex_Digit_Display hex_digit_display_6 (.value(LedData[7:4]));  // open: dp
  Hex_Digit_Display hex_digit_display_7 (.value(LedData[11:8]));  // open: dp
  // Probe on \总周期数 
  Multiplexer #(.select(1), .width(32), .disabled("Z"), .enable("false")) multiplexer_3 (
    .in0(multiplexer_2_out), .in1(hardware_stack_1_data_out), .out(multiplexer_3_out), .sel(pop));
  Demultiplexer #(.select(2), .width(1), .tristate("false"), .disabled(0), .enable("true")) demultiplexer_1 (
    .out1(CLRA), .out2(CLRB), .out3(CLRC), .in(Int), .sel(interrupt), .en(priority_encoder_1_gs));  // open: out0
  Multiplexer #(.select(1), .width(2), .disabled("Z"), .enable("false")) multiplexer_4 (
    .in0(interrupt), .in1(2'b00), .out(multiplexer_4_out), .sel(pop));
  Hex_Digit_Display hex_digit_display_8 (.value(LedData[3:0]));  // open: dp
  // Probe on multiplexer_3_out
  // Probe on multiplexer_3_out
  not not_1 (not_1_out, halt);
  and and_3 (and_3_out, priority_encoder_1_gs, t_ff_1_qn);
  Register #(.width(2), .trigger("rising"), .Select("low")) Interrut (
    .D(multiplexer_4_out), .en(or_4_out), .Q(Interrut_q), .clk(CLK));  // open: clr
  or or_4 (or_4_out, pop, Int);
  // Probe on PC
  // Probe on PC
  Register #(.width(32), .trigger("rising"), .Select("low")) u_PC (
    .D(multiplexer_3_out), .en(not_1_out), .Q(PC), .clk(CLK), .clr(RST));
  // Probe on interrupt
  Comparator #(.width(2), .mode("unsigned")) comparator_1 (
    .a(interrupt), .b(Interrut_q), .gt(comparator_1_gt));  // open: eq, lt
  // Probe on Interrut_q
  or or_5 (IR1_t, IR1, IRA);
  // Probe on PC[11:2]
  Multiplexer #(.select(1), .width(1), .disabled("Z"), .enable("false")) multiplexer_5 (
    .in0(1'b0), .in1(comparator_1_gt), .out(multiplexer_5_out), .sel(and_3_out));
  or or_6 (IR2_t, IR2, IRB);
  // RiscV_Probe riscv_probe_1: pin names not known; wires that end beside it: IR
  and and_4 (Int, and_3_out, multiplexer_5_out);
  ROM #(.addrWidth(10), .dataWidth(32), .Select("high")) rom_1 (.addr(PC[11:2]), .data(IR));
  // Probe on IR
  or or_7 (IR3_t, IR3, IRC);
  \单周期硬布线控制器  \u_单周期硬布线控制器_1  (
    .Funct({IR[30], IR[25], IR[14:12]}), .OP(IR[6:2]), .ALU_OP(AluOP), .MemToReg(MemToReg),
    .MemWrite(MemWrite), .ALU_SRC(AluSrcB), .RegWrite(RegWrite), .ecall(\单周期硬布线控制器_1_ecall ),
    .S_type(S_type), .Jalr(JALR), .Beq(Beq), .JAL(JAL), .Bne(Bne), .AUIPC(AUIPC), .BLTU(BLTU), .LH(LH),
    .LUI(LUI), .CSRRSI(CSRRSI), .CSRRCI(CSRRCI));
  Multiplexer #(.select(1), .width(5), .disabled("Z"), .enable("false")) multiplexer_6 (
    .in0(IR[19:15]), .in1(5'b10001), .out(multiplexer_6_out), .sel(ecall));
  Multiplexer #(.select(1), .width(5), .disabled("Z"), .enable("false")) multiplexer_7 (
    .in0(IR[24:20]), .in1(5'b01010), .out(multiplexer_7_out), .sel(ecall));
  assign I_offset = {{20{IR[31]}}, IR[31:20]};  // Bit_Extender bit_extender_1
  assign bit_extender_2_out = {{20{IR[31]}}, {IR[31:25], IR[11:7]}};  // Bit_Extender bit_extender_2
  assign {bit_extender_3_out[31], B_offset} = {{20{IR[31]}}, {IR[31], IR[7], IR[30:25], IR[11:8]}};  // Bit_Extender bit_extender_3
  assign {bit_extender_4_out[31], J_offset} = {{12{IR[31]}}, {IR[31], IR[19:12], IR[20], IR[30:21]}};  // Bit_Extender bit_extender_4
  not not_2 (not_2_out, pop);
  and and_5 (pop, IR[21], \单周期硬布线控制器_1_ecall );
  rd_in rd_in_1 (
    .ALU_result(ALU_reslut), .Mem_result(Mem_reslut), .MemToReg(MemToReg), .PC(PC), .JAL(JAL), .JALR(JALR),
    .RDin(RDin), .U_imm({IR[31:12], {12{1'b0}}}), .LUI(LUI), .AUIPC(AUIPC), .LH(LH),
    .Mem_LH_result(Mem_LH_reslut));
  and and_6 (ecall, \单周期硬布线控制器_1_ecall , not_2_out);
  // Probe on multiplexer_6_out
  // Probe on multiplexer_7_out
  // Probe on IR[11:7]
  // Probe on RDin
  // Probe on I_offset
  // Probe on bit_extender_2_out
  // Probe on {B_offset, 1'b0}
  // Probe on {J_offset, 1'b0}
  // Probe on {IR[31:12], {12{1'b0}}}
  Regifile regifile_1 (
    .Din(RDin), .Clk(CLK), .R1(rs1_data), .R2(MDin), .WE(RegWrite), .W_num(IR[11:7]),
    .R1_num(multiplexer_6_out), .R2_num(multiplexer_7_out));
  Multiplexer #(.select(1), .width(32), .disabled("Z"), .enable("false")) multiplexer_8 (
    .in0(MDin), .in1(I_offset), .out(multiplexer_8_out), .sel(AluSrcB));
  D_Flip_Flop #(.trigger("high"), .Pre_Clr_Positions("LEGACY"), .NegatePresetClear("false"), .enable("true"), .NewFFLayout("false")) d_ff_1 (.Q(d_ff_1_q));  // open: clk, D, Qn, preset, en, reset
  // Probe on 13'h6
  Multiplexer #(.select(1), .width(32), .disabled("Z"), .enable("false")) multiplexer_9 (
    .in0(multiplexer_8_out), .in1(bit_extender_2_out), .out(multiplexer_9_out), .sel(S_type));
  Comparator #(.width(13), .mode("twosComplement")) comparator_2 (
    .a(CNT_num), .b(13'h6), .eq(comparator_2_eq), .lt(comparator_2_lt));  // open: gt
  Clock #(.highDuration(1), .lowDuration(1)) clock_2 (.out(clock_2_out));
  // Probe on rs1_data
  // Probe on multiplexer_9_out
  Counter #(.width(13), .max('h1fff), .ongoal("stay"), .trigger("rising"), .behavior("old")) counter_1 (
    .count(comparator_2_lt), .Q(CNT_num), .clk(clock_2_out));  // open: load, D, carry, clr, preset
  nand nand_1 (nand_1_out, d_ff_1_q, comparator_2_eq);
  ALU alu_1 (
    .X(rs1_data), .Y(multiplexer_9_out), .AluOP(AluOP), .Equal(ALU_equal), .Result(ALU_reslut),
    .out_4(ALU_more_equal), .out_6(ALU_less));  // open: Result_2
  assign CLK = nand_1_out ? clock_2_out : 1'bz;  // Controlled_Buffer controlled_buffer_1
  Pull_Resistor #(.pull(1)) pull_resistor_1 (.node(CLK));
  // Probe on ALU_reslut
  Comparator #(.width(16), .mode("twosComplement")) comparator_3 (
    .a(16'h258), .b(\总周期数 ), .eq(comparator_3_eq));  // open: gt, lt
  Comparator #(.width(16), .mode("twosComplement")) comparator_4 (
    .a(\总周期数 ), .b(16'h1), .eq(comparator_4_eq));  // open: gt, lt
  Comparator #(.width(16), .mode("twosComplement")) comparator_5 (
    .a(\总周期数 ), .b(16'h4), .eq(comparator_5_eq));  // open: gt, lt
  Comparator #(.width(16), .mode("twosComplement")) comparator_6 (
    .a(\总周期数 ), .b(16'h7), .eq(comparator_6_eq));  // open: gt, lt
  Comparator #(.width(16), .mode("twosComplement")) comparator_7 (
    .a(\总周期数 ), .b(16'h241), .eq(comparator_7_eq));  // open: gt, lt
  or or_8 (or_8_out, MemWrite, MemToReg);
  or or_9 (or_9_out, comparator_3_eq, comparator_4_eq);
  assign IRA = or_9_out ? ~CLK : 1'bz;  // Controlled_Inverter controlled_inverter_1
  assign IRB = comparator_5_eq ? ~CLK : 1'bz;  // Controlled_Inverter controlled_inverter_2
  or or_10 (or_10_out, comparator_6_eq, comparator_7_eq);
  assign IRC = or_10_out ? ~CLK : 1'bz;  // Controlled_Inverter controlled_inverter_3
  RAM #(.addrWidth(10), .dataWidth(32), .bus("separate"), .Select("high")) ram_1 (
    .addr(ALU_reslut[11:2]), .din(MDin), .data(Mem_reslut), .str(MemWrite), .sel(or_8_out), .clk(CLK),
    .ld(MemToReg), .clr(RST));
  Pull_Resistor #(.pull(0)) pull_resistor_2 (.node(IRA));
  Pull_Resistor #(.pull(0)) pull_resistor_3 (.node(IRB));
  Pull_Resistor #(.pull(0)) pull_resistor_4 (.node(IRC));
  not not_3 (not_3_out, halt);
  Counter #(.width(16), .max('hffff), .ongoal("wrap"), .trigger("rising"), .behavior("new")) counter_2 (
    .D(16'h1), .count(not_3_out), .Q(\总周期数 ), .clk(CLK), .clr(RST));  // open: load, carry, preset, down
  assign bit_extender_5_out = {{16{Mem_reslut[15]}}, Mem_reslut[15:0]};  // Bit_Extender bit_extender_5
  assign bit_extender_6_out = {{16{Mem_reslut[31]}}, Mem_reslut[31:16]};  // Bit_Extender bit_extender_6
  ecall_deal ecall_deal_1 (
    .ecall(ecall), .a0(MDin), .clk(CLK), .go(Go), .LedData(LedData), .halt(halt), .rs1_data(rs1_data));
  Button \u_复位  (.out(RST));
  Multiplexer #(.select(2), .width(32), .disabled("Z"), .enable("false")) multiplexer_10 (
    .in0(bit_extender_5_out), .in1({32{1'b0}}), .in2(bit_extender_6_out), .in3({32{1'b0}}),
    .out(Mem_LH_reslut), .sel(ALU_reslut[1:0]));

  // Other names for the same wires on the sheet: push = Int; rs2_data[31:0] = MDin; U_RDin[31:12] = IR[31:12];
  //   uret = pop

  // Notes on the sheet:
  //   中断源
  //   中断等待指示
  //   总复位信号应将除ROM以外所有存储组件全部清零
  //   数码管输出
  //   数码管输出应该用寄存器锁存，否则显示数据只能一闪而过
  //   指令存储器
  //   指令字
  //   contents of rom_1 (hex, n*v repeats v):
  //   7d000113 100413 1f41993 41f9d993 433 c00913 800b13 140413 f47413 800293 100313 499993 89e9b3 1300533
  //   2200893 73 406282b3 fe0294e3 140413 f00f93 1f47433 1c41413 800293 100313 49d993 89e9b3 1300533
  //   2200893 73 406282b3 fe0294e3 1c45413 406b0b33 b0463 f95ff06f 2b3 fff2c293 1029293 fff2e293 500533
  //   2200893 73 f5dff06f 1112023 410113 a12023 410113 812023 410113 1312023 410113 1412023 410113 1512023
  //   410113 1612023 410113 40e073 100b13 300a13 100a93 1600433 441413 14469b3 1300533 2200893 73 fe0416e3
  //   415a0a33 fe0a10e3 40f073 ffc10113 12b03 ffc10113 12a83 ffc10113 12a03 ffc10113 12983 ffc10113 12403
  //   ffc10113 12503 ffc10113 12883 200073 1112023 410113 a12023 410113 812023 410113 1312023 410113
  //   1412023 410113 1512023 410113 1612023 410113 40e073 200b13 300a13 100a93 1600433 441413 14469b3
  //   1300533 2200893 73 fe0416e3 415a0a33 fe0a10e3 40f073 ffc10113 12b03 ffc10113 12a83 ffc10113 12a03
  //   ffc10113 12983 ffc10113 12403 ffc10113 12503 ffc10113 12883 200073 1112023 410113 a12023 410113
  //   812023 410113 1312023 410113 1412023 410113 1512023 410113 1612023 410113 40e073 300b13 300a13
  //   100a93 1600433 441413 14469b3 1300533 2200893 73 fe0416e3 415a0a33 fe0a10e3 40f073 ffc10113 12b03
  //   ffc10113 12a83 ffc10113 12a03 ffc10113 12983 ffc10113 12403 ffc10113 12503 ffc10113 12883 200073
  //   rd
  //   JAL
  //   JALR
  //   opcode
  //   funct
  //   ecall
  //   rs1
  //   rs2
  //   I:imm
  //   S:imm
  //   B:imm
  //   J:imm
  //   U:imm
  //   Beq
  //   Bne
  //   MemToReg
  //   MemWrite
  //   AluOP
  //   AluSrcB
  //   RegWrite
  //   S_type
  //   为方便自动评测，需要输出PC，IR，寄存器堆写如数据RDin
  //   RAM写使能MemWrite、RAM写入数据MDin等信号
  //   控制位
  //   暂停节拍，不能为0
  //   可计数暂停的时钟源
  //   多级中断测试信号模拟器
  //   数据存储器
  //   ecall 信号处理
  //   周期计数
endmodule

module \流水线单级中断  (
  output RegWrite,
  output MemWrite,
  output [31:0] IF_PC,
  output [31:0] ID_PC,
  output [31:0] EX_PC,
  output [31:0] M_PC,
  output [31:0] WB_PC,
  output [31:0] RDin,
  output [31:0] MDin,
  output [31:0] LedData
);

  wire and_1_out, and_2_out, and_6_out, and_7_out, and_8_out, and_10_out, and_11_out, and_12_out, and_13_out,
       BranchTaken, CLK, clock_1_out, clock_2_out, CLRA, CLRB, CLRC, comparator_1_eq, comparator_2_eq,
       comparator_3_eq, comparator_4_eq, comparator_5_eq, comparator_5_lt, d_ff_1_q, ecall_deal_1_halt,
       EX_AUIPC, EX_Beq, EX_Bltu, EX_Bne, EX_ecall, EX_eq, EX_JAL, EX_JALR, EX_less, EX_LUI, ex_mem_1_p16,
       ex_mem_1_p18, ex_mem_1_p19, ex_mem_1_p25, EX_SrcB, Go, halt, id_ex_1_lhout, id_ex_1_memtoregout,
       id_ex_1_memwriteout, id_ex_1_regwriteout, Int, IRA, IRB, IRC, mem_we_1_haltout, mem_we_1_memtoregout,
       nand_1_out, not_1_out, not_2_out, not_3_out, not_4_out, not_5_out, not_6_out, not_7_out, or_1_out,
       or_2_out, or_3_out, or_4_out, or_5_out, or_7_out, or_8_out, or_9_out, or_10_out, pause,
       priority_encoder_1_gs, pull_resistor_1_node, pull_resistor_2_node, pull_resistor_3_node, RST,
       t_ff_1_q, t_ff_1_qn, uret, W1, W2, W3, \中断_1_与中断屏蔽位与 , \中断_2_与中断屏蔽位与 , \中断_3_与中断屏蔽位与 ,
       \单周期硬布线控制器_1_alu_src , \单周期硬布线控制器_1_auipc , \单周期硬布线控制器_1_beq , \单周期硬布线控制器_1_bltu , \单周期硬布线控制器_1_bne ,
       \单周期硬布线控制器_1_ecall , \单周期硬布线控制器_1_jal , \单周期硬布线控制器_1_jalr , \单周期硬布线控制器_1_lh , \单周期硬布线控制器_1_lui ,
       \单周期硬布线控制器_1_memtoreg , \单周期硬布线控制器_1_memwrite , \单周期硬布线控制器_1_regwrite , \单周期硬布线控制器_1_s_type ,
       \相关逻辑处理_重定向_1_id_ex_clr , \相关逻辑处理_重定向_1_if_id_clr , \相关逻辑处理_重定向_1_stall ;
  wire [1:0] id_ex_1_rs1_f_out, id_ex_1_rs2_f_out, interrupt, \相关逻辑处理_重定向_1_rs1_forward ,
       \相关逻辑处理_重定向_1_rs2_forward ;
  wire [3:0] EX_AluOP, \单周期硬布线控制器_1_alu_op ;
  wire [4:0] ex_mem_1_p22, id_ex_1_rdout, mem_we_1_rdout, multiplexer_5_out, multiplexer_6_out,
       multiplexer_8_out;
  wire [12:0] CNT_num;
  wire [15:0] \LoadUse次数 , \总周期数 , \无条件分支数 , \条件分支成功数 ;
  wire [31:0] adder_2_out, adder_3_out, adder_4_out, adder_5_out, and_9_out, bit_extender_1_out,
       bit_extender_2_out, bit_extender_3_out, bit_extender_4_out, bit_extender_5_out, bit_extender_6_out,
       EX_ALUData, EX_IR, id_ex_1_immout, id_ex_1_rs1out, id_ex_1_rs2out, ID_IR, IF_IR, MEM_ALUData, MEM_IR,
       mem_we_1_alu_resultout, mem_we_1_mem_resultout, multiplexer_1_out, multiplexer_2_out,
       multiplexer_3_out, multiplexer_4_out, multiplexer_7_out, multiplexer_9_out, multiplexer_10_out,
       multiplexer_11_out, multiplexer_12_out, multiplexer_13_out, multiplexer_14_out, multiplexer_15_out,
       multiplexer_16_out, multiplexer_17_out, multiplexer_18_out, multiplexer_19_out, multiplexer_20_out,
       pc_4, ram_1_data, regifile_1_r1, regifile_1_r2, register_1_q, WB_IR;

  Button \u_总复位  (.out(RST));
  Button _1 (.out(IRA));
  Button _2 (.out(IRB));
  Button _3 (.out(IRC));
  // Probe on \总周期数 
  // Probe on \总周期数 
  Button \u_继续运行  (.out(Go));
  LED #(.active("true")) led_1 (.in(W1));
  LED #(.active("true")) led_2 (.in(W2));
  LED #(.active("true")) led_3 (.in(W3));
  Multiplexer #(.select(1), .width(32), .disabled("Z"), .enable("false")) multiplexer_1 (
    .in0(pc_4), .in1(multiplexer_15_out), .out(multiplexer_1_out), .sel(BranchTaken));
  Hex_Digit_Display hex_digit_display_1 (.value(LedData[31:28]));  // open: dp
  // Probe on IF_PC[19:0]
  // RiscV_Probe riscv_probe_1: pin names not known; wires that end beside it: IF_IR
  Multiplexer #(.select(1), .width(32), .disabled("Z"), .enable("false")) multiplexer_2 (
    .in0(multiplexer_1_out), .in1(multiplexer_3_out), .out(multiplexer_2_out), .sel(Int));
  Multiplexer #(.select(2), .width(32), .disabled("Z"), .enable("false")) multiplexer_3 (
    .in0({32{1'b0}}), .in1(32'h30ac), .in2(32'h3150), .in3(32'h31f4), .out(multiplexer_3_out), .sel(interrupt));
  \中断  \u_中断_1  (.wait_uret(W1), .\与中断屏蔽位与 (\中断_1_与中断屏蔽位与 ), .\同步清零信号 (CLRA), .clk(CLK), .button(IRA));
  \中断  \u_中断_2  (.wait_uret(W2), .\与中断屏蔽位与 (\中断_2_与中断屏蔽位与 ), .\同步清零信号 (CLRB), .clk(CLK), .button(IRB));
  \中断  \u_中断_3  (.wait_uret(W3), .\与中断屏蔽位与 (\中断_3_与中断屏蔽位与 ), .\同步清零信号 (CLRC), .clk(CLK), .button(IRC));
  Hex_Digit_Display hex_digit_display_2 (.value(LedData[23:20]));  // open: dp
  Hex_Digit_Display hex_digit_display_3 (.value(LedData[27:24]));  // open: dp
  // Probe on ID_PC[19:0]
  // RiscV_Probe riscv_probe_2: pin names not known; wires that end beside it: ID_IR
  Register #(.width(32), .trigger("rising"), .Select("low")) register_1 (
    .D(multiplexer_1_out), .en(Int), .Q(register_1_q), .clk(CLK));  // open: clr
  Comparator #(.width(16), .mode("twosComplement")) comparator_1 (
    .a(16'h23b), .b(\总周期数 ), .eq(comparator_1_eq));  // open: gt, lt
  Comparator #(.width(16), .mode("twosComplement")) comparator_2 (
    .a(\总周期数 ), .b(16'h1), .eq(comparator_2_eq));  // open: gt, lt
  Comparator #(.width(16), .mode("twosComplement")) comparator_3 (
    .a(\总周期数 ), .b(16'h4), .eq(comparator_3_eq));  // open: gt, lt
  Comparator #(.width(16), .mode("twosComplement")) comparator_4 (
    .a(\总周期数 ), .b(16'h7), .eq(comparator_4_eq));  // open: gt, lt
  Hex_Digit_Display hex_digit_display_4 (.value(LedData[15:12]));  // open: dp
  Hex_Digit_Display hex_digit_display_5 (.value(LedData[19:16]));  // open: dp
  Multiplexer #(.select(1), .width(32), .disabled("Z"), .enable("false")) multiplexer_4 (
    .in0(multiplexer_2_out), .in1(register_1_q), .out(multiplexer_4_out), .sel(uret));
  Priority_Encoder #(.select(2), .disabled("Z")) priority_encoder_1 (
    .in0(1'b0), .in1(\中断_1_与中断屏蔽位与 ), .in2(\中断_2_与中断屏蔽位与 ), .in3(\中断_3_与中断屏蔽位与 ), .out(interrupt),
    .gs(priority_encoder_1_gs), .en_in(1'b1));  // open: en_out
  or or_1 (or_1_out, comparator_1_eq, comparator_2_eq);
  Pull_Resistor #(.pull(0)) pull_resistor_1 (.node(pull_resistor_1_node));
  assign pull_resistor_1_node = or_1_out ? ~CLK : 1'bz;  // Controlled_Inverter controlled_inverter_1
  Pull_Resistor #(.pull(0)) pull_resistor_2 (.node(pull_resistor_2_node));
  assign pull_resistor_2_node = comparator_3_eq ? ~CLK : 1'bz;  // Controlled_Inverter controlled_inverter_2
  Pull_Resistor #(.pull(0)) pull_resistor_3 (.node(pull_resistor_3_node));
  assign pull_resistor_3_node = comparator_4_eq ? ~CLK : 1'bz;  // Controlled_Inverter controlled_inverter_3
  Hex_Digit_Display hex_digit_display_6 (.value(LedData[7:4]));  // open: dp
  Hex_Digit_Display hex_digit_display_7 (.value(LedData[11:8]));  // open: dp
  Clock #(.highDuration(1), .lowDuration(1)) clock_1 (.out(clock_1_out));
  // Probe on EX_PC[19:0]
  // RiscV_Probe riscv_probe_3: pin names not known; wires that end beside it: clock_1_out, EX_IR, CLK
  not not_1 (not_1_out, halt);
  Demultiplexer #(.select(2), .width(1), .tristate("false"), .disabled(0), .enable("true")) demultiplexer_1 (
    .out1(CLRA), .out2(CLRB), .out3(CLRC), .in(Int), .sel(interrupt), .en(priority_encoder_1_gs));  // open: out0
  and and_1 (and_1_out, t_ff_1_qn, Int);
  and and_2 (and_2_out, uret, t_ff_1_q);
  Hex_Digit_Display hex_digit_display_8 (.value(LedData[3:0]));  // open: dp
  and and_3 (pause, not_2_out, not_1_out);
  Register #(.width(32), .trigger("rising"), .Select("low")) PC (
    .D(multiplexer_4_out), .en(pause), .Q(IF_PC), .clk(CLK), .clr(RST));
  or or_2 (or_2_out, and_1_out, and_2_out);
  // Probe on \总周期数 
  // Probe on M_PC[19:0]
  // RiscV_Probe riscv_probe_4: pin names not known; wires that end beside it: MEM_IR
  T_Flip_Flop #(.trigger("rising"), .Pre_Clr_Positions("ABOVE_BELOW"), .NegatePresetClear("false"), .enable("false"), .NewFFLayout("true")) t_ff_1 (
    .clk(CLK), .T(or_2_out), .Q(t_ff_1_q), .Qn(t_ff_1_qn));  // open: preset, reset
  // Probe on \总周期数 
  // Probe on \无条件分支数 
  // Probe on \条件分支成功数 
  // Probe on \LoadUse次数 
  // Probe on \LoadUse次数 
  Adder #(.width(32)) adder_1 (.a(IF_PC), .b(32'h4), .out(pc_4));  // open: cin, cout
  and and_4 (Int, priority_encoder_1_gs, t_ff_1_qn);
  // Probe on IF_PC[11:0]
  // Probe on WB_PC[19:0]
  // RiscV_Probe riscv_probe_5: pin names not known; wires that end beside it: WB_IR
  not not_2 (not_2_out, \相关逻辑处理_重定向_1_stall );
  // RiscV_Probe riscv_probe_6: pin names not known; wires that end beside it: IF_IR
  ROM #(.addrWidth(10), .dataWidth(32), .Select("high")) \u_指令存储器  (.addr(IF_PC[11:2]), .data(IF_IR));
  // Probe on ID_PC[11:0]
  // Probe on EX_PC[11:0]
  IF_ID if_id_1 (
    .IRin(IF_IR), .PCin(IF_PC), .CLK(CLK), .RST(\相关逻辑处理_重定向_1_if_id_clr ), .halt(halt), .IRout(ID_IR),
    .PCout(ID_PC), .en(not_2_out));
  // Probe on M_PC[11:0]
  D_Flip_Flop #(.trigger("high"), .Pre_Clr_Positions("LEGACY"), .NegatePresetClear("false"), .enable("true"), .NewFFLayout("false")) d_ff_1 (.Q(d_ff_1_q));  // open: clk, D, Qn, preset, en, reset
  // Probe on 13'h340
  and and_5 (uret, ID_IR[21], \单周期硬布线控制器_1_ecall );
  // Probe on WB_PC[11:0]
  Comparator #(.width(13), .mode("twosComplement")) comparator_5 (
    .a(CNT_num), .b(13'h340), .eq(comparator_5_eq), .lt(comparator_5_lt));  // open: gt
  Clock #(.highDuration(1), .lowDuration(1)) clock_2 (.out(clock_2_out));
  \单周期硬布线控制器  \u_单周期硬布线控制器_1  (
    .Funct({ID_IR[30], ID_IR[25], ID_IR[14:12]}), .OP(ID_IR[6:2]), .ALU_OP(\单周期硬布线控制器_1_alu_op ),
    .MemToReg(\单周期硬布线控制器_1_memtoreg ), .MemWrite(\单周期硬布线控制器_1_memwrite ), .ALU_SRC(\单周期硬布线控制器_1_alu_src ),
    .RegWrite(\单周期硬布线控制器_1_regwrite ), .ecall(\单周期硬布线控制器_1_ecall ), .S_type(\单周期硬布线控制器_1_s_type ),
    .Jalr(\单周期硬布线控制器_1_jalr ), .Beq(\单周期硬布线控制器_1_beq ), .JAL(\单周期硬布线控制器_1_jal ), .Bne(\单周期硬布线控制器_1_bne ),
    .AUIPC(\单周期硬布线控制器_1_auipc ), .BLTU(\单周期硬布线控制器_1_bltu ), .LH(\单周期硬布线控制器_1_lh ), .LUI(\单周期硬布线控制器_1_lui ));  // open: CSRRSI, CSRRCI
  and and_6 (and_6_out, \单周期硬布线控制器_1_ecall , not_3_out);
  not not_3 (not_3_out, uret);
  Multiplexer #(.select(1), .width(5), .disabled("Z"), .enable("false")) multiplexer_5 (
    .in0(ID_IR[19:15]), .in1(5'b10001), .out(multiplexer_5_out), .sel(and_6_out));
  Multiplexer #(.select(1), .width(5), .disabled("Z"), .enable("false")) multiplexer_6 (
    .in0(ID_IR[24:20]), .in1(5'b01010), .out(multiplexer_6_out), .sel(and_6_out));
  nand nand_1 (nand_1_out, d_ff_1_q, comparator_5_eq);
  Counter #(.width(13), .max('h1fff), .ongoal("stay"), .trigger("rising"), .behavior("old")) counter_1 (
    .count(comparator_5_lt), .Q(CNT_num), .clk(clock_2_out));  // open: load, D, carry, clr, preset
  assign bit_extender_1_out = {{20{ID_IR[31]}}, ID_IR[31:20]};  // Bit_Extender bit_extender_1
  assign bit_extender_2_out = {{20{ID_IR[31]}}, {ID_IR[31:25], ID_IR[11:7]}};  // Bit_Extender bit_extender_2
  assign bit_extender_3_out = {{20{ID_IR[31]}}, {ID_IR[31], ID_IR[7], ID_IR[30:25], ID_IR[11:8]}};  // Bit_Extender bit_extender_3
  assign bit_extender_4_out = {{12{ID_IR[31]}}, {ID_IR[31], ID_IR[19:12], ID_IR[20], ID_IR[30:21]}};  // Bit_Extender bit_extender_4
  assign CLK = nand_1_out ? clock_2_out : 1'bz;  // Controlled_Buffer controlled_buffer_1
  Multiplexer #(.select(1), .width(32), .disabled("Z"), .enable("false")) multiplexer_7 (
    .in0(bit_extender_1_out), .in1(bit_extender_2_out), .out(multiplexer_7_out), .sel(\单周期硬布线控制器_1_s_type ));
  Pull_Resistor #(.pull(1)) pull_resistor_4 (.node(CLK));
  // Probe on multiplexer_5_out
  // Probe on multiplexer_8_out
  Multiplexer #(.select(1), .width(5), .disabled("Z"), .enable("false")) multiplexer_8 (
    .in0(multiplexer_6_out), .in1({5{1'b0}}), .out(multiplexer_8_out), .sel(and_7_out));
  and and_7 (and_7_out, not_4_out, or_4_out);
  // Probe on RDin
  or or_3 (or_3_out, \单周期硬布线控制器_1_beq , \单周期硬布线控制器_1_bne , \单周期硬布线控制器_1_bltu );
  not not_4 (not_4_out, \单周期硬布线控制器_1_s_type );
  or or_4 (or_4_out, \单周期硬布线控制器_1_lui , \单周期硬布线控制器_1_auipc , \单周期硬布线控制器_1_jalr , \单周期硬布线控制器_1_jal , \单周期硬布线控制器_1_alu_src );
  // Probe on multiplexer_5_out
  // Probe on multiplexer_6_out
  // Probe on mem_we_1_rdout
  Multiplexer #(.select(1), .width(32), .disabled("Z"), .enable("false")) multiplexer_9 (
    .in0(multiplexer_7_out), .in1({bit_extender_3_out[30:0], 1'b0}), .out(multiplexer_9_out), .sel(or_3_out));
  Multiplexer #(.select(1), .width(32), .disabled("Z"), .enable("false")) multiplexer_10 (
    .in0(multiplexer_9_out), .in1({bit_extender_4_out[30:0], 1'b0}), .out(multiplexer_10_out),
    .sel(\单周期硬布线控制器_1_jal ));
  not not_5 (not_5_out, halt);
  Counter #(.width(16), .max('hffff), .ongoal("wrap"), .trigger("rising"), .behavior("new")) counter_2 (
    .D(16'h1), .count(not_5_out), .Q(\总周期数 ), .clk(CLK), .clr(RST));  // open: load, carry, preset, down
  Regifile regifile_1 (
    .Din(RDin), .Clk(CLK), .R1(regifile_1_r1), .R2(regifile_1_r2), .WE(RegWrite), .W_num(mem_we_1_rdout),
    .R1_num(multiplexer_5_out), .R2_num(multiplexer_6_out));
  or or_5 (or_5_out, \单周期硬布线控制器_1_lui , \单周期硬布线控制器_1_auipc );
  Multiplexer #(.select(1), .width(32), .disabled("Z"), .enable("false")) multiplexer_11 (
    .in0(multiplexer_10_out), .in1({ID_IR[31:12], {12{1'b0}}}), .out(multiplexer_11_out), .sel(or_5_out));
  // Probe on \相关逻辑处理_重定向_1_rs2_forward 
  // Probe on \相关逻辑处理_重定向_1_rs1_forward 
  // Probe on regifile_1_r1
  // Probe on regifile_1_r2
  // Probe on multiplexer_11_out
  // Probe on ID_IR[11:7]
  // Probe on ID_PC
  // RiscV_Probe riscv_probe_7: pin names not known
  ID_EX id_ex_1 (
    .JALin(\单周期硬布线控制器_1_jal ), .JALRin(\单周期硬布线控制器_1_jalr ), .Beqin(\单周期硬布线控制器_1_beq ),
    .AUIPCin(\单周期硬布线控制器_1_auipc ), .Bnein(\单周期硬布线控制器_1_bne ), .LUIin(\单周期硬布线控制器_1_lui ),
    .MemToRegin(\单周期硬布线控制器_1_memtoreg ), .LHin(\单周期硬布线控制器_1_lh ), .MemWritein(\单周期硬布线控制器_1_memwrite ),
    .RS1(regifile_1_r1), .BLTUin(\单周期硬布线控制器_1_bltu ), .AluOPin(\单周期硬布线控制器_1_alu_op ), .RS2(regifile_1_r2),
    .AluSrcBin(\单周期硬布线控制器_1_alu_src ), .RD(ID_IR[11:7]), .RegWrite(\单周期硬布线控制器_1_regwrite ),
    .imm(multiplexer_11_out), .CLK(CLK), .RST(\相关逻辑处理_重定向_1_id_ex_clr ), .halt(halt), .JALout(EX_JAL),
    .JALRout(EX_JALR), .Beqout(EX_Beq), .ALUIPCout(EX_AUIPC), .Bneout(EX_Bne), .LUIout(EX_LUI),
    .MemToRegout(id_ex_1_memtoregout), .LHout(id_ex_1_lhout), .MemWriteout(id_ex_1_memwriteout),
    .RS1out(id_ex_1_rs1out), .BLTUout(EX_Bltu), .AluOPout(EX_AluOP), .RS2out(id_ex_1_rs2out),
    .AluSrcBout(EX_SrcB), .RDout(id_ex_1_rdout), .RegWriteout(id_ex_1_regwriteout), .Immout(id_ex_1_immout),
    .PC(ID_PC), .PCout(EX_PC), .Ecallin(and_6_out), .Ecallout(EX_ecall), .IRin(ID_IR), .IRout(EX_IR),
    .RS1_f_in(\相关逻辑处理_重定向_1_rs1_forward ), .RS1_f_out(id_ex_1_rs1_f_out),
    .RS2_f_in(\相关逻辑处理_重定向_1_rs2_forward ), .RS2_f_out(id_ex_1_rs2_f_out));  // open: URETin, CSRRSIin, CSRRCIin, S_typein, URETout, CSRRSIout, CSRRCIout, S_typeout
  or or_6 (BranchTaken, and_11_out, EX_JALR, EX_JAL, and_10_out, and_8_out);
  // Probe on MEM_ALUData
  Adder #(.width(32)) adder_2 (.a(multiplexer_12_out), .b(id_ex_1_immout), .out(adder_2_out));  // open: cin, cout
  and and_8 (and_8_out, EX_eq, EX_Beq);
  // Probe on id_ex_1_rs1_f_out
  Multiplexer #(.select(2), .width(32), .disabled("Z"), .enable("false")) multiplexer_12 (
    .in0(id_ex_1_rs1out), .in1(RDin), .in2(MEM_ALUData), .in3(id_ex_1_rs1out), .out(multiplexer_12_out),
    .sel(id_ex_1_rs1_f_out));
  // Probe on id_ex_1_rs2_f_out
  Multiplexer #(.select(2), .width(32), .disabled("Z"), .enable("false")) multiplexer_13 (
    .in0(id_ex_1_rs2out), .in1(RDin), .in2(MEM_ALUData), .in3(id_ex_1_rs2out), .out(multiplexer_13_out),
    .sel(id_ex_1_rs2_f_out));
  or or_7 (or_7_out, EX_JAL, EX_JALR);
  Adder #(.width(32)) adder_3 (.a(EX_PC), .b(id_ex_1_immout), .out(adder_3_out));  // open: cin, cout
  Multiplexer #(.select(1), .width(32), .disabled("Z"), .enable("false")) multiplexer_14 (
    .in0(EX_ALUData), .in1(adder_4_out), .out(multiplexer_14_out), .sel(or_7_out));
  Adder #(.width(32)) adder_4 (.a(32'h4), .b(EX_PC), .out(adder_4_out));  // open: cin, cout
  Adder #(.width(32)) adder_5 (.a(id_ex_1_immout), .b(EX_PC), .out(adder_5_out));  // open: cin, cout
  assign and_9_out = adder_2_out & 32'hfffffffe;  // AND_Gate and_9, 32 bits wide
  and and_10 (and_10_out, not_6_out, EX_Bne);
  not not_6 (not_6_out, EX_eq);
  // Probe on RDin
  // Probe on multiplexer_13_out
  Multiplexer #(.select(1), .width(32), .disabled("Z"), .enable("false")) multiplexer_15 (
    .in0(adder_5_out), .in1(and_9_out), .out(multiplexer_15_out), .sel(EX_JALR));
  // Probe on multiplexer_15_out
  and and_11 (and_11_out, EX_Bltu, EX_less);
  Multiplexer #(.select(1), .width(32), .disabled("Z"), .enable("false")) multiplexer_16 (
    .in0(multiplexer_13_out), .in1(id_ex_1_immout), .out(multiplexer_16_out), .sel(EX_SrcB));
  Multiplexer #(.select(1), .width(32), .disabled("Z"), .enable("false")) multiplexer_17 (
    .in0(multiplexer_14_out), .in1(adder_3_out), .out(multiplexer_17_out), .sel(EX_AUIPC));
  // Probe on multiplexer_12_out
  // Probe on multiplexer_16_out
  Multiplexer #(.select(1), .width(32), .disabled("Z"), .enable("false")) multiplexer_18 (
    .in0(multiplexer_17_out), .in1(id_ex_1_immout), .out(multiplexer_18_out), .sel(EX_LUI));
  ALU alu_1 (
    .X(multiplexer_12_out), .Y(multiplexer_16_out), .AluOP(EX_AluOP), .Equal(EX_eq), .Result(EX_ALUData),
    .out_6(EX_less));  // open: Result_2, out_4
  // Probe on multiplexer_18_out
  // Probe on id_ex_1_rdout
  // RiscV_Probe riscv_probe_8: pin names not known
  or or_8 (or_8_out, EX_JAL, EX_JALR);
  Counter #(.width(16), .max('hffff), .ongoal("wrap"), .trigger("rising"), .behavior("new")) counter_3 (
    .D(16'h1), .count(or_8_out), .Q(\无条件分支数 ), .clk(CLK));  // open: load, carry, clr, preset, down
  ecall_deal ecall_deal_1 (
    .ecall(EX_ecall), .a0(multiplexer_13_out), .clk(CLK), .go(1'b0), .LedData(LedData),
    .halt(ecall_deal_1_halt), .rs1_data(multiplexer_12_out));
  // EX_MEM ex_mem_1: pin names not known; wires that end beside it: EX_eq, EX_less, id_ex_1_memtoregout, id_ex_1_memwriteout, id_ex_1_regwriteout, id_ex_1_lhout, multiplexer_18_out, multiplexer_13_out, id_ex_1_rdout, EX_PC, EX_IR, ecall_deal_1_halt, RST, CLK, halt, ex_mem_1_p16, MemWrite, ex_mem_1_p18, ex_mem_1_p19, MEM_ALUData, MDin, ex_mem_1_p22, M_PC, MEM_IR, ex_mem_1_p25
  or or_9 (or_9_out, EX_Beq, EX_Bne, EX_Bltu);
  // Probe on MDin
  // RiscV_Probe riscv_probe_9: pin names not known; wires that end beside it: multiplexer_18_out
  and and_12 (and_12_out, or_9_out, BranchTaken);
  Counter #(.width(16), .max('hffff), .ongoal("wrap"), .trigger("rising"), .behavior("new")) counter_4 (
    .D(16'h1), .count(and_12_out), .Q(\条件分支成功数 ), .clk(CLK));  // open: load, carry, clr, preset, down
  // Probe on ex_mem_1_p22
  // Probe on ex_mem_1_p22
  or or_10 (or_10_out, MemWrite, ex_mem_1_p16);
  // Probe on MEM_ALUData
  RAM #(.addrWidth(10), .dataWidth(32), .bus("separate"), .Select("high")) ram_1 (
    .addr(MEM_ALUData[11:2]), .din(MDin), .data(ram_1_data), .str(MemWrite), .sel(or_10_out), .clk(CLK),
    .ld(ex_mem_1_p16), .clr(RST));
  \相关逻辑处理_重定向  \u_相关逻辑处理_重定向_1  (
    .rs1(multiplexer_5_out), .rs2(multiplexer_8_out), .EX_WriteReg(id_ex_1_rdout),
    .EX_MemToReg(id_ex_1_memtoregout), .EX_RegWrite(id_ex_1_regwriteout), .MEM_WriteReg(ex_mem_1_p22),
    .MEM_RegWrite(ex_mem_1_p18), .BranchTaken(BranchTaken), .stall(\相关逻辑处理_重定向_1_stall ),
    .IF_ID_CLR(\相关逻辑处理_重定向_1_if_id_clr ), .ID_EX_CLR(\相关逻辑处理_重定向_1_id_ex_clr ),
    .RS1_Forward(\相关逻辑处理_重定向_1_rs1_forward ), .RS2_Forward(\相关逻辑处理_重定向_1_rs2_forward ));  // open: PC_EN, LoadUse
  assign bit_extender_5_out = {{16{ram_1_data[15]}}, ram_1_data[15:0]};  // Bit_Extender bit_extender_5
  assign bit_extender_6_out = {{16{ram_1_data[31]}}, ram_1_data[31:16]};  // Bit_Extender bit_extender_6
  Counter #(.width(16), .max('hffff), .ongoal("wrap"), .trigger("rising"), .behavior("new")) counter_5 (
    .D(16'h1), .Q(\LoadUse次数 ), .clk(CLK));  // open: load, count, carry, clr, preset, down
  Multiplexer #(.select(2), .width(32), .disabled("Z"), .enable("false")) multiplexer_19 (
    .in0(bit_extender_5_out), .in1({32{1'b0}}), .in2(bit_extender_6_out), .in3({32{1'b0}}),
    .out(multiplexer_19_out), .sel(MEM_ALUData[1:0]));
  // Probe on MEM_ALUData
  Multiplexer #(.select(1), .width(32), .disabled("Z"), .enable("false")) multiplexer_20 (
    .in0(ram_1_data), .in1(multiplexer_19_out), .out(multiplexer_20_out), .sel(ex_mem_1_p19));
  // Probe on multiplexer_20_out
  MEM_WE mem_we_1 (
    .MemToRegin(ex_mem_1_p16), .ALU_Result(MEM_ALUData), .Mem_Result(multiplexer_20_out),
    .RegWrite(ex_mem_1_p18), .RD(ex_mem_1_p22), .CLK(CLK), .RST(RST), .halt(halt),
    .MemToRegout(mem_we_1_memtoregout), .ALU_Resultout(mem_we_1_alu_resultout),
    .Mem_Resultout(mem_we_1_mem_resultout), .RegWriteout(RegWrite), .RDout(mem_we_1_rdout), .PC(M_PC),
    .PCout(WB_PC), .Haltin(ex_mem_1_p25), .Haltout(mem_we_1_haltout), .IRin(MEM_IR), .IRout(WB_IR));  // open: JALin, JALRin, Beqin, AUIPCin, Bnein, LUIin, LHin, MemWritein, BLTUin, AluOPin, URETin, AluSrcBin, CSRRSIin, CSRRCIin, S_typein, JALout, JALRout, Beqout, ALUIPCout, Bneout, LUIout, LHout, MemWriteout, BLTUout, AluOPout, URETout, AluSrcBout, CSRRSIout, CSRRCIout, S_typeout, Ecallin, Ecallout
  Multiplexer #(.select(1), .width(32), .disabled("Z"), .enable("false")) multiplexer_21 (
    .in0(mem_we_1_alu_resultout), .in1(mem_we_1_mem_resultout), .out(RDin), .sel(mem_we_1_memtoregout));
  // Probe on RDin
  // RiscV_Probe riscv_probe_10: pin names not known; wires that end beside it: ex_mem_1_p25
  and and_13 (and_13_out, mem_we_1_haltout, not_7_out);
  not not_7 (not_7_out, Go);
  D_Flip_Flop #(.trigger("falling"), .Pre_Clr_Positions("ABOVE_BELOW"), .NegatePresetClear("false"), .enable("false"), .NewFFLayout("true")) d_ff_2 (
    .clk(CLK), .D(and_13_out), .Q(halt));  // open: Qn, preset, reset

  // Other names for the same wires on the sheet: MEM_PC[31:0] = M_PC; WB_WriteData[31:0] = RDin;
  //   插入气泡数[15:0] = \LoadUse次数 

  // Notes on the sheet:
  //   中断源
  //   时空图监测，可删除
  //   中断等待指示
  //   单级中断测试信号模拟器
  //   中断不能被其他中断请求中断
  //   数码管输出
  //   ctrl+k关闭时钟连续运行，将控制位置零，进入单步调试模式调试
  //   contents of 指令存储器 (hex, n*v repeats v):
  //   7d000113 100413 1f41993 41f9d993 433 c00913 800b13 140413 f47413 800293 100313 499993 89e9b3 1300533
  //   2200893 73 406282b3 fe0294e3 140413 f00f93 1f47433 1c41413 800293 100313 49d993 89e9b3 1300533
  //   2200893 73 406282b3 fe0294e3 1c45413 406b0b33 b0463 f95ff06f 2b3 fff2c293 1029293 fff2e293 500533
  //   2200893 73 f5dff06f 1112023 410113 a12023 410113 812023 410113 1312023 410113 1412023 410113 1512023
  //   410113 1612023 410113 100b13 300a13 100a93 1600433 441413 14469b3 1300533 2200893 73 fe0416e3
  //   415a0a33 fe0a10e3 ffc10113 12b03 ffc10113 12a83 ffc10113 12a03 ffc10113 12983 ffc10113 12403
  //   ffc10113 12503 ffc10113 12883 200073 1112023 410113 a12023 410113 812023 410113 1312023 410113
  //   1412023 410113 1512023 410113 1612023 410113 200b13 300a13 100a93 1600433 441413 14469b3 1300533
  //   2200893 73 fe0416e3 415a0a33 fe0a10e3 ffc10113 12b03 ffc10113 12a83 ffc10113 12a03 ffc10113 12983
  //   ffc10113 12403 ffc10113 12503 ffc10113 12883 200073 1112023 410113 a12023 410113 812023 410113
  //   1312023 410113 1412023 410113 1512023 410113 1612023 410113 300b13 300a13 100a93 1600433 441413
  //   14469b3 1300533 2200893 73 fe0416e3 415a0a33 fe0a10e3 ffc10113 12b03 ffc10113 12a83 ffc10113 12a03
  //   ffc10113 12983 ffc10113 12403 ffc10113 12503 ffc10113 12883 200073
  //   控制位
  //   流水调试日志用
  //   暂停节拍，不能为0
  //   AUIPC
  //   opcode
  //   funct
  //   rs1
  //   rs2
  //   I:imm
  //   S:imm
  //   B:imm
  //   J:imm
  //   U:imm
  //   rd
  //   戳工具置1进入计数暂停模式，ctrl+k时钟自动运行到对应节拍暂停
  //   Beq
  //   JAL
  //   JALR
  //   Bne
  //   LUI
  //   MemToReg
  //   MemWrite
  //   AluOP
  //   AluSrcB
  //   RegWrite
  //   S_type
  //   ecall
  //   可计数暂停的时钟源
  //   为方便自动评测，需要输出流水线各段保存的PC值，注意是PC不是PC+4，另外ID段寄存器写入信息，Mem段内存写入信息也要输出
  //   数据存储器
endmodule

module \封装正确性测试  (
);

  wire IR1, IR2, IR3, MemW, RegW;
  wire [31:0] EX_PC, ID_PC, IF_PC, IR, LED, MDin, MDinr, MEM_PC, PC, RDin, RDinr, WB_PC;

  \单周期RISC_V  \u_单周期risc_v_1  (
    .IR1(IR1), .IR2(IR2), .IR3(IR3), .RegWrite(RegW), .MemWrite(MemW), .PC(PC), .IR(IR), .RDin(RDin),
    .MDin(MDin), .LedData(LED));
  \气泡流水线  \u_气泡流水线_1  (
    .RegWrite(RegW), .MemWrite(MemW), .IF_PC(IF_PC), .ID_PC(ID_PC), .EX_PC(EX_PC), .M_PC(MEM_PC),
    .WB_PC(WB_PC), .RDin(RDinr), .MDin(MDinr), .LedData(LED));
  \单周期_单级中断  \u_单周期_单级中断_1  (
    .IR1(IR1), .IR2(IR2), .IR3(IR3), .RegWrite(RegW), .MemWrite(MemW), .PC(PC), .IR(IR), .RDin(RDin),
    .MDin(MDin), .LedData(LED));
  \理想流水线  \u_理想流水线_1  (
    .RegWrite(RegW), .MemWrite(MemW), .IF_PC(IF_PC), .ID_PC(ID_PC), .EX_PC(EX_PC), .M_PC(MEM_PC),
    .WB_PC(WB_PC), .RDin(RDinr), .MDin(MDinr), .LedData(LED));
  \重定向流水线  \u_重定向流水线_1  (
    .RegWrite(RegW), .MemWrite(MemW), .IF_PC(IF_PC), .ID_PC(ID_PC), .EX_PC(EX_PC), .M_PC(MEM_PC),
    .WB_PC(WB_PC), .RDin(RDinr), .MDin(MDinr), .LedData(LED));
  \单周期_多级中断  \u_单周期_多级中断_1  (
    .IR1(IR1), .IR2(IR2), .IR3(IR3), .RegWrite(RegW), .MemWrite(MemW), .PC(PC), .IR(IR), .RDin(RDin),
    .MDin(MDin), .LedData(LED));

  // Notes on the sheet:
  //   单周期封装测试
  //   气泡流水封装测试
  //   单周期+单级中断封装测试
  //   请检查上面封装有无位宽不匹配，引脚标签是否和连接的标签相对应，否则无法在educoder平台上正确测试
  //   理想流水封装测试
  //   重定向流水封装测试
  //   单周期+多级中断封装测试
endmodule

module ecall_deal (
  input  clk,
  input  go,
  input  ecall,
  input  [31:0] rs1_data,
  input  [31:0] a0,
  output halt,
  output [31:0] LedData
);

  wire and_1_out, and_2_out, comparator_1_eq, comparator_2_eq, not_1_out;

  Comparator #(.width(32), .mode("twosComplement")) comparator_1 (
    .a(rs1_data), .b(32'ha), .eq(comparator_1_eq));  // open: gt, lt
  Comparator #(.width(32), .mode("twosComplement")) comparator_2 (
    .a(rs1_data), .b(32'h22), .eq(comparator_2_eq));  // open: gt, lt
  not not_1 (not_1_out, go);
  and and_1 (and_1_out, ecall, comparator_2_eq);
  and and_2 (and_2_out, comparator_1_eq, ecall, not_1_out);
  D_Flip_Flop #(.trigger("falling"), .Pre_Clr_Positions("ABOVE_BELOW"), .NegatePresetClear("false"), .enable("false"), .NewFFLayout("true")) d_ff_1 (
    .clk(clk), .D(and_2_out), .Q(halt), .reset(go));  // open: Qn, preset
  Register #(.width(32), .trigger("rising"), .Select("low")) a0_reg (
    .D(a0), .en(and_1_out), .Q(LedData), .clk(clk));  // open: clr
endmodule

module pc_next (
  input  [31:0] pc,
  input  [31:0] B_offset,
  input  [31:0] J_offset,
  input  [31:0] rs1,
  input  [31:0] I_offset,
  input  ALU_equal,
  input  ALU_less,
  input  Beq,
  input  Bne,
  input  BLTU,
  input  JAL,
  input  JALR,
  output [31:0] next_pc
);

  wire and_1_out, and_2_out, and_3_out, not_1_out, or_1_out;
  wire [31:0] adder_1_out, adder_2_out, adder_3_out, adder_4_out, multiplexer_1_out, multiplexer_2_out;

  Adder #(.width(32)) adder_1 (.a(pc), .b(32'h4), .out(adder_1_out));  // open: cin, cout
  Adder #(.width(32)) adder_2 (.a(pc), .b(B_offset), .out(adder_2_out));  // open: cin, cout
  not not_1 (not_1_out, ALU_equal);
  and and_1 (and_1_out, not_1_out, Bne);
  and and_2 (and_2_out, ALU_equal, Beq);
  or or_1 (or_1_out, and_2_out, and_1_out, and_3_out);
  Multiplexer #(.select(1), .width(32), .disabled("Z"), .enable("false")) multiplexer_1 (
    .in0(adder_1_out), .in1(adder_2_out), .out(multiplexer_1_out), .sel(or_1_out));
  and and_3 (and_3_out, ALU_less, BLTU);
  Adder #(.width(32)) adder_3 (.a(pc), .b(J_offset), .out(adder_3_out));  // open: cin, cout
  Multiplexer #(.select(1), .width(32), .disabled("Z"), .enable("false")) multiplexer_2 (
    .in0(multiplexer_1_out), .in1(adder_3_out), .out(multiplexer_2_out), .sel(JAL));
  Adder #(.width(32)) adder_4 (.a(rs1), .b(I_offset), .out(adder_4_out));  // open: cin, cout
  Multiplexer #(.select(1), .width(32), .disabled("Z"), .enable("false")) multiplexer_3 (
    .in0(multiplexer_2_out), .in1(adder_4_out), .out(next_pc), .sel(JALR));
endmodule

module rd_in (
  input  [31:0] ALU_result,
  input  [31:0] Mem_result,
  input  [31:0] PC,
  input  [31:0] U_imm,
  input  [31:0] Mem_LH_result,
  input  MemToReg,
  input  JAL,
  input  JALR,
  input  LUI,
  input  AUIPC,
  input  LH,
  output [31:0] RDin
);

  wire or_1_out, or_2_out;
  wire [31:0] adder_1_out, adder_2_out, multiplexer_1_out, multiplexer_2_out, multiplexer_3_out;

  Multiplexer #(.select(1), .width(32), .disabled("Z"), .enable("false")) multiplexer_1 (
    .in0(ALU_result), .in1(Mem_result), .out(multiplexer_1_out), .sel(MemToReg));
  or or_1 (or_1_out, JAL, JALR);
  Multiplexer #(.select(1), .width(32), .disabled("Z"), .enable("false")) multiplexer_2 (
    .in0(multiplexer_1_out), .in1(adder_1_out), .out(multiplexer_2_out), .sel(or_1_out));
  Adder #(.width(32)) adder_1 (.a(PC), .b(32'h4), .out(adder_1_out));  // open: cin, cout
  or or_2 (or_2_out, LUI, AUIPC);
  Multiplexer #(.select(1), .width(32), .disabled("Z"), .enable("false")) multiplexer_3 (
    .in0(multiplexer_2_out), .in1(adder_2_out), .out(multiplexer_3_out), .sel(or_2_out));
  Adder #(.width(32)) adder_2 (.a(PC), .b(U_imm), .out(adder_2_out));  // open: cin, cout
  Multiplexer #(.select(1), .width(32), .disabled("Z"), .enable("false")) multiplexer_4 (
    .in0(multiplexer_3_out), .in1(Mem_LH_result), .out(RDin), .sel(LH));
endmodule

module IF_ID (
  input  [31:0] IRin,
  input  [31:0] PCin,
  input  CLK,
  input  RST,
  input  halt,
  input  en,
  output [31:0] IRout,
  output [31:0] PCout
);

  wire and_1_out, not_1_out;
  wire [31:0] multiplexer_1_out, multiplexer_2_out;

  not not_1 (not_1_out, halt);
  Multiplexer #(.select(1), .width(32), .disabled("Z"), .enable("false")) multiplexer_1 (
    .in0(IRin), .in1({32{1'b0}}), .out(multiplexer_1_out), .sel(RST));
  Multiplexer #(.select(1), .width(32), .disabled("Z"), .enable("false")) multiplexer_2 (
    .in0(PCin), .in1({32{1'b0}}), .out(multiplexer_2_out), .sel(RST));
  and and_1 (and_1_out, en, not_1_out);
  Register #(.width(32), .trigger("rising"), .Select("low")) IR_reg (
    .D(multiplexer_1_out), .en(and_1_out), .Q(IRout), .clk(CLK));  // open: clr
  Register #(.width(32), .trigger("rising"), .Select("low")) PC_reg (
    .D(multiplexer_2_out), .en(and_1_out), .Q(PCout), .clk(CLK));  // open: clr
endmodule

module ID_EX (
  input  JALin,
  input  Ecallin,
  input  JALRin,
  input  Beqin,
  input  AUIPCin,
  input  Bnein,
  input  [31:0] PC,
  input  LUIin,
  input  MemToRegin,
  input  LHin,
  input  [31:0] RS1,
  input  MemWritein,
  input  BLTUin,
  input  [3:0] AluOPin,
  input  [31:0] RS2,
  input  URETin,
  input  AluSrcBin,
  input  [4:0] RD,
  input  CSRRSIin,
  input  RegWrite,
  input  [31:0] imm,
  input  CSRRCIin,
  input  S_typein,
  input  CLK,
  input  RST,
  input  halt,
  input  [31:0] IRin,
  input  [1:0] RS1_f_in,
  input  [1:0] RS2_f_in,
  output JALout,
  output Ecallout,
  output JALRout,
  output Beqout,
  output ALUIPCout,
  output Bneout,
  output [31:0] PCout,
  output LUIout,
  output MemToRegout,
  output LHout,
  output [31:0] RS1out,
  output MemWriteout,
  output BLTUout,
  output [3:0] AluOPout,
  output [31:0] RS2out,
  output URETout,
  output AluSrcBout,
  output [4:0] RDout,
  output CSRRSIout,
  output RegWriteout,
  output [31:0] Immout,
  output CSRRCIout,
  output S_typeout,
  output [31:0] IRout,
  output [1:0] RS1_f_out,
  output [1:0] RS2_f_out
);

  wire multiplexer_9_out, multiplexer_10_out, multiplexer_11_out, multiplexer_12_out, multiplexer_13_out,
       multiplexer_15_out, multiplexer_16_out, multiplexer_17_out, multiplexer_18_out, multiplexer_19_out,
       multiplexer_20_out, multiplexer_21_out, multiplexer_22_out, multiplexer_23_out, multiplexer_24_out,
       multiplexer_25_out, multiplexer_26_out, not_1_out;
  wire [1:0] multiplexer_7_out, multiplexer_8_out;
  wire [3:0] multiplexer_14_out;
  wire [4:0] multiplexer_4_out;
  wire [31:0] multiplexer_1_out, multiplexer_2_out, multiplexer_3_out, multiplexer_5_out, multiplexer_6_out;

  not not_1 (not_1_out, halt);
  Multiplexer #(.select(1), .width(32), .disabled("Z"), .enable("false")) multiplexer_1 (
    .in0(PC), .in1({32{1'b0}}), .out(multiplexer_1_out), .sel(RST));
  Multiplexer #(.select(1), .width(32), .disabled("Z"), .enable("false")) multiplexer_2 (
    .in0(RS1), .in1({32{1'b0}}), .out(multiplexer_2_out), .sel(RST));
  Multiplexer #(.select(1), .width(32), .disabled("Z"), .enable("false")) multiplexer_3 (
    .in0(RS2), .in1({32{1'b0}}), .out(multiplexer_3_out), .sel(RST));
  Multiplexer #(.select(1), .width(5), .disabled("Z"), .enable("false")) multiplexer_4 (
    .in0(RD), .in1({5{1'b0}}), .out(multiplexer_4_out), .sel(RST));
  Multiplexer #(.select(1), .width(32), .disabled("Z"), .enable("false")) multiplexer_5 (
    .in0(imm), .in1({32{1'b0}}), .out(multiplexer_5_out), .sel(RST));
  Multiplexer #(.select(1), .width(32), .disabled("Z"), .enable("false")) multiplexer_6 (
    .in0(IRin), .in1({32{1'b0}}), .out(multiplexer_6_out), .sel(RST));
  Multiplexer #(.select(1), .width(2), .disabled("Z"), .enable("false")) multiplexer_7 (
    .in0(RS1_f_in), .in1(2'b00), .out(multiplexer_7_out), .sel(RST));
  Multiplexer #(.select(1), .width(2), .disabled("Z"), .enable("false")) multiplexer_8 (
    .in0(RS2_f_in), .in1(2'b00), .out(multiplexer_8_out), .sel(RST));
  Register #(.width(32), .trigger("rising"), .Select("low")) register_1 (
    .D(multiplexer_1_out), .en(not_1_out), .Q(PCout), .clk(CLK));  // open: clr
  Register #(.width(32), .trigger("rising"), .Select("low")) register_2 (
    .D(multiplexer_2_out), .en(not_1_out), .Q(RS1out), .clk(CLK));  // open: clr
  Register #(.width(32), .trigger("rising"), .Select("low")) register_3 (
    .D(multiplexer_3_out), .en(not_1_out), .Q(RS2out), .clk(CLK));  // open: clr
  Register #(.width(5), .trigger("rising"), .Select("low")) register_4 (
    .D(multiplexer_4_out), .en(not_1_out), .Q(RDout), .clk(CLK));  // open: clr
  Register #(.width(32), .trigger("rising"), .Select("low")) register_5 (
    .D(multiplexer_5_out), .en(not_1_out), .Q(Immout), .clk(CLK));  // open: clr
  Register #(.width(32), .trigger("rising"), .Select("low")) register_6 (
    .D(multiplexer_6_out), .en(not_1_out), .Q(IRout), .clk(CLK));  // open: clr
  Register #(.width(2), .trigger("rising"), .Select("low")) register_7 (
    .D(multiplexer_7_out), .en(not_1_out), .Q(RS1_f_out), .clk(CLK));  // open: clr
  Register #(.width(2), .trigger("rising"), .Select("low")) register_8 (
    .D(multiplexer_8_out), .en(not_1_out), .Q(RS2_f_out), .clk(CLK));  // open: clr
  Multiplexer #(.select(1), .width(1), .disabled("Z"), .enable("false")) multiplexer_9 (
    .in0(Ecallin), .in1(1'b0), .out(multiplexer_9_out), .sel(RST));
  Multiplexer #(.select(1), .width(1), .disabled("Z"), .enable("false")) multiplexer_10 (
    .in0(Beqin), .in1(1'b0), .out(multiplexer_10_out), .sel(RST));
  Multiplexer #(.select(1), .width(1), .disabled("Z"), .enable("false")) multiplexer_11 (
    .in0(Bnein), .in1(1'b0), .out(multiplexer_11_out), .sel(RST));
  Multiplexer #(.select(1), .width(1), .disabled("Z"), .enable("false")) multiplexer_12 (
    .in0(MemToRegin), .in1(1'b0), .out(multiplexer_12_out), .sel(RST));
  Multiplexer #(.select(1), .width(1), .disabled("Z"), .enable("false")) multiplexer_13 (
    .in0(MemWritein), .in1(1'b0), .out(multiplexer_13_out), .sel(RST));
  Multiplexer #(.select(1), .width(4), .disabled("Z"), .enable("false")) multiplexer_14 (
    .in0(AluOPin), .in1(4'b0000), .out(multiplexer_14_out), .sel(RST));
  Multiplexer #(.select(1), .width(1), .disabled("Z"), .enable("false")) multiplexer_15 (
    .in0(AluSrcBin), .in1(1'b0), .out(multiplexer_15_out), .sel(RST));
  Multiplexer #(.select(1), .width(1), .disabled("Z"), .enable("false")) multiplexer_16 (
    .in0(RegWrite), .in1(1'b0), .out(multiplexer_16_out), .sel(RST));
  Multiplexer #(.select(1), .width(1), .disabled("Z"), .enable("false")) multiplexer_17 (
    .in0(S_typein), .in1(1'b0), .out(multiplexer_17_out), .sel(RST));
  Register #(.width(1), .trigger("rising"), .Select("low")) register_9 (
    .D(multiplexer_9_out), .en(not_1_out), .Q(Ecallout), .clk(CLK));  // open: clr
  Register #(.width(1), .trigger("rising"), .Select("low")) register_10 (
    .D(multiplexer_10_out), .en(not_1_out), .Q(Beqout), .clk(CLK));  // open: clr
  Register #(.width(1), .trigger("rising"), .Select("low")) register_11 (
    .D(multiplexer_11_out), .en(not_1_out), .Q(Bneout), .clk(CLK));  // open: clr
  Register #(.width(1), .trigger("rising"), .Select("low")) register_12 (
    .D(multiplexer_12_out), .en(not_1_out), .Q(MemToRegout), .clk(CLK));  // open: clr
  Register #(.width(1), .trigger("rising"), .Select("low")) register_13 (
    .D(multiplexer_13_out), .en(not_1_out), .Q(MemWriteout), .clk(CLK));  // open: clr
  Register #(.width(4), .trigger("rising"), .Select("low")) register_14 (
    .D(multiplexer_14_out), .en(not_1_out), .Q(AluOPout), .clk(CLK));  // open: clr
  Register #(.width(1), .trigger("rising"), .Select("low")) register_15 (
    .D(multiplexer_15_out), .en(not_1_out), .Q(AluSrcBout), .clk(CLK));  // open: clr
  Register #(.width(1), .trigger("rising"), .Select("low")) register_16 (
    .D(multiplexer_16_out), .en(not_1_out), .Q(RegWriteout), .clk(CLK));  // open: clr
  Register #(.width(1), .trigger("rising"), .Select("low")) register_17 (
    .D(multiplexer_17_out), .en(not_1_out), .Q(S_typeout), .clk(CLK));  // open: clr
  Multiplexer #(.select(1), .width(1), .disabled("Z"), .enable("false")) multiplexer_18 (
    .in0(JALin), .in1(1'b0), .out(multiplexer_18_out), .sel(RST));
  Multiplexer #(.select(1), .width(1), .disabled("Z"), .enable("false")) multiplexer_19 (
    .in0(JALRin), .in1(1'b0), .out(multiplexer_19_out), .sel(RST));
  Multiplexer #(.select(1), .width(1), .disabled("Z"), .enable("false")) multiplexer_20 (
    .in0(AUIPCin), .in1(1'b0), .out(multiplexer_20_out), .sel(RST));
  Multiplexer #(.select(1), .width(1), .disabled("Z"), .enable("false")) multiplexer_21 (
    .in0(LUIin), .in1(1'b0), .out(multiplexer_21_out), .sel(RST));
  Multiplexer #(.select(1), .width(1), .disabled("Z"), .enable("false")) multiplexer_22 (
    .in0(LHin), .in1(1'b0), .out(multiplexer_22_out), .sel(RST));
  Multiplexer #(.select(1), .width(1), .disabled("Z"), .enable("false")) multiplexer_23 (
    .in0(BLTUin), .in1(1'b0), .out(multiplexer_23_out), .sel(RST));
  Multiplexer #(.select(1), .width(1), .disabled("Z"), .enable("false")) multiplexer_24 (
    .in0(URETin), .in1(1'b0), .out(multiplexer_24_out), .sel(RST));
  Multiplexer #(.select(1), .width(1), .disabled("Z"), .enable("false")) multiplexer_25 (
    .in0(CSRRSIin), .in1(1'b0), .out(multiplexer_25_out), .sel(RST));
  Multiplexer #(.select(1), .width(1), .disabled("Z"), .enable("false")) multiplexer_26 (
    .in0(CSRRCIin), .in1(1'b0), .out(multiplexer_26_out), .sel(RST));
  Register #(.width(1), .trigger("rising"), .Select("low")) register_18 (
    .D(multiplexer_18_out), .en(not_1_out), .Q(JALout), .clk(CLK));  // open: clr
  Register #(.width(1), .trigger("rising"), .Select("low")) register_19 (
    .D(multiplexer_19_out), .en(not_1_out), .Q(JALRout), .clk(CLK));  // open: clr
  Register #(.width(1), .trigger("rising"), .Select("low")) register_20 (
    .D(multiplexer_20_out), .en(not_1_out), .Q(ALUIPCout), .clk(CLK));  // open: clr
  Register #(.width(1), .trigger("rising"), .Select("low")) register_21 (
    .D(multiplexer_21_out), .en(not_1_out), .Q(LUIout), .clk(CLK));  // open: clr
  Register #(.width(1), .trigger("rising"), .Select("low")) register_22 (
    .D(multiplexer_22_out), .en(not_1_out), .Q(LHout), .clk(CLK));  // open: clr
  Register #(.width(1), .trigger("rising"), .Select("low")) register_23 (
    .D(multiplexer_23_out), .en(not_1_out), .Q(BLTUout), .clk(CLK));  // open: clr
  Register #(.width(1), .trigger("rising"), .Select("low")) register_24 (
    .D(multiplexer_24_out), .en(not_1_out), .Q(URETout), .clk(CLK));  // open: clr
  Register #(.width(1), .trigger("rising"), .Select("low")) register_25 (
    .D(multiplexer_25_out), .en(not_1_out), .Q(CSRRSIout), .clk(CLK));  // open: clr
  Register #(.width(1), .trigger("rising"), .Select("low")) register_26 (
    .D(multiplexer_26_out), .en(not_1_out), .Q(CSRRCIout), .clk(CLK));  // open: clr
endmodule

module EX_MEM (
  input  Haltin,
  input  JALin,
  input  Ecallin,
  input  JALRin,
  input  Beqin,
  input  AUIPCin,
  input  Bnein,
  input  [31:0] IRin,
  input  LUIin,
  input  MemToRegin,
  input  [31:0] PC,
  input  LHin,
  input  MemWritein,
  input  [31:0] ALU_Result,
  input  BLTUin,
  input  [3:0] AluOPin,
  input  [31:0] WriteData,
  input  URETin,
  input  AluSrcBin,
  input  CSRRSIin,
  input  [4:0] RD,
  input  RegWrite,
  input  CSRRCIin,
  input  S_typein,
  input  CLK,
  input  RST,
  input  halt,
  output Haltout,
  output JALout,
  output Ecallout,
  output JALRout,
  output Beqout,
  output ALUIPCout,
  output Bneout,
  output [31:0] IRout,
  output LUIout,
  output MemToRegout,
  output [31:0] PCout,
  output LHout,
  output MemWriteout,
  output [31:0] ALU_Resultout,
  output BLTUout,
  output [3:0] AluOPout,
  output [31:0] WirteDataout,
  output URETout,
  output AluSrcBout,
  output CSRRSIout,
  output [4:0] RDout,
  output RegWriteout,
  output CSRRCIout,
  output S_typeout
);

  wire not_1_out;

  not not_1 (not_1_out, halt);
  Register #(.width(32), .trigger("rising"), .Select("low")) register_1 (
    .D(IRin), .en(not_1_out), .Q(IRout), .clk(CLK), .clr(RST));
  Register #(.width(32), .trigger("rising"), .Select("low")) register_2 (
    .D(PC), .en(not_1_out), .Q(PCout), .clk(CLK), .clr(RST));
  Register #(.width(32), .trigger("rising"), .Select("low")) register_3 (
    .D(ALU_Result), .en(not_1_out), .Q(ALU_Resultout), .clk(CLK), .clr(RST));
  Register #(.width(32), .trigger("rising"), .Select("low")) register_4 (
    .D(WriteData), .en(not_1_out), .Q(WirteDataout), .clk(CLK), .clr(RST));
  Register #(.width(5), .trigger("rising"), .Select("low")) register_5 (
    .D(RD), .en(not_1_out), .Q(RDout), .clk(CLK), .clr(RST));
  Register #(.width(1), .trigger("rising"), .Select("low")) register_6 (
    .D(Haltin), .en(not_1_out), .Q(Haltout), .clk(CLK), .clr(RST));
  Register #(.width(1), .trigger("rising"), .Select("low")) register_7 (
    .D(Ecallin), .en(not_1_out), .Q(Ecallout), .clk(CLK), .clr(RST));
  Register #(.width(1), .trigger("rising"), .Select("low")) register_8 (
    .D(Beqin), .en(not_1_out), .Q(Beqout), .clk(CLK), .clr(RST));
  Register #(.width(1), .trigger("rising"), .Select("low")) register_9 (
    .D(Bnein), .en(not_1_out), .Q(Bneout), .clk(CLK), .clr(RST));
  Register #(.width(1), .trigger("rising"), .Select("low")) register_10 (
    .D(MemToRegin), .en(not_1_out), .Q(MemToRegout), .clk(CLK), .clr(RST));
  Register #(.width(1), .trigger("rising"), .Select("low")) register_11 (
    .D(MemWritein), .en(not_1_out), .Q(MemWriteout), .clk(CLK), .clr(RST));
  Register #(.width(4), .trigger("rising"), .Select("low")) register_12 (
    .D(AluOPin), .en(not_1_out), .Q(AluOPout), .clk(CLK), .clr(RST));
  Register #(.width(1), .trigger("rising"), .Select("low")) register_13 (
    .D(AluSrcBin), .en(not_1_out), .Q(AluSrcBout), .clk(CLK), .clr(RST));
  Register #(.width(1), .trigger("rising"), .Select("low")) register_14 (
    .D(RegWrite), .en(not_1_out), .Q(RegWriteout), .clk(CLK), .clr(RST));
  Register #(.width(1), .trigger("rising"), .Select("low")) register_15 (
    .D(S_typein), .en(not_1_out), .Q(S_typeout), .clk(CLK), .clr(RST));
  Register #(.width(1), .trigger("rising"), .Select("low")) register_16 (
    .D(JALin), .en(not_1_out), .Q(JALout), .clk(CLK), .clr(RST));
  Register #(.width(1), .trigger("rising"), .Select("low")) register_17 (
    .D(JALRin), .en(not_1_out), .Q(JALRout), .clk(CLK), .clr(RST));
  Register #(.width(1), .trigger("rising"), .Select("low")) register_18 (
    .D(AUIPCin), .en(not_1_out), .Q(ALUIPCout), .clk(CLK), .clr(RST));
  Register #(.width(1), .trigger("rising"), .Select("low")) register_19 (
    .D(LUIin), .en(not_1_out), .Q(LUIout), .clk(CLK), .clr(RST));
  Register #(.width(1), .trigger("rising"), .Select("low")) register_20 (
    .D(LHin), .en(not_1_out), .Q(LHout), .clk(CLK), .clr(RST));
  Register #(.width(1), .trigger("rising"), .Select("low")) register_21 (
    .D(BLTUin), .en(not_1_out), .Q(BLTUout), .clk(CLK), .clr(RST));
  Register #(.width(1), .trigger("rising"), .Select("low")) register_22 (
    .D(URETin), .en(not_1_out), .Q(URETout), .clk(CLK), .clr(RST));
  Register #(.width(1), .trigger("rising"), .Select("low")) register_23 (
    .D(CSRRSIin), .en(not_1_out), .Q(CSRRSIout), .clk(CLK), .clr(RST));
  Register #(.width(1), .trigger("rising"), .Select("low")) register_24 (
    .D(CSRRCIin), .en(not_1_out), .Q(CSRRCIout), .clk(CLK), .clr(RST));
endmodule

module MEM_WE (
  input  Haltin,
  input  JALin,
  input  Ecallin,
  input  JALRin,
  input  Beqin,
  input  AUIPCin,
  input  Bnein,
  input  LUIin,
  input  MemToRegin,
  input  [31:0] IRin,
  input  LHin,
  input  MemWritein,
  input  [31:0] PC,
  input  BLTUin,
  input  [3:0] AluOPin,
  input  [31:0] ALU_Result,
  input  URETin,
  input  AluSrcBin,
  input  [31:0] Mem_Result,
  input  CSRRSIin,
  input  RegWrite,
  input  [4:0] RD,
  input  CSRRCIin,
  input  S_typein,
  input  CLK,
  input  RST,
  input  halt,
  output Haltout,
  output JALout,
  output Ecallout,
  output JALRout,
  output Beqout,
  output ALUIPCout,
  output Bneout,
  output LUIout,
  output MemToRegout,
  output [31:0] IRout,
  output LHout,
  output MemWriteout,
  output [31:0] PCout,
  output BLTUout,
  output [3:0] AluOPout,
  output [31:0] ALU_Resultout,
  output URETout,
  output AluSrcBout,
  output [31:0] Mem_Resultout,
  output CSRRSIout,
  output RegWriteout,
  output [4:0] RDout,
  output CSRRCIout,
  output S_typeout
);

  wire not_1_out;

  not not_1 (not_1_out, halt);
  Register #(.width(32), .trigger("rising"), .Select("low")) register_1 (
    .D(IRin), .en(not_1_out), .Q(IRout), .clk(CLK), .clr(RST));
  Register #(.width(32), .trigger("rising"), .Select("low")) register_2 (
    .D(PC), .en(not_1_out), .Q(PCout), .clk(CLK), .clr(RST));
  Register #(.width(32), .trigger("rising"), .Select("low")) register_3 (
    .D(ALU_Result), .en(not_1_out), .Q(ALU_Resultout), .clk(CLK), .clr(RST));
  Register #(.width(32), .trigger("rising"), .Select("low")) register_4 (
    .D(Mem_Result), .en(not_1_out), .Q(Mem_Resultout), .clk(CLK), .clr(RST));
  Register #(.width(5), .trigger("rising"), .Select("low")) register_5 (
    .D(RD), .en(not_1_out), .Q(RDout), .clk(CLK), .clr(RST));
  Register #(.width(1), .trigger("rising"), .Select("low")) register_6 (
    .D(Haltin), .en(not_1_out), .Q(Haltout), .clk(CLK), .clr(RST));
  Register #(.width(1), .trigger("rising"), .Select("low")) register_7 (
    .D(Ecallin), .en(not_1_out), .Q(Ecallout), .clk(CLK), .clr(RST));
  Register #(.width(1), .trigger("rising"), .Select("low")) register_8 (
    .D(Beqin), .en(not_1_out), .Q(Beqout), .clk(CLK), .clr(RST));
  Register #(.width(1), .trigger("rising"), .Select("low")) register_9 (
    .D(Bnein), .en(not_1_out), .Q(Bneout), .clk(CLK), .clr(RST));
  Register #(.width(1), .trigger("rising"), .Select("low")) register_10 (
    .D(MemToRegin), .en(not_1_out), .Q(MemToRegout), .clk(CLK), .clr(RST));
  Register #(.width(1), .trigger("rising"), .Select("low")) register_11 (
    .D(MemWritein), .en(not_1_out), .Q(MemWriteout), .clk(CLK), .clr(RST));
  Register #(.width(4), .trigger("rising"), .Select("low")) register_12 (
    .D(AluOPin), .en(not_1_out), .Q(AluOPout), .clk(CLK), .clr(RST));
  Register #(.width(1), .trigger("rising"), .Select("low")) register_13 (
    .D(AluSrcBin), .en(not_1_out), .Q(AluSrcBout), .clk(CLK), .clr(RST));
  Register #(.width(1), .trigger("rising"), .Select("low")) register_14 (
    .D(RegWrite), .en(not_1_out), .Q(RegWriteout), .clk(CLK), .clr(RST));
  Register #(.width(1), .trigger("rising"), .Select("low")) register_15 (
    .D(S_typein), .en(not_1_out), .Q(S_typeout), .clk(CLK), .clr(RST));
  Register #(.width(1), .trigger("rising"), .Select("low")) register_16 (
    .D(JALin), .en(not_1_out), .Q(JALout), .clk(CLK), .clr(RST));
  Register #(.width(1), .trigger("rising"), .Select("low")) register_17 (
    .D(JALRin), .en(not_1_out), .Q(JALRout), .clk(CLK), .clr(RST));
  Register #(.width(1), .trigger("rising"), .Select("low")) register_18 (
    .D(AUIPCin), .en(not_1_out), .Q(ALUIPCout), .clk(CLK), .clr(RST));
  Register #(.width(1), .trigger("rising"), .Select("low")) register_19 (
    .D(LUIin), .en(not_1_out), .Q(LUIout), .clk(CLK), .clr(RST));
  Register #(.width(1), .trigger("rising"), .Select("low")) register_20 (
    .D(LHin), .en(not_1_out), .Q(LHout), .clk(CLK), .clr(RST));
  Register #(.width(1), .trigger("rising"), .Select("low")) register_21 (
    .D(BLTUin), .en(not_1_out), .Q(BLTUout), .clk(CLK), .clr(RST));
  Register #(.width(1), .trigger("rising"), .Select("low")) register_22 (
    .D(URETin), .en(not_1_out), .Q(URETout), .clk(CLK), .clr(RST));
  Register #(.width(1), .trigger("rising"), .Select("low")) register_23 (
    .D(CSRRSIin), .en(not_1_out), .Q(CSRRSIout), .clk(CLK), .clr(RST));
  Register #(.width(1), .trigger("rising"), .Select("low")) register_24 (
    .D(CSRRCIin), .en(not_1_out), .Q(CSRRCIout), .clk(CLK), .clr(RST));
endmodule

module signalControl (
  input  [4:0] OP,
  input  [4:0] Funct,
  output [3:0] ALU_OP,
  output MemToReg,
  output MemWrite,
  output ALU_SRC,
  output RegWrite,
  output ecall,
  output S_type,
  output Beq,
  output Bne,
  output Jalr,
  output JAL,
  output LUI,
  output AUIPC,
  output LH,
  output BLTU
);

  // Probe on OP
  \运算控制器自动生成  \u_运算控制器自动生成_1  (
    .OP2(OP[0]), .OP3(OP[1]), .OP4(OP[2]), .OP5(OP[3]), .OP6(OP[4]), .F12(Funct[0]), .F13(Funct[1]),
    .F14(Funct[2]), .F25(Funct[3]), .F30(Funct[4]), .S0(ALU_OP[0]), .S1(ALU_OP[1]), .S2(ALU_OP[2]),
    .S3(ALU_OP[3]));
  \控制信号自动生成  \u_控制信号自动生成_1  (
    .OP2(OP[0]), .OP3(OP[1]), .OP4(OP[2]), .OP5(OP[3]), .MemToReg(MemToReg), .OP6(OP[4]), .F12(Funct[0]),
    .F13(Funct[1]), .F14(Funct[2]), .F25(Funct[3]), .F30(Funct[4]), .MemWrite(MemWrite), .ALU_SRC(ALU_SRC),
    .RegWrite(RegWrite), .ecall(ecall), .S_Type(S_type), .BEQ(Beq), .BNE(Bne), .JALR(Jalr), .JAL(JAL),
    .LUI(LUI), .AUIPC(AUIPC), .LH(LH), .BLTU(BLTU));  // open: CSRRSI, CSRRCI
  // Probe on Funct
  // Probe on ALU_OP

  // Other names for the same wires on the sheet: OP_CODE[4:0] = OP

  // Notes on the sheet:
  //   运算器控制器，根据指令生成运算器功能选择信号
  //   控制信号生成，产生数据通路需要的其他控制信号
endmodule
module \相关逻辑处理_气泡  (
  input  [4:0] ID_rs1,
  input  [4:0] ID_rs2,
  input  [4:0] EX_rd,
  input  [4:0] MEM_rd,
  input  EX_rw,
  input  MEM_rw,
  input  branch,
  output stall,
  output IF_ID_en,
  output IF_ID_clr,
  output ID_EX_clr
);

  wire and_1_out, and_2_out, comparator_1_eq, comparator_2_eq, comparator_3_eq, comparator_4_eq,
       comparator_5_eq, comparator_6_eq, not_1_out, not_2_out, or_1_out, or_2_out;

  Comparator #(.width(5), .mode("twosComplement")) comparator_1 (
    .a(ID_rs1), .b(EX_rd), .eq(comparator_1_eq));  // open: gt, lt
  Comparator #(.width(5), .mode("twosComplement")) comparator_2 (
    .a(ID_rs1), .b(MEM_rd), .eq(comparator_2_eq));  // open: gt, lt
  Comparator #(.width(5), .mode("twosComplement")) comparator_3 (
    .a(ID_rs2), .b(EX_rd), .eq(comparator_3_eq));  // open: gt, lt
  Comparator #(.width(5), .mode("twosComplement")) comparator_4 (
    .a(ID_rs2), .b(MEM_rd), .eq(comparator_4_eq));  // open: gt, lt
  Comparator #(.width(5), .mode("twosComplement")) comparator_5 (
    .a(ID_rs1), .b({5{1'b0}}), .eq(comparator_5_eq));  // open: gt, lt
  Comparator #(.width(5), .mode("twosComplement")) comparator_6 (
    .a(ID_rs2), .b({5{1'b0}}), .eq(comparator_6_eq));  // open: gt, lt
  not not_1 (not_1_out, comparator_5_eq);
  not not_2 (not_2_out, comparator_6_eq);
  or or_1 (or_1_out, comparator_2_eq, comparator_1_eq);
  or or_2 (or_2_out, comparator_3_eq, comparator_4_eq);
  and and_1 (and_1_out, or_1_out, not_1_out);
  and and_2 (and_2_out, or_2_out, not_2_out);
  or or_3 (stall, and_1_out, and_2_out);
  not not_3 (IF_ID_en, stall);
  or or_4 (ID_EX_clr, branch, stall);

  assign IF_ID_clr = branch;
endmodule

module \相关逻辑处理_重定向  (
  input  [4:0] rs1,
  input  [4:0] rs2,
  input  [4:0] EX_WriteReg,
  input  EX_MemToReg,
  input  EX_RegWrite,
  input  [4:0] MEM_WriteReg,
  input  MEM_RegWrite,
  input  BranchTaken,
  output LoadUse,
  output stall,
  output IF_ID_CLR,
  output ID_EX_CLR,
  output PC_EN,
  output [1:0] RS1_Forward,
  output [1:0] RS2_Forward
);

  wire and_1_out, and_2_out, and_3_out, and_4_out, and_5_out, and_6_out, comparator_1_eq, comparator_2_eq,
       comparator_3_eq, comparator_4_eq, comparator_5_eq, comparator_6_eq, not_1_out, not_2_out;
  wire [1:0] multiplexer_1_out, multiplexer_2_out;

  Comparator #(.width(5), .mode("twosComplement")) comparator_1 (
    .a(rs1), .b(EX_WriteReg), .eq(comparator_1_eq));  // open: gt, lt
  not not_1 (not_1_out, comparator_2_eq);
  Comparator #(.width(5), .mode("twosComplement")) comparator_2 (
    .a(rs1), .b({5{1'b0}}), .eq(comparator_2_eq));  // open: gt, lt
  Comparator #(.width(5), .mode("twosComplement")) comparator_3 (
    .a(rs2), .b(EX_WriteReg), .eq(comparator_3_eq));  // open: gt, lt
  not not_2 (not_2_out, comparator_4_eq);
  Comparator #(.width(5), .mode("twosComplement")) comparator_4 (
    .a(rs2), .b({5{1'b0}}), .eq(comparator_4_eq));  // open: gt, lt
  Comparator #(.width(5), .mode("twosComplement")) comparator_5 (
    .a(rs1), .b(MEM_WriteReg), .eq(comparator_5_eq));  // open: gt, lt
  Comparator #(.width(5), .mode("twosComplement")) comparator_6 (
    .a(rs2), .b(MEM_WriteReg), .eq(comparator_6_eq));  // open: gt, lt
  and and_1 (and_1_out, EX_MemToReg, comparator_1_eq, not_1_out);
  and and_2 (and_2_out, EX_MemToReg, comparator_3_eq, not_2_out);
  and and_3 (and_3_out, MEM_RegWrite, not_2_out, comparator_6_eq);
  or or_1 (LoadUse, and_1_out, and_2_out);
  and and_4 (and_4_out, MEM_RegWrite, not_1_out, comparator_5_eq);
  and and_5 (and_5_out, EX_RegWrite, comparator_3_eq, not_2_out);
  Multiplexer #(.select(1), .width(2), .disabled("Z"), .enable("false")) multiplexer_1 (
    .in0(2'b00), .in1(2'b01), .out(multiplexer_1_out), .sel(and_3_out));
  and and_6 (and_6_out, EX_RegWrite, comparator_1_eq, not_1_out);
  Multiplexer #(.select(1), .width(2), .disabled("Z"), .enable("false")) multiplexer_2 (
    .in0(2'b00), .in1(2'b01), .out(multiplexer_2_out), .sel(and_4_out));
  Multiplexer #(.select(1), .width(2), .disabled("Z"), .enable("false")) multiplexer_3 (
    .in0(multiplexer_1_out), .in1(2'b10), .out(RS2_Forward), .sel(and_5_out));
  Multiplexer #(.select(1), .width(2), .disabled("Z"), .enable("false")) multiplexer_4 (
    .in0(multiplexer_2_out), .in1(2'b10), .out(RS1_Forward), .sel(and_6_out));
  or or_2 (ID_EX_CLR, LoadUse, BranchTaken);
  not not_3 (PC_EN, LoadUse);

  assign IF_ID_CLR = BranchTaken;
  assign stall = LoadUse;
endmodule

module \中断  (
  input  clk,
  input  button,
  input  \同步清零信号 ,
  output \与中断屏蔽位与 ,
  output wait_uret
);

  wire and_1_out, d_ff_1_q, or_2_out;

  or or_1 (wait_uret, \与中断屏蔽位与 , d_ff_1_q);
  D_Flip_Flop #(.trigger("rising"), .Pre_Clr_Positions("LEGACY"), .NegatePresetClear("false"), .enable("true"), .NewFFLayout("false")) d_ff_1 (
    .clk(button), .D(1'b1), .Q(d_ff_1_q), .reset(\与中断屏蔽位与 ));  // open: Qn, preset, en
  or or_2 (or_2_out, d_ff_1_q, \与中断屏蔽位与 );
  and and_1 (and_1_out, or_2_out, ~\同步清零信号 );  // AND_Gate
  D_Flip_Flop #(.trigger("rising"), .Pre_Clr_Positions("LEGACY"), .NegatePresetClear("false"), .enable("true"), .NewFFLayout("false")) IR1 (
    .clk(clk), .D(and_1_out), .Q(\与中断屏蔽位与 ));  // open: Qn, preset, en, reset

  // Notes on the sheet:
  //   中断信号采样参考电路
  //   Reset 
endmodule

module hardware_stack (
  input  push,
  input  pop,
  input  [31:0] data_in,
  input  clk,
  output [31:0] data_out
);

  wire or_1_out;
  wire [31:0] multiplexer_1_out, multiplexer_2_out, multiplexer_3_out, register_2_q, register_3_q;

  Multiplexer #(.select(1), .width(32), .disabled("Z"), .enable("false")) multiplexer_1 (
    .in0(data_in), .in1(register_2_q), .out(multiplexer_1_out), .sel(pop));
  Multiplexer #(.select(1), .width(32), .disabled("Z"), .enable("false")) multiplexer_2 (
    .in0(data_out), .in1(register_3_q), .out(multiplexer_2_out), .sel(pop));
  Multiplexer #(.select(1), .width(32), .disabled("Z"), .enable("false")) multiplexer_3 (
    .in0(register_2_q), .in1({32{1'b0}}), .out(multiplexer_3_out), .sel(pop));
  or or_1 (or_1_out, push, pop);
  Register #(.width(32), .trigger("rising"), .Select("low")) register_1 (
    .D(multiplexer_1_out), .en(or_1_out), .Q(data_out), .clk(clk));  // open: clr
  Register #(.width(32), .trigger("rising"), .Select("low")) register_2 (
    .D(multiplexer_2_out), .en(or_1_out), .Q(register_2_q), .clk(clk));  // open: clr
  Register #(.width(32), .trigger("rising"), .Select("low")) register_3 (
    .D(multiplexer_3_out), .en(or_1_out), .Q(register_3_q), .clk(clk));  // open: clr
endmodule
